// Logisim project P0_L0_CRC.circ as structural Verilog
module \四位模二取余  (
  input  _0,
  input  _1,
  input  _2,
  input  _3,
  input  [3:0] \除数 ,
  output O0,
  output O1,
  output O2,
  output O3
);

  wire judge, multiplexer_1_out, multiplexer_2_out, multiplexer_3_out, multiplexer_4_out;

  Multiplexer multiplexer_1 (.in0(\除数 [0]), .in1(1'b0), .out(multiplexer_1_out), .sel(judge));  // open: en
  Multiplexer multiplexer_2 (.in0(\除数 [1]), .in1(1'b0), .out(multiplexer_2_out), .sel(judge));  // open: en
  Multiplexer multiplexer_3 (.in0(\除数 [2]), .in1(1'b0), .out(multiplexer_3_out), .sel(judge));  // open: en
  Multiplexer multiplexer_4 (.in0(\除数 [3]), .in1(1'b0), .out(multiplexer_4_out), .sel(judge));  // open: en
  xor xor_1 (O0, _0, multiplexer_1_out);
  xor xor_2 (O1, _1, multiplexer_2_out);
  xor xor_3 (O2, _2, multiplexer_3_out);
  xor xor_4 (O3, multiplexer_4_out, _3);
  Comparator #(.width(1)) comparator_1 (.a(_3), .b(1'b0), .eq(judge));  // open: gt, lt

  // Other names for the same wires on the sheet: _0_t = \除数 [0]; _1_t = \除数 [1]; _2_t = \除数 [2]; _3_t = \除数 [3]
endmodule

module \CRC时序  (
  input  [7:0] \八位原数据帧 ,
  input  [3:0] \除数 ,
  output [10:0] out_3
);

  wire clk, counter_1_q, counter_2_q, \end , multiplexer_1_out, multiplexer_2_out, multiplexer_3_out,
       multiplexer_4_out, O0, O00, O11, O22, O33;
  wire [5:0] multiplexer_5_out;
  wire [6:0] shift, shifter_1_out;
  wire [7:0] counter_3_q;

  Counter #(.width(1), .max('h1), .ongoal("stay")) counter_1 (
    .Q(counter_1_q), .clk(clk));  // open: load, D, count, carry, clr
  Clock clock_1 (.out(clk));
  Counter #(.width(1), .max('h1), .ongoal("stay")) counter_2 (
    .Q(counter_2_q), .clk(clk));  // open: load, D, count, carry, clr
  Counter #(.ongoal("stay")) counter_3 (.Q(counter_3_q), .clk(clk));  // open: load, D, count, carry, clr
  Multiplexer multiplexer_1 (.in0(\八位原数据帧 [4]), .in1(O00), .out(multiplexer_1_out), .sel(counter_1_q));  // open: en
  Multiplexer multiplexer_2 (.in0(\八位原数据帧 [5]), .in1(O11), .out(multiplexer_2_out), .sel(counter_1_q));  // open: en
  Multiplexer multiplexer_3 (.in0(\八位原数据帧 [6]), .in1(O22), .out(multiplexer_3_out), .sel(counter_1_q));  // open: en
  Multiplexer multiplexer_4 (.in0(\八位原数据帧 [7]), .in1(O33), .out(multiplexer_4_out), .sel(counter_1_q));  // open: en
  Multiplexer #(.width(7)) multiplexer_5 (
    .in0({\八位原数据帧 [3:0], 3'b000}), .in1(shift), .out({O0, multiplexer_5_out}), .sel(counter_2_q));  // open: en
  Comparator #(.mode("unsigned")) comparator_1 (.a(8'h6), .b(counter_3_q), .lt(\end ));  // open: gt, eq
  Shifter #(.width(7)) shifter_1 (.in({O0, multiplexer_5_out}), .\dist (3'b001), .out(shifter_1_out));
  \四位模二取余  \u_四位模二取余  (
    ._0(multiplexer_1_out), ._1(multiplexer_2_out), ._2(multiplexer_3_out), ._3(multiplexer_4_out),
    .\除数 (\除数 ), .O0(out_3[0]), .O1(out_3[1]), .O2(out_3[2]));  // open: O3
  Register #(.width(7)) register_1 (.D(shifter_1_out), .Q(shift), .clk(clk));  // open: en, clr
  \寄存器  \u_寄存器  (
    .in_1(O0), .in_2(out_3[0]), .in_3(out_3[1]), .in_4(out_3[2]), .\end (\end ), .clk(clk), .out_7(O00),
    .out_8(O11), .out_9(O22), .out_10(O33));

  assign out_3[10:3] = \八位原数据帧 ;

  // Other names for the same wires on the sheet: O1 = out_3[0]; O2 = out_3[1]; O3 = out_3[2];
  //   tobeshift[6:3] = \八位原数据帧 [3:0]; 原数据[7:0] = \八位原数据帧 
endmodule

module \寄存器  (
  input  in_1,
  input  in_2,
  input  in_3,
  input  in_4,
  input  clk,
  input  \end ,
  output out_7,
  output out_8,
  output out_9,
  output out_10
);

  wire ena;

  not not_1 (ena, \end );
  Register #(.width(1)) register_1 (.D(in_1), .en(ena), .Q(out_7), .clk(clk));  // open: clr
  Register #(.width(1)) register_2 (.D(in_2), .en(ena), .Q(out_8), .clk(clk));  // open: clr
  Register #(.width(1)) register_3 (.D(in_3), .en(ena), .Q(out_9), .clk(clk));  // open: clr
  Register #(.width(1)) register_4 (.D(in_4), .en(ena), .Q(out_10), .clk(clk));  // open: clr
endmodule

module CRC (
  input  [7:0] \八位原数据帧 ,
  input  [3:0] \除数 ,
  output [10:0] out_3
);

  wire \四位模二取余_1_o0 , \四位模二取余_1_o1 , \四位模二取余_1_o2 , \四位模二取余_2_o0 , \四位模二取余_2_o1 , \四位模二取余_2_o2 ,
       \四位模二取余_3_o0 , \四位模二取余_3_o1 , \四位模二取余_3_o2 , \四位模二取余_4_o0 , \四位模二取余_4_o1 , \四位模二取余_4_o2 ,
       \四位模二取余_5_o0 , \四位模二取余_5_o1 , \四位模二取余_5_o2 , \四位模二取余_6_o0 , \四位模二取余_6_o1 , \四位模二取余_6_o2 ,
       \四位模二取余_8_o0 , \四位模二取余_8_o1 , \四位模二取余_8_o2 ;

  \四位模二取余  \u_四位模二取余_1  (
    ._0(\八位原数据帧 [4]), ._1(\八位原数据帧 [5]), ._2(\八位原数据帧 [6]), ._3(\八位原数据帧 [7]), .\除数 (\除数 ), .O0(\四位模二取余_1_o0 ),
    .O1(\四位模二取余_1_o1 ), .O2(\四位模二取余_1_o2 ));  // open: O3
  \四位模二取余  \u_四位模二取余_2  (
    ._0(\八位原数据帧 [3]), ._1(\四位模二取余_1_o0 ), ._2(\四位模二取余_1_o1 ), ._3(\四位模二取余_1_o2 ), .\除数 (\除数 ),
    .O0(\四位模二取余_2_o0 ), .O1(\四位模二取余_2_o1 ), .O2(\四位模二取余_2_o2 ));  // open: O3
  \四位模二取余  \u_四位模二取余_3  (
    ._0(\八位原数据帧 [2]), ._1(\四位模二取余_2_o0 ), ._2(\四位模二取余_2_o1 ), ._3(\四位模二取余_2_o2 ), .\除数 (\除数 ),
    .O0(\四位模二取余_3_o0 ), .O1(\四位模二取余_3_o1 ), .O2(\四位模二取余_3_o2 ));  // open: O3
  \四位模二取余  \u_四位模二取余_4  (
    ._0(\八位原数据帧 [1]), ._1(\四位模二取余_3_o0 ), ._2(\四位模二取余_3_o1 ), ._3(\四位模二取余_3_o2 ), .\除数 (\除数 ),
    .O0(\四位模二取余_4_o0 ), .O1(\四位模二取余_4_o1 ), .O2(\四位模二取余_4_o2 ));  // open: O3
  \四位模二取余  \u_四位模二取余_5  (
    ._0(\八位原数据帧 [0]), ._1(\四位模二取余_4_o0 ), ._2(\四位模二取余_4_o1 ), ._3(\四位模二取余_4_o2 ), .\除数 (\除数 ),
    .O0(\四位模二取余_5_o0 ), .O1(\四位模二取余_5_o1 ), .O2(\四位模二取余_5_o2 ));  // open: O3
  \四位模二取余  \u_四位模二取余_6  (
    ._0(1'b0), ._1(\四位模二取余_5_o0 ), ._2(\四位模二取余_5_o1 ), ._3(\四位模二取余_5_o2 ), .\除数 (\除数 ), .O0(\四位模二取余_6_o0 ),
    .O1(\四位模二取余_6_o1 ), .O2(\四位模二取余_6_o2 ));  // open: O3
  \四位模二取余  \u_四位模二取余_7  (
    ._0(1'b0), ._1(\四位模二取余_8_o0 ), ._2(\四位模二取余_8_o1 ), ._3(\四位模二取余_8_o2 ), .\除数 (\除数 ), .O0(out_3[0]),
    .O1(out_3[1]), .O2(out_3[2]));  // open: O3
  \四位模二取余  \u_四位模二取余_8  (
    ._0(1'b0), ._1(\四位模二取余_6_o0 ), ._2(\四位模二取余_6_o1 ), ._3(\四位模二取余_6_o2 ), .\除数 (\除数 ), .O0(\四位模二取余_8_o0 ),
    .O1(\四位模二取余_8_o1 ), .O2(\四位模二取余_8_o2 ));  // open: O3

  assign out_3[10:3] = \八位原数据帧 ;

  // Other names for the same wires on the sheet: _3 = \八位原数据帧 [0]; 原数据[7:0] = \八位原数据帧 ; _4 = \八位原数据帧 [1];
  //   _5 = \八位原数据帧 [2]; _6 = \八位原数据帧 [3]
endmodule
