// Logisim project P0_L0_FSM.circ as structural Verilog
module fsm (
  input  in_1,
  input  [1:0] \input ,
  output out
);

  wire clk_out, s0, s00, s1, s11;

  \状态转移  \u_状态转移_输出  (.s0(s0), .s1(s1), .in0(\input [1]), .in1(\input [0]), .s00(s00), .s11(s11), .out(out));
  Clock clk (.out(clk_out));
  \置位清零  \u_置位清零  (.in_1(s00), .in_2(s11), .reset(in_1), .clk(clk_out), .out_5(s0), .out_6(s1));

  // Other names for the same wires on the sheet: in1 = \input [0]; in0 = \input [1]; reset = in_1

  // Notes on the sheet:
  //   Mealy型状态机，输出直接响应输入
endmodule

module \状态转移  (
  input  s0,
  input  s1,
  input  in0,
  input  in1,
  output s00,
  output s11,
  output out
);

  wire and_1_out, and_2_out, and_3_out, and_4_out, not_1_out, not_2_out, not_3_out, not_4_out, not_5_out,
       not_6_out, not_7_out, not_8_out, not_9_out;

  not not_1 (not_1_out, s0);
  and and_1 (and_1_out, not_1_out, s1, not_2_out);
  not not_2 (not_2_out, in1);
  and and_2 (and_2_out, s0, not_3_out, not_4_out);
  not not_3 (not_3_out, s1);
  not not_4 (not_4_out, in1);
  not not_5 (not_5_out, in0);
  and and_3 (and_3_out, not_5_out, in1);
  and and_4 (and_4_out, s0, not_6_out, not_7_out);
  not not_6 (not_6_out, s1);
  not not_7 (not_7_out, in1);
  not not_8 (not_8_out, s1);
  not not_9 (not_9_out, in1);
  or or_1 (s00, and_1_out, and_2_out);
  or or_2 (s11, and_3_out, and_4_out);
  and and_5 (out, s0, not_8_out, not_9_out);
endmodule

module \状态输出  (
  input  s0,
  input  s1,
  input  in0,
  input  in1,
  output out
);

  wire not_1_out, not_2_out;

  and and_1 (out, s0, not_1_out, not_2_out);
  not not_1 (not_1_out, s1);
  not not_2 (not_2_out, in1);
endmodule

module \置位清零  (
  input  in_1,
  input  in_2,
  input  reset,
  input  clk,
  output out_5,
  output out_6
);

  wire multiplexer_1_out, multiplexer_2_out;

  Multiplexer multiplexer_1 (.in0(in_1), .in1(1'b0), .out(multiplexer_1_out), .sel(reset));  // open: en
  Register #(.width(1)) register_1 (.D(multiplexer_1_out), .Q(out_5), .clk(clk));  // open: en, clr
  Register #(.width(1)) register_2 (.D(multiplexer_2_out), .Q(out_6), .clk(clk));  // open: en, clr
  Multiplexer multiplexer_2 (.in0(in_2), .in1(1'b0), .out(multiplexer_2_out), .sel(reset));  // open: en
endmodule
