// Logisim project P0_L0_GRF.circ as structural Verilog: 2 circuits, main circuit main
module main (
  input  reset,
  input  in_2,
  input  in_3,
  input  [31:0] in_4,
  input  in_5,
  input  in_6,
  input  [4:0] in_7,
  input  in_8,
  input  in_9,
  input  in_10,
  input  in_11,
  input  in_12,
  input  in_13,
  input  in_14,
  output out_15,
  output out_16,
  output out_17,
  output out_18,
  output out_19,
  output out_20
);

  wire clock_1_out, we;
  wire [31:0] demultiplexer_1_out0;

  Demultiplexer #(.select(5), .width(32), .tristate("true")) demultiplexer_1 (
    .out0(demultiplexer_1_out0), .in(in_4), .sel(in_7));  // open: out1, out2, out3, out4, out5, out6, out7, out8, out9, out10, out11, out12, out13, out14, out15, out16, out17, out18, out19, out20, out21, out22, out23, out24, out25, out26, out27, out28, out29, out30, out31, en
  Demultiplexer demultiplexer_2 (.out0(out_19), .out1(out_20), .in(in_12), .sel(in_14), .en(in_13));
  Clock clock_1 (.out(clock_1_out));
  Register #(.width(32)) register_1 (.D(demultiplexer_1_out0), .en(we), .clk(clock_1_out), .clr(reset));  // open: Q
  Decoder decoder_1 ();  // open: out0, out1, sel, en
  Multiplexer multiplexer_1 (.in0(in_5), .in1(in_6), .out(out_17), .sel(in_8));  // open: en
  Decoder #(.disabled(0)) decoder_2 (.out0(out_15), .out1(out_16), .sel(in_2), .en(in_3));
  Register #(.width(1)) register_2 (.D(in_9), .en(in_10), .Q(out_18), .clk(in_11));  // open: clr
endmodule

module grf (
  input  in_1,
  input  in_2,
  input  in_3,
  input  [4:0] in_4,
  input  [4:0] in_5,
  input  [4:0] in_6,
  input  [31:0] in_7,
  output [31:0] out_8,
  output [31:0] RD2
);

  wire A30, A31, A32, A33, A34, A35, A36, A37, A38, A39, A310, A311, A312, A313, A314, A315, A316, A317,
       A318, A319, A320, A321, A322, A323, A324, A325, A326, A327, A328, A329, A330, A331;
  wire [31:0] multiplexer_1_out, multiplexer_2_out, multiplexer_3_out, multiplexer_4_out, multiplexer_5_out,
       multiplexer_6_out, multiplexer_7_out, multiplexer_8_out, multiplexer_9_out, multiplexer_10_out,
       multiplexer_11_out, multiplexer_12_out, multiplexer_13_out, multiplexer_14_out, multiplexer_15_out,
       multiplexer_16_out, multiplexer_17_out, multiplexer_18_out, multiplexer_19_out, multiplexer_20_out,
       multiplexer_21_out, multiplexer_22_out, multiplexer_23_out, multiplexer_24_out, multiplexer_25_out,
       multiplexer_26_out, multiplexer_27_out, multiplexer_28_out, multiplexer_29_out, multiplexer_30_out,
       multiplexer_31_out, S1, S2, S3, S4, S5, S6, S7, S8, S9, S10, S11, S12, S13, S14, S15, S16, S17, S18,
       S19, S20, S21, S22, S23, S24, S25, S26, S27, S28, S29, S30, S31;

  Multiplexer #(.width(32)) multiplexer_1 (.in0(S1), .in1(in_7), .out(multiplexer_1_out), .sel(A31));  // open: en
  Multiplexer #(.width(32)) multiplexer_2 (.in0(S2), .in1(in_7), .out(multiplexer_2_out), .sel(A32));  // open: en
  Multiplexer #(.width(32)) multiplexer_3 (.in0(S3), .in1(in_7), .out(multiplexer_3_out), .sel(A33));  // open: en
  Multiplexer #(.width(32)) multiplexer_4 (.in0(S4), .in1(in_7), .out(multiplexer_4_out), .sel(A34));  // open: en
  Multiplexer #(.width(32)) multiplexer_5 (.in0(S5), .in1(in_7), .out(multiplexer_5_out), .sel(A35));  // open: en
  Multiplexer #(.width(32)) multiplexer_6 (.in0(S6), .in1(in_7), .out(multiplexer_6_out), .sel(A36));  // open: en
  Multiplexer #(.width(32)) multiplexer_7 (.in0(S7), .in1(in_7), .out(multiplexer_7_out), .sel(A37));  // open: en
  Register #(.width(32)) register_1 (.D(multiplexer_1_out), .en(in_3), .Q(S1), .clk(in_1), .clr(in_2));
  Register #(.width(32)) register_2 (.D(multiplexer_2_out), .en(in_3), .Q(S2), .clk(in_1), .clr(in_2));
  Register #(.width(32)) register_3 (.D(multiplexer_3_out), .en(in_3), .Q(S3), .clk(in_1), .clr(in_2));
  Register #(.width(32)) register_4 (.D(multiplexer_4_out), .en(in_3), .Q(S4), .clk(in_1), .clr(in_2));
  Register #(.width(32)) register_5 (.D(multiplexer_5_out), .en(in_3), .Q(S5), .clk(in_1), .clr(in_2));
  Multiplexer #(.width(32)) multiplexer_8 (.in0(S8), .in1(in_7), .out(multiplexer_8_out), .sel(A38));  // open: en
  Multiplexer #(.width(32)) multiplexer_9 (.in0(S9), .in1(in_7), .out(multiplexer_9_out), .sel(A39));  // open: en
  Multiplexer #(.width(32)) multiplexer_10 (.in0(S10), .in1(in_7), .out(multiplexer_10_out), .sel(A310));  // open: en
  Multiplexer #(.width(32)) multiplexer_11 (.in0(S11), .in1(in_7), .out(multiplexer_11_out), .sel(A311));  // open: en
  Multiplexer #(.width(32)) multiplexer_12 (.in0(S12), .in1(in_7), .out(multiplexer_12_out), .sel(A312));  // open: en
  Multiplexer #(.width(32)) multiplexer_13 (.in0(S13), .in1(in_7), .out(multiplexer_13_out), .sel(A313));  // open: en
  Multiplexer #(.width(32)) multiplexer_14 (.in0(S14), .in1(in_7), .out(multiplexer_14_out), .sel(A314));  // open: en
  Multiplexer #(.width(32)) multiplexer_15 (.in0(S15), .in1(in_7), .out(multiplexer_15_out), .sel(A315));  // open: en
  Multiplexer #(.width(32)) multiplexer_16 (.in0(S16), .in1(in_7), .out(multiplexer_16_out), .sel(A316));  // open: en
  Multiplexer #(.width(32)) multiplexer_17 (.in0(S18), .in1(in_7), .out(multiplexer_17_out), .sel(A318));  // open: en
  Multiplexer #(.width(32)) multiplexer_18 (.in0(S19), .in1(in_7), .out(multiplexer_18_out), .sel(A319));  // open: en
  Multiplexer #(.width(32)) multiplexer_19 (.in0(S20), .in1(in_7), .out(multiplexer_19_out), .sel(A320));  // open: en
  Multiplexer #(.width(32)) multiplexer_20 (.in0(S22), .in1(in_7), .out(multiplexer_20_out), .sel(A322));  // open: en
  Multiplexer #(.width(32)) multiplexer_21 (.in0(S23), .in1(in_7), .out(multiplexer_21_out), .sel(A323));  // open: en
  Multiplexer #(.width(32)) multiplexer_22 (.in0(S25), .in1(in_7), .out(multiplexer_22_out), .sel(A325));  // open: en
  Register #(.width(32)) register_6 (.D(multiplexer_6_out), .en(in_3), .Q(S6), .clk(in_1), .clr(in_2));
  Register #(.width(32)) register_7 (.D(multiplexer_7_out), .en(in_3), .Q(S7), .clk(in_1), .clr(in_2));
  Register #(.width(32)) register_8 (.D(multiplexer_8_out), .en(in_3), .Q(S8), .clk(in_1), .clr(in_2));
  Register #(.width(32)) register_9 (.D(multiplexer_9_out), .en(in_3), .Q(S9), .clk(in_1), .clr(in_2));
  Register #(.width(32)) register_10 (.D(multiplexer_10_out), .en(in_3), .Q(S10), .clk(in_1), .clr(in_2));
  Register #(.width(32)) register_11 (.D(multiplexer_11_out), .en(in_3), .Q(S11), .clk(in_1), .clr(in_2));
  Register #(.width(32)) register_12 (.D(multiplexer_12_out), .en(in_3), .Q(S12), .clk(in_1), .clr(in_2));
  Register #(.width(32)) register_13 (.D(multiplexer_13_out), .en(in_3), .Q(S13), .clk(in_1), .clr(in_2));
  Register #(.width(32)) register_14 (.D(multiplexer_14_out), .en(in_3), .Q(S14), .clk(in_1), .clr(in_2));
  Register #(.width(32)) register_15 (.D(multiplexer_15_out), .en(in_3), .Q(S15), .clk(in_1), .clr(in_2));
  Multiplexer #(.width(32)) multiplexer_23 (.in0(S17), .in1(in_7), .out(multiplexer_23_out), .sel(A317));  // open: en
  Register #(.width(32)) register_16 (.D(multiplexer_17_out), .en(in_3), .Q(S18), .clk(in_1), .clr(in_2));
  Register #(.width(32)) register_17 (.D(multiplexer_18_out), .en(in_3), .Q(S19), .clk(in_1), .clr(in_2));
  Multiplexer #(.width(32)) multiplexer_24 (.in0(S21), .in1(in_7), .out(multiplexer_24_out), .sel(A321));  // open: en
  Register #(.width(32)) register_18 (.D(multiplexer_20_out), .en(in_3), .Q(S22), .clk(in_1), .clr(in_2));
  Multiplexer #(.width(32)) multiplexer_25 (.in0(S24), .in1(in_7), .out(multiplexer_25_out), .sel(A324));  // open: en
  Multiplexer #(.width(32)) multiplexer_26 (.in0(S26), .in1(in_7), .out(multiplexer_26_out), .sel(A326));  // open: en
  Multiplexer #(.width(32)) multiplexer_27 (.in0(S27), .in1(in_7), .out(multiplexer_27_out), .sel(A327));  // open: en
  Multiplexer #(.width(32)) multiplexer_28 (.in0(S28), .in1(in_7), .out(multiplexer_28_out), .sel(A328));  // open: en
  Multiplexer #(.width(32)) multiplexer_29 (.in0(S29), .in1(in_7), .out(multiplexer_29_out), .sel(A329));  // open: en
  Multiplexer #(.width(32)) multiplexer_30 (.in0(S30), .in1(in_7), .out(multiplexer_30_out), .sel(A330));  // open: en
  Multiplexer #(.width(32)) multiplexer_31 (.in0(S31), .in1(in_7), .out(multiplexer_31_out), .sel(A331));  // open: en
  Decoder #(.select(5)) decoder_1 (
    .out0(A30), .out1(A31), .out2(A32), .out3(A33), .out4(A34), .out5(A35), .out6(A36), .out7(A37),
    .out8(A38), .out9(A39), .out10(A310), .out11(A311), .out12(A312), .out13(A313), .out14(A314),
    .out15(A315), .out16(A316), .out17(A317), .out18(A318), .out19(A319), .out20(A320), .out21(A321),
    .out22(A322), .out23(A323), .out24(A324), .out25(A325), .out26(A326), .out27(A327), .out28(A328),
    .out29(A329), .out30(A330), .out31(A331), .sel(in_6));  // open: en
  Register #(.width(32)) register_19 (.D(multiplexer_16_out), .en(in_3), .Q(S16), .clk(in_1), .clr(in_2));
  Register #(.width(32)) register_20 (.D(multiplexer_23_out), .en(in_3), .Q(S17), .clk(in_1), .clr(in_2));
  Register #(.width(32)) register_21 (.D(multiplexer_19_out), .en(in_3), .Q(S20), .clk(in_1), .clr(in_2));
  Register #(.width(32)) register_22 (.D(multiplexer_24_out), .en(in_3), .Q(S21), .clk(in_1), .clr(in_2));
  Register #(.width(32)) register_23 (.D(multiplexer_21_out), .en(in_3), .Q(S23), .clk(in_1), .clr(in_2));
  Register #(.width(32)) register_24 (.D(multiplexer_25_out), .en(in_3), .Q(S24), .clk(in_1), .clr(in_2));
  Register #(.width(32)) register_25 (.D(multiplexer_22_out), .en(in_3), .Q(S25), .clk(in_1), .clr(in_2));
  Register #(.width(32)) register_26 (.D(multiplexer_26_out), .en(in_3), .Q(S26), .clk(in_1), .clr(in_2));
  Register #(.width(32)) register_27 (.D(multiplexer_27_out), .en(in_3), .Q(S27), .clk(in_1), .clr(in_2));
  Register #(.width(32)) register_28 (.D(multiplexer_28_out), .en(in_3), .Q(S28), .clk(in_1), .clr(in_2));
  Register #(.width(32)) register_29 (.D(multiplexer_29_out), .en(in_3), .Q(S29), .clk(in_1), .clr(in_2));
  Register #(.width(32)) register_30 (.D(multiplexer_30_out), .en(in_3), .Q(S30), .clk(in_1), .clr(in_2));
  Register #(.width(32)) register_31 (.D(multiplexer_31_out), .en(in_3), .Q(S31), .clk(in_1), .clr(in_2));
  Multiplexer #(.select(5), .width(32)) multiplexer_32 (
    .in0({32{1'b0}}), .in1(S1), .in2(S2), .in3(S3), .in4(S4), .in5(S5), .in6(S6), .in7(S7), .in8(S8),
    .in9(S9), .in10(S10), .in11(S11), .in12(S12), .in13(S13), .in14(S14), .in15(S15), .in16(S16), .in17(S17),
    .in18(S18), .in19(S19), .in20(S20), .in21(S21), .in22(S22), .in23(S23), .in24(S24), .in25(S25),
    .in26(S26), .in27(S27), .in28(S28), .in29(S29), .in30(S30), .in31(S31), .out(out_8), .sel(in_4));  // open: en
  Multiplexer #(.select(5), .width(32)) multiplexer_33 (
    .in0({32{1'b0}}), .in1(S1), .in2(S2), .in3(S3), .in4(S4), .in5(S5), .in6(S6), .in7(S7), .in8(S8),
    .in9(S9), .in10(S10), .in11(S11), .in12(S12), .in13(S13), .in14(S14), .in15(S15), .in16(S16), .in17(S17),
    .in18(S18), .in19(S19), .in20(S20), .in21(S21), .in22(S22), .in23(S23), .in24(S24), .in25(S25),
    .in26(S26), .in27(S27), .in28(S28), .in29(S29), .in30(S30), .in31(S31), .out(RD2), .sel(in_5));  // open: en

  // Other names for the same wires on the sheet: A1[4:0] = in_4; A2[4:0] = in_5; A3[4:0] = in_6; clk = in_1;
  //   reset = in_2; wd[31:0] = in_7; we = in_3
endmodule
