// Logisim project P0_L0_GRF2.circ as structural Verilog: 1 circuit, main circuit grf
module grf (
  input  in_1,
  input  in_2,
  input  in_3,
  input  [4:0] in_4,
  input  [4:0] in_5,
  input  [4:0] in_6,
  input  [31:0] in_7,
  output [31:0] out_8,
  output [31:0] RD2
);

  wire [31:0] S0, S1, S2, S3, S4, S5, S6, S7, S8, S9, S10, S11, S12, S13, S14, S15, S16, S17, S18, S19, S20,
       S21, S22, S23, S24, S25, S26, S27, S28, S29, S30, S31, wd0, wd1, wd2, wd3, wd4, wd5, wd6, wd7, wd8,
       wd9, wd10, wd11, wd12, wd13, wd14, wd15, wd16, wd17, wd18, wd19, wd20, wd21, wd22, wd23, wd24, wd25,
       wd26, wd27, wd28, wd29, wd30, wd31;

  Register #(.width(32)) register_1 (.D(wd1), .en(in_3), .Q(S1), .clk(in_1), .clr(in_2));
  Register #(.width(32)) register_2 (.D(wd2), .en(in_3), .Q(S2), .clk(in_1), .clr(in_2));
  Register #(.width(32)) register_3 (.D(wd3), .en(in_3), .Q(S3), .clk(in_1), .clr(in_2));
  Register #(.width(32)) register_4 (.D(wd4), .en(in_3), .Q(S4), .clk(in_1), .clr(in_2));
  Register #(.width(32)) register_5 (.D(wd5), .en(in_3), .Q(S5), .clk(in_1), .clr(in_2));
  Register #(.width(32)) register_6 (.D(wd6), .en(in_3), .Q(S6), .clk(in_1), .clr(in_2));
  Register #(.width(32)) register_7 (.D(wd7), .en(in_3), .Q(S7), .clk(in_1), .clr(in_2));
  Register #(.width(32)) register_8 (.D(wd8), .en(in_3), .Q(S8), .clk(in_1), .clr(in_2));
  Register #(.width(32)) register_9 (.D(wd9), .en(in_3), .Q(S9), .clk(in_1), .clr(in_2));
  Register #(.width(32)) register_10 (.D(wd10), .en(in_3), .Q(S10), .clk(in_1), .clr(in_2));
  Register #(.width(32)) register_11 (.D(wd11), .en(in_3), .Q(S11), .clk(in_1), .clr(in_2));
  Register #(.width(32)) register_12 (.D(wd12), .en(in_3), .Q(S12), .clk(in_1), .clr(in_2));
  Register #(.width(32)) register_13 (.D(wd13), .en(in_3), .Q(S13), .clk(in_1), .clr(in_2));
  Register #(.width(32)) register_14 (.D(wd14), .en(in_3), .Q(S14), .clk(in_1), .clr(in_2));
  Register #(.width(32)) register_15 (.D(wd15), .en(in_3), .Q(S15), .clk(in_1), .clr(in_2));
  Register #(.width(32)) register_16 (.D(wd16), .en(in_3), .Q(S16), .clk(in_1), .clr(in_2));
  Multiplexer #(.select(5), .width(32)) multiplexer_1 (
    .in0({32{1'b0}}), .in1(S1), .in2(S2), .in3(S3), .in4(S4), .in5(S5), .in6(S6), .in7(S7), .in8(S8),
    .in9(S9), .in10(S10), .in11(S11), .in12(S12), .in13(S13), .in14(S14), .in15(S15), .in16(S16), .in17(S17),
    .in18(S18), .in19(S19), .in20(S20), .in21(S21), .in22(S22), .in23(S23), .in24(S24), .in25(S25),
    .in26(S26), .in27(S27), .in28(S28), .in29(S29), .in30(S30), .in31(S31), .out(out_8), .sel(in_4));  // open: en
  Register #(.width(32)) register_17 (.D(wd17), .en(in_3), .Q(S17), .clk(in_1), .clr(in_2));
  Register #(.width(32)) register_18 (.D(wd18), .en(in_3), .Q(S18), .clk(in_1), .clr(in_2));
  Register #(.width(32)) register_19 (.D(wd19), .en(in_3), .Q(S19), .clk(in_1), .clr(in_2));
  Register #(.width(32)) register_20 (.D(wd20), .en(in_3), .Q(S20), .clk(in_1), .clr(in_2));
  Register #(.width(32)) register_21 (.D(wd21), .en(in_3), .Q(S21), .clk(in_1), .clr(in_2));
  Register #(.width(32)) register_22 (.D(wd22), .en(in_3), .Q(S22), .clk(in_1), .clr(in_2));
  Register #(.width(32)) register_23 (.D(wd23), .en(in_3), .Q(S23), .clk(in_1), .clr(in_2));
  Register #(.width(32)) register_24 (.D(wd24), .en(in_3), .Q(S24), .clk(in_1), .clr(in_2));
  Register #(.width(32)) register_25 (.D(wd25), .en(in_3), .Q(S25), .clk(in_1), .clr(in_2));
  Register #(.width(32)) register_26 (.D(wd26), .en(in_3), .Q(S26), .clk(in_1), .clr(in_2));
  Register #(.width(32)) register_27 (.D(wd27), .en(in_3), .Q(S27), .clk(in_1), .clr(in_2));
  Register #(.width(32)) register_28 (.D(wd28), .en(in_3), .Q(S28), .clk(in_1), .clr(in_2));
  Multiplexer #(.select(5), .width(32)) multiplexer_2 (
    .in0({32{1'b0}}), .in1(S1), .in2(S2), .in3(S3), .in4(S4), .in5(S5), .in6(S6), .in7(S7), .in8(S8),
    .in9(S9), .in10(S10), .in11(S11), .in12(S12), .in13(S13), .in14(S14), .in15(S15), .in16(S16), .in17(S17),
    .in18(S18), .in19(S19), .in20(S20), .in21(S21), .in22(S22), .in23(S23), .in24(S24), .in25(S25),
    .in26(S26), .in27(S27), .in28(S28), .in29(S29), .in30(S30), .in31(S31), .out(RD2), .sel(in_5));  // open: en
  Register #(.width(32)) register_29 (.D(wd29), .en(in_3), .Q(S29), .clk(in_1), .clr(in_2));
  Register #(.width(32)) register_30 (.D(wd30), .en(in_3), .Q(S30), .clk(in_1), .clr(in_2));
  Register #(.width(32)) register_31 (.D(wd31), .en(in_3), .Q(S31), .clk(in_1), .clr(in_2));
  Register #(.width(32)) register_32 (.D(wd0), .en(1'b0), .Q(S0), .clk(in_1), .clr(in_2));
  Demultiplexer #(.select(5), .width(32), .tristate("true")) demultiplexer_1 (
    .out0(wd0), .out1(wd1), .out2(wd2), .out3(wd3), .out4(wd4), .out5(wd5), .out6(wd6), .out7(wd7),
    .out8(wd8), .out9(wd9), .out10(wd10), .out11(wd11), .out12(wd12), .out13(wd13), .out14(wd14),
    .out15(wd15), .out16(wd16), .out17(wd17), .out18(wd18), .out19(wd19), .out20(wd20), .out21(wd21),
    .out22(wd22), .out23(wd23), .out24(wd24), .out25(wd25), .out26(wd26), .out27(wd27), .out28(wd28),
    .out29(wd29), .out30(wd30), .out31(wd31), .in(in_7), .sel(in_6), .en(in_3));

  // Other names for the same wires on the sheet: A1[4:0] = in_4; A2[4:0] = in_5; A3[4:0] = in_6; clk = in_1;
  //   reset = in_2; wd[31:0] = in_7; we = in_3
endmodule
