// Logisim project P0_L1_ftoi.circ as structural Verilog
module ftoi (
  input  [15:0] in_1,
  output [31:0] out_2
);

  wire expsign, judge_out_2;
  wire [4:0] M, subtractor_1_out;
  wire [31:0] multiplexer_1_out, multiplexer_2_out, not_1_out, \正res , \负res ;

  \左移模块  \u_左移模块  (.fractions(in_1[9:0]), .M(M), .res(\正res ));
  assign not_1_out = ~\正res ;  // NOT_Gate not_1, 32 bits wide
  Adder #(.width(32)) adder_1 (.a(not_1_out), .b(32'h1), .out(\负res ));  // open: cin, cout
  Subtractor #(.width(5)) subtractor_1 (.a(in_1[14:10]), .b(5'b01111), .out(subtractor_1_out));  // open: bin, bout
  Multiplexer #(.width(32)) multiplexer_1 (
    .in0(\正res ), .in1(\负res ), .out(multiplexer_1_out), .sel(in_1[15]));  // open: en
  \补码转原码  \u_补码转原码  (.in_1(subtractor_1_out), .\output (M), .sign(expsign));
  Multiplexer #(.width(32)) multiplexer_2 (
    .in0(multiplexer_1_out), .in1({32{1'b0}}), .out(multiplexer_2_out), .sel(expsign));  // open: en
  judge judge (.in_1(in_1[14:10]), .out_2(judge_out_2));
  Multiplexer #(.width(32)) multiplexer_3 (
    .in0({32{1'b0}}), .in1(multiplexer_2_out), .out(out_2), .sel(judge_out_2));  // open: en

  // Other names for the same wires on the sheet: fraction[9:0] = in_1[9:0]; exponent[4:0] = in_1[14:10];
  //   sign = in_1[15]; 移位完成[31:0] = \正res 
endmodule

module judge (
  input  [4:0] in_1,
  output out_2
);

  wire comparator_1_gt, comparator_2_lt;

  Comparator #(.width(5), .mode("unsigned")) comparator_1 (
    .a(in_1), .b({5{1'b0}}), .gt(comparator_1_gt));  // open: eq, lt
  Comparator #(.width(5), .mode("unsigned")) comparator_2 (
    .a(in_1), .b({5{1'b1}}), .lt(comparator_2_lt));  // open: gt, eq
  and and_1 (out_2, comparator_1_gt, comparator_2_lt);
endmodule

module \补码转原码  (
  input  [4:0] in_1,
  output [4:0] \output ,
  output sign
);

  wire [3:0] multiplexer_1_out, subtractor_1_out, \负数 ;

  Subtractor #(.width(4)) subtractor_1 (.a(in_1[3:0]), .b(4'b0001), .out(subtractor_1_out));  // open: bin, bout
  assign \负数  = ~subtractor_1_out;  // NOT_Gate not_1, 4 bits wide
  Multiplexer #(.width(4)) multiplexer_1 (
    .in0(in_1[3:0]), .in1(\负数 ), .out(multiplexer_1_out), .sel(in_1[4]));  // open: en
  assign \output  = {{1{1'b0}}, multiplexer_1_out};  // Bit_Extender bit_extender_1

  assign sign = in_1[4];

  // Other names for the same wires on the sheet: number[3:0] = in_1[3:0]
endmodule

module \左移模块  (
  input  [9:0] fractions,
  input  [4:0] M,
  output [31:0] res
);

  wire comparator_1_gt;
  wire [4:0] \移动位数1 , \移动位数2 ;
  wire [31:0] fractions_t, \大于10的结果 , \小于等于10的结果 ;

  assign fractions_t = {{21{1'b0}}, {1'b1, fractions}};  // Bit_Extender bit_extender_1
  Subtractor #(.width(5)) subtractor_1 (.a(5'b01010), .b(M), .out(\移动位数1 ));  // open: bin, bout
  Subtractor #(.width(5)) subtractor_2 (.a(M), .b(5'b01010), .out(\移动位数2 ));  // open: bin, bout
  Shifter #(.width(32), .shift("ar")) shifter_1 (.in(fractions_t), .\dist (\移动位数1 ), .out(\小于等于10的结果 ));
  Shifter #(.width(32)) shifter_2 (.in(fractions_t), .\dist (\移动位数2 ), .out(\大于10的结果 ));
  Comparator #(.width(5), .mode("unsigned")) comparator_1 (.a(M), .b(5'b01010), .gt(comparator_1_gt));  // open: eq, lt
  Multiplexer #(.width(32)) multiplexer_1 (
    .in0(\小于等于10的结果 ), .in1(\大于10的结果 ), .out(res), .sel(comparator_1_gt));  // open: en

  // Other names for the same wires on the sheet: 移动位数[4:0] = M
endmodule
