// Logisim project P0_L1_navigation_2020.circ as structural Verilog: 4 circuits, main circuit navigation
module navigation (
  input  [1:0] dir,
  input  CLK,
  input  RESET,
  output ARRIVE,
  output HIT,
  output HIT_2
);

  wire and_2_out, comparator_1_eq, comparator_2_eq, comparator_3_eq, \hit输出_1_hit , S0, s00, S1, S2, s11, s22;

  \状态转移  \u_状态转移  (.S2(S2), .S1(S1), .S0(S0), .IN1(dir[1]), .IN0(dir[0]), .S22(s22), .S11(s11), .S00(s00));
  \寄存器  \u_寄存器  (.in_1(s22), .in_2(s11), .in_3(s00), .clk(CLK), .reset(RESET), .out_6(S2), .out_7(S1), .out_8(S0));
  \hit输出  \hit输出_1  (.S2(S2), .S1(S1), .S0(S0), .IN1(dir[1]), .IN0(dir[0]), .hit(\hit输出_1_hit ));
  Comparator #(.width(1)) comparator_1 (.a(S2), .b(s22), .eq(comparator_1_eq));  // open: gt, lt
  Comparator #(.width(1)) comparator_2 (.a(S1), .b(s11), .eq(comparator_2_eq));  // open: gt, lt
  Comparator #(.width(1)) comparator_3 (.a(S0), .b(s00), .eq(comparator_3_eq));  // open: gt, lt
  Register #(.width(1)) register_1 (.D(\hit输出_1_hit ), .Q(HIT), .clk(CLK), .clr(RESET));  // open: en
  and and_1 (ARRIVE, ~S0, ~S1, S2);  // AND_Gate
  and and_2 (and_2_out, comparator_1_eq, comparator_2_eq, comparator_3_eq);
  Register #(.width(1)) register_2 (.D(and_2_out), .Q(HIT_2), .clk(CLK), .clr(RESET));  // open: en

  // Other names for the same wires on the sheet: IN0 = dir[0]; IN1 = dir[1]

  // Notes on the sheet:
  //   这两种方法应该都正确
  //   Moore状态机，输出不直接响应输入，输出前面要加一个寄存器
endmodule

module \状态转移  (
  input  S2,
  input  S1,
  input  S0,
  input  IN1,
  input  IN0,
  output S22,
  output S11,
  output S00
);

  wire and_1_out, and_2_out, and_3_out, and_4_out, and_5_out, and_6_out, and_7_out, and_8_out, and_9_out,
       and_10_out, and_11_out, not_1_out, not_2_out, not_3_out, not_4_out, not_5_out, not_6_out, not_7_out,
       not_8_out, not_9_out, not_10_out, not_11_out, not_12_out, not_13_out, not_14_out, not_15_out,
       not_16_out, not_17_out;

  not not_1 (not_1_out, S0);
  not not_2 (not_2_out, IN1);
  not not_3 (not_3_out, IN0);
  not not_4 (not_4_out, IN1);
  not not_5 (not_5_out, S1);
  not not_6 (not_6_out, IN1);
  not not_7 (not_7_out, IN1);
  not not_8 (not_8_out, IN0);
  not not_9 (not_9_out, S0);
  not not_10 (not_10_out, IN1);
  not not_11 (not_11_out, S0);
  not not_12 (not_12_out, IN0);
  not not_13 (not_13_out, S2);
  not not_14 (not_14_out, S1);
  not not_15 (not_15_out, IN1);
  not not_16 (not_16_out, IN0);
  not not_17 (not_17_out, IN0);
  and and_1 (and_1_out, S1, not_1_out, not_2_out, not_3_out);
  and and_2 (and_2_out, S1, S0, not_4_out, IN0);
  and and_3 (and_3_out, not_5_out, S0, not_6_out);
  and and_4 (and_4_out, S0, not_7_out, not_8_out);
  and and_5 (and_5_out, S1, not_9_out, not_10_out, IN0);
  and and_6 (and_6_out, S1, not_11_out, IN1, not_12_out);
  and and_7 (and_7_out, S1, S0, IN1, IN0);
  and and_8 (and_8_out, not_13_out, not_14_out, not_15_out, not_16_out);
  and and_9 (and_9_out, S0, IN1, IN0);
  and and_10 (and_10_out, S1, IN1, IN0);
  and and_11 (and_11_out, S1, S0, not_17_out);
  or or_1 (S22, and_1_out, and_2_out);
  or or_2 (S11, and_3_out, and_4_out, and_5_out, and_6_out, and_7_out);
  or or_3 (S00, and_8_out, and_9_out, and_10_out, and_11_out);
endmodule

module \hit输出  (
  input  S2,
  input  S1,
  input  S0,
  input  IN1,
  input  IN0,
  output hit
);

  wire and_1_out, and_2_out, and_3_out, and_4_out, and_5_out, not_1_out, not_2_out, not_3_out, not_4_out,
       not_5_out, not_6_out, not_7_out, not_8_out, not_9_out, not_10_out, not_11_out;

  not not_1 (not_1_out, S2);
  not not_2 (not_2_out, S0);
  not not_3 (not_3_out, IN1);
  not not_4 (not_4_out, S2);
  not not_5 (not_5_out, S1);
  not not_6 (not_6_out, S0);
  not not_7 (not_7_out, S2);
  not not_8 (not_8_out, S0);
  not not_9 (not_9_out, IN0);
  not not_10 (not_10_out, IN1);
  not not_11 (not_11_out, IN0);
  and and_1 (and_1_out, not_1_out, not_2_out, not_3_out, IN0);
  and and_2 (and_2_out, not_4_out, not_5_out, not_6_out, IN1);
  and and_3 (and_3_out, not_7_out, not_8_out, IN1, not_9_out);
  and and_4 (and_4_out, S0, IN1, IN0);
  and and_5 (and_5_out, S1, S0, not_10_out, not_11_out);
  or or_1 (hit, and_1_out, and_2_out, and_3_out, and_4_out, and_5_out);
endmodule

module \寄存器  (
  input  in_1,
  input  in_2,
  input  in_3,
  input  clk,
  input  reset,
  output out_6,
  output out_7,
  output out_8
);

  wire counter_1_q, register_1_q, register_2_q, register_3_q;

  Register #(.width(1)) register_1 (.D(in_1), .Q(register_1_q), .clk(clk), .clr(reset));  // open: en
  Register #(.width(1)) register_2 (.D(in_2), .Q(register_2_q), .clk(clk), .clr(reset));  // open: en
  Register #(.width(1)) register_3 (.D(in_3), .Q(register_3_q), .clk(clk), .clr(reset));  // open: en
  Multiplexer multiplexer_1 (.in0(1'b0), .in1(register_1_q), .out(out_6), .sel(counter_1_q));  // open: en
  Multiplexer multiplexer_2 (.in0(1'b0), .in1(register_2_q), .out(out_7), .sel(counter_1_q));  // open: en
  Multiplexer multiplexer_3 (.in0(1'b0), .in1(register_3_q), .out(out_8), .sel(counter_1_q));  // open: en
  Counter #(.width(1), .max('h1), .ongoal("stay")) counter_1 (
    .Q(counter_1_q), .clk(clk));  // open: load, D, count, carry, clr
endmodule
