// Logisim project practice_4bitsort.circ as structural Verilog
module _1_bitswap (
  input  A,
  input  B,
  input  swap,
  output AA,
  output BB
);

  wire and_1_out, and_2_out, and_3_out, and_4_out, not_1_out, not_2_out;

  not not_1 (not_1_out, swap);
  not not_2 (not_2_out, swap);
  and and_1 (and_1_out, B, swap);
  and and_2 (and_2_out, A, not_1_out);
  and and_3 (and_3_out, B, not_2_out);
  and and_4 (and_4_out, A, swap);
  or or_1 (AA, and_1_out, and_2_out);
  or or_2 (BB, and_3_out, and_4_out);
endmodule

module _4_bitswap (
  input  [3:0] A,
  input  [3:0] B,
  input  swap,
  output [3:0] AA,
  output [3:0] BB
);

  _1_bitswap u_1_bitswap_1 (.A(A[0]), .B(B[0]), .swap(swap), .AA(AA[0]), .BB(BB[0]));
  _1_bitswap u_1_bitswap_2 (.A(A[1]), .B(B[1]), .swap(swap), .AA(AA[1]), .BB(BB[1]));
  _1_bitswap u_1_bitswap_3 (.A(A[2]), .B(B[2]), .swap(swap), .AA(AA[2]), .BB(BB[2]));
  _1_bitswap u_1_bitswap_4 (.A(A[3]), .B(B[3]), .swap(swap), .AA(AA[3]), .BB(BB[3]));
endmodule

module _4_bitsort (
  input  [3:0] in_1,
  input  [3:0] in_2,
  input  [3:0] in_3,
  input  [3:0] in_4,
  output [3:0] out_5,
  output [3:0] out_6,
  output [3:0] out_7,
  output [3:0] out_8
);

  wire comparator_1_lt, comparator_2_lt, comparator_3_lt, comparator_4_lt;
  wire [3:0] n4_bitswap_1_aa, n4_bitswap_1_bb, n4_bitswap_2_aa, n4_bitswap_2_bb;

  Comparator #(.width(4), .mode("unsigned")) comparator_1 (.a(in_1), .b(in_2), .lt(comparator_1_lt));  // open: gt, eq
  Comparator #(.width(4), .mode("unsigned")) comparator_2 (.a(in_3), .b(in_4), .lt(comparator_2_lt));  // open: gt, eq
  _4_bitswap u_4_bitswap_1 (.A(in_1), .B(in_2), .swap(comparator_1_lt), .AA(n4_bitswap_1_aa), .BB(n4_bitswap_1_bb));
  _4_bitswap u_4_bitswap_2 (.A(in_3), .B(in_4), .swap(comparator_2_lt), .AA(n4_bitswap_2_aa), .BB(n4_bitswap_2_bb));
  Comparator #(.width(4), .mode("unsigned")) comparator_3 (
    .a(n4_bitswap_1_aa), .b(n4_bitswap_2_aa), .lt(comparator_3_lt));  // open: gt, eq
  Comparator #(.width(4), .mode("unsigned")) comparator_4 (
    .a(n4_bitswap_1_bb), .b(n4_bitswap_2_bb), .lt(comparator_4_lt));  // open: gt, eq
  _4_bitswap u_4_bitswap_3 (.A(n4_bitswap_1_aa), .B(n4_bitswap_2_aa), .swap(comparator_3_lt), .AA(out_5), .BB(out_6));
  _4_bitswap u_4_bitswap_4 (.A(n4_bitswap_1_bb), .B(n4_bitswap_2_bb), .swap(comparator_4_lt), .AA(out_7), .BB(out_8));
endmodule
