// Logisim project CPUU.circ as structural Verilog: 17 circuits, main circuit main
module main (
  input  Reset,
  output [31:0] out_2,
  output out_3,
  output [4:0] out_4,
  output [31:0] out_5,
  output out_6,
  output [4:0] out_7,
  output [31:0] out_8
);

  wire clk, Zero;
  wire [1:0] ASel, BSel, DMType, EXTop, NPCOp, WDSel, WRSel;
  wire [4:0] _10_6, ALUop, splitter_1__15_11, splitter_1__20_16, splitter_1__25_21;
  wire [5:0] Funct, Opcode;
  wire [15:0] splitter_1_imm_offset;
  wire [25:0] splitter_1_j_index;
  wire [31:0] ALUres, Bimm, DMres, ext_1_out, multiplexer_3_out, multiplexer_4_out, npc_1_npc,
       pc_1_addressout, PC_4, rf_1_out_8, sllshamt;

  // Probe on npc_1_npc
  NPC npc_1 (
    .PC(pc_1_addressout), .Bimm(Bimm), .Jimm(splitter_1_j_index), .NPC(npc_1_npc), .NPCOp(NPCOp),
    .zero(Zero), .PC_4(PC_4));  // open: Ra
  PC pc_1 (.Addressin(npc_1_npc), .Addressout(pc_1_addressout), .Clk(clk), .Reset(Reset));
  // Probe on pc_1_addressout
  IM im_1 (.Address(pc_1_addressout), .Instruction(out_2));
  // Mips_Probe mips_probe_1: pin names not known; wires that end beside it: out_2
  // Probe on out_2
  Clock u_clk (.out(clk));
  Splitter splitter_1 (
    .in_1(out_2), .Opcode(Opcode), ._25_21(splitter_1__25_21), ._20_16(splitter_1__20_16),
    ._15_11(splitter_1__15_11), ._10_6(_10_6), ._5_0(Funct), .Imm_Offset(splitter_1_imm_offset),
    .j_index(splitter_1_j_index));
  // Probe on splitter_1__20_16
  // Probe on out_4
  // Probe on splitter_1__25_21
  Multiplexer #(.select(2), .width(5)) multiplexer_1 (
    .in0(splitter_1__20_16), .in1(splitter_1__15_11), .in2({5{1'b1}}), .out(out_4), .sel(WRSel));  // open: in3, en
  Controller controller (
    .Opcode(Opcode), .Funct(Funct), .NPCOp(NPCOp), .WRSel(WRSel), .WDSel(WDSel), .RFWE(out_3), .EXTop(EXTop),
    .BSel(BSel), .ALUop(ALUop), .DMWE(out_6), .DMtype(DMType), .ASel(ASel));  // open: JudgeB
  Multiplexer #(.select(2), .width(32)) multiplexer_2 (
    .in0({ALUres[31:7], out_7, ALUres[1:0]}), .in1(DMres), .in2(PC_4), .out(out_5), .sel(WDSel));  // open: in3, en
  EXT ext_1 (.Imm_Offset(splitter_1_imm_offset), .Out(ext_1_out), .EXTOp(EXTop));
  RF rf_1 (
    .in_4(splitter_1__25_21), .in_5(splitter_1__20_16), .in_6(out_4), .in_7(out_5), .out_8(rf_1_out_8),
    .RD2(out_8), .in_1(clk), .in_2(Reset), .in_3(out_3));
  Multiplexer #(.select(2), .width(32)) multiplexer_3 (
    .in0(rf_1_out_8), .in1(sllshamt), .out(multiplexer_3_out), .sel(ASel));  // open: in2, in3, en
  Multiplexer #(.select(2), .width(32)) multiplexer_4 (
    .in0(out_8), .in1(ext_1_out), .out(multiplexer_4_out), .sel(BSel));  // open: in2, in3, en
  Shifter #(.width(32)) shifter_1 (.in(ext_1_out), .\dist (5'b00010), .out(Bimm));
  Shifter #(.width(32), .shift("lr")) shifter_2 (.in(ext_1_out), .\dist (5'b00110), .out(sllshamt));
  ALU alu_1 (
    .A(multiplexer_3_out), .B(multiplexer_4_out), .Res({ALUres[31:7], out_7, ALUres[1:0]}), .ALUop(ALUop),
    .Zero(Zero));  // open: overflow
  DM dm_1 (
    .Address({ALUres[31:7], out_7, ALUres[1:0]}), .WD(out_8), .Clk(clk), .Reset(Reset), .DMWE(out_6),
    .DMtype(DMType), .NRD(DMres));

  // Other names for the same wires on the sheet: ALUres[6:2] = out_7; MemAddr[4:0] = out_7; Instr[31:0] = out_2;
  //   MemData[31:0] = out_8; DMWE = out_6; MemWrite = out_6; RedAddr[4:0] = out_4; RegData[31:0] = out_5;
  //   RegWrite = out_3; RFWE = out_3

  // Notes on the sheet:
  //   ALU
endmodule

module IM (
  input  [31:0] Address,
  output [31:0] Instruction
);

  wire [9:0] bit_extender_1_out;
  wire [31:0] shifter_1_out;

  Shifter #(.width(32), .shift("lr")) shifter_1 (.in(Address), .\dist (5'b00010), .out(shifter_1_out));
  Bit_Extender #(.in_width(32), .out_width(10)) bit_extender_1 (.in(shifter_1_out), .out(bit_extender_1_out));
  ROM #(.addrWidth(10), .dataWidth(32)) rom_1 (.addr(bit_extender_1_out), .data(Instruction));  // open: sel

  // Notes on the sheet:
  //   contents of rom_1 (hex, n*v repeats v):
  //   350804d2 3529162e 1095024 ac0a0000 356bfff3 a50b0002 810c0003 1886821
endmodule

module PC (
  input  Clk,
  input  Reset,
  input  [31:0] Addressin,
  output [31:0] Addressout
);

  Register #(.width(32)) register_1 (.D(Addressin), .Q(Addressout), .clk(Clk), .clr(Reset));  // open: en
endmodule

module NPC (
  input  [1:0] NPCOp,
  input  [31:0] PC,
  input  [31:0] Bimm,
  input  zero,
  input  [25:0] Jimm,
  input  [31:0] Ra,
  output [31:0] PC_4,
  output [31:0] NPC
);

  wire [31:0] adder_2_out, B;

  Adder #(.width(32)) adder_1 (.a(PC), .b(32'h4), .out(PC_4));  // open: cin, cout
  Adder #(.width(32)) adder_2 (.a(PC_4), .b(Bimm), .out(adder_2_out));  // open: cin, cout
  Multiplexer #(.width(32)) multiplexer_1 (.in0(PC_4), .in1(adder_2_out), .out(B), .sel(zero));  // open: en
  Multiplexer #(.select(2), .width(32)) multiplexer_2 (
    .in0(PC_4), .in1(B), .in2({PC[31:28], Jimm, 2'b00}), .out(NPC), .sel(NPCOp));  // open: in3, en

  // Other names for the same wires on the sheet: JPC[31:2] = {PC[31:28], Jimm}
endmodule

module Splitter (
  input  [31:0] in_1,
  output [5:0] Opcode,
  output [4:0] _25_21,
  output [4:0] _20_16,
  output [4:0] _15_11,
  output [4:0] _10_6,
  output [5:0] _5_0,
  output [15:0] Imm_Offset,
  output [25:0] j_index
);


  assign _5_0 = in_1[5:0];
  assign _10_6 = in_1[10:6];
  assign _15_11 = in_1[15:11];
  assign _20_16 = in_1[20:16];
  assign _25_21 = in_1[25:21];
  assign Imm_Offset = in_1[15:0];
  assign j_index = in_1[25:0];
  assign Opcode = in_1[31:26];
endmodule

module Controller (
  input  [5:0] Opcode,
  input  [5:0] Funct,
  input  [4:0] JudgeB,
  output [1:0] NPCOp,
  output [1:0] WRSel,
  output [1:0] WDSel,
  output RFWE,
  output [1:0] EXTop,
  output [1:0] BSel,
  output [4:0] ALUop,
  output DMWE,
  output [1:0] DMtype,
  output [1:0] ASel
);

  wire \和逻辑_1_addu , \和逻辑_1_and , \和逻辑_1_beq , \和逻辑_1_j , \和逻辑_1_jal , \和逻辑_1_lb , \和逻辑_1_lui , \和逻辑_1_lw ,
       \和逻辑_1_nop , \和逻辑_1_ori , \和逻辑_1_sh , \和逻辑_1_sll , \和逻辑_1_subu , \和逻辑_1_sw ;

  \和逻辑  \u_和逻辑_1  (
    .op(Opcode), .funct(Funct), .Ori(\和逻辑_1_ori ), .Lw(\和逻辑_1_lw ), .Sw(\和逻辑_1_sw ), .Beq(\和逻辑_1_beq ),
    .Lui(\和逻辑_1_lui ), .Addu(\和逻辑_1_addu ), .Subu(\和逻辑_1_subu ), .Nop(\和逻辑_1_nop ), .Sh(\和逻辑_1_sh ),
    .j(\和逻辑_1_j ), .\and (\和逻辑_1_and ), .jal(\和逻辑_1_jal ), .sll(\和逻辑_1_sll ), .lb(\和逻辑_1_lb ));
  \或逻辑  \u_或逻辑_1  (
    .Addu(\和逻辑_1_addu ), .Subu(\和逻辑_1_subu ), .Ori(\和逻辑_1_ori ), .Lw(\和逻辑_1_lw ), .Sw(\和逻辑_1_sw ),
    .Beq(\和逻辑_1_beq ), .Lui(\和逻辑_1_lui ), .Nop(\和逻辑_1_nop ), .NPCOp(NPCOp), .WRSel(WRSel), .WDSel(WDSel),
    .RFWE(RFWE), .EXTOp(EXTop), .BSel(BSel), .ALUop(ALUop), .DMWE(DMWE), .sh(\和逻辑_1_sh ), .DMtype(DMtype),
    .j(\和逻辑_1_j ), .\and (\和逻辑_1_and ), .jal(\和逻辑_1_jal ), .sll(\和逻辑_1_sll ), .ASel(ASel), .lb(\和逻辑_1_lb ));
endmodule

module \和逻辑  (
  input  [5:0] op,
  input  [5:0] funct,
  output Addu,
  output Subu,
  output Ori,
  output Lw,
  output Sw,
  output Beq,
  output Lui,
  output Nop,
  output Sh,
  output j,
  output \and ,
  output jal,
  output sll,
  output lb
);

  wire addu_out, and_10_out, beq_out, j_out, jal_out, lb_out, lui_out, lw_out, nop_out, not_1_out, not_2_out,
       not_3_out, not_4_out, not_5_out, not_6_out, not_7_out, not_8_out, not_9_out, not_10_out, not_11_out,
       not_12_out, op_0, ori_out, sh_out, sll_out, subu_out, sw_out;

  Comparator #(.width(6)) comparator_1 (.a({6{1'b0}}), .b(op), .eq(op_0));  // open: gt, lt
  not not_1 (not_1_out, op[5]);
  not not_2 (not_2_out, op[4]);
  not not_3 (not_3_out, op[3]);
  not not_4 (not_4_out, op[2]);
  not not_5 (not_5_out, op[1]);
  not not_6 (not_6_out, op[0]);
  and u_ori (ori_out, not_1_out, not_2_out, op[3], op[2], not_5_out, op[0]);
  and u_lw (lw_out, op[5], not_2_out, not_3_out, not_4_out, op[1], op[0]);
  and u_sw (sw_out, op[5], not_2_out, op[3], not_4_out, op[1], op[0]);
  and u_beq (beq_out, not_1_out, not_2_out, not_3_out, op[2], not_5_out, not_6_out);
  and u_lui (lui_out, not_1_out, not_2_out, op[3], op[2], op[1], op[0]);
  and u_sh (sh_out, op[5], not_2_out, op[3], not_4_out, not_5_out, op[0]);
  and u_j (j_out, not_6_out, op[1], not_4_out, not_3_out, not_2_out, not_1_out);
  and u_jal (jal_out, not_1_out, not_2_out, not_3_out, not_4_out, op[1], op[0]);
  and u_lb (lb_out, op[5], not_2_out, not_3_out, not_4_out, not_5_out, not_6_out);
  and and_1 (Ori, ~op_0, ori_out);  // AND_Gate
  and and_2 (Lw, ~op_0, lw_out);  // AND_Gate
  and and_3 (Sw, ~op_0, sw_out);  // AND_Gate
  and and_4 (Beq, ~op_0, beq_out);  // AND_Gate
  and and_5 (Lui, ~op_0, lui_out);  // AND_Gate
  and and_6 (Sh, ~op_0, sh_out);  // AND_Gate
  and and_7 (j, ~op_0, j_out);  // AND_Gate
  and and_8 (jal, ~op_0, jal_out);  // AND_Gate
  and and_9 (lb, ~op_0, lb_out);  // AND_Gate
  not not_7 (not_7_out, funct[5]);
  not not_8 (not_8_out, funct[4]);
  not not_9 (not_9_out, funct[3]);
  not not_10 (not_10_out, funct[2]);
  not not_11 (not_11_out, funct[1]);
  not not_12 (not_12_out, funct[0]);
  and u_addu (addu_out, funct[5], not_8_out, not_9_out, not_10_out, not_11_out, funct[0]);
  and u_subu (subu_out, funct[5], not_8_out, not_9_out, not_10_out, funct[1], funct[0]);
  and u_nop (nop_out, not_7_out, not_8_out, not_9_out, not_10_out, not_11_out, not_12_out);
  and and_10 (and_10_out, funct[5], not_8_out, not_9_out, funct[2], not_11_out, not_12_out);
  and u_sll (sll_out, not_7_out, not_8_out, not_9_out, not_10_out, not_11_out, not_12_out);
  and and_11 (Addu, op_0, addu_out);
  and and_12 (Subu, op_0, subu_out);
  and and_13 (Nop, op_0, nop_out);
  and and_14 (\and , op_0, and_10_out);
  and and_15 (sll, op_0, sll_out);
endmodule

module \或逻辑  (
  input  Addu,
  input  Subu,
  input  Ori,
  input  Lw,
  input  Sw,
  input  Beq,
  input  Lui,
  input  Nop,
  input  sh,
  input  j,
  input  \and ,
  input  jal,
  input  sll,
  input  lb,
  output [1:0] NPCOp,
  output [1:0] WRSel,
  output [1:0] WDSel,
  output RFWE,
  output [1:0] EXTOp,
  output [1:0] BSel,
  output [4:0] ALUop,
  output DMWE,
  output [1:0] DMtype,
  output [1:0] ASel
);

  wire \判断溢出 ;

  or NPCop1 (NPCOp[1], j, jal);
  buf NPCop0 (NPCOp[0], Beq);  // OR_Gate
  buf WRSel1 (WRSel[1], jal);  // OR_Gate
  or WRSel0 (WRSel[0], Addu, Subu, \and , sll);
  buf WDSel1 (WDSel[1], jal);  // OR_Gate
  or WDSel0 (WDSel[0], Lw, lb);
  or u_RFWE (RFWE, Addu, Subu, Ori, Lw, Lui, \and , jal, sll, lb);
  // OR_Gate EXTOp1 is placed but not wired
  or EXTOp0 (EXTOp[0], Lw, Sw, Beq, sh);
  // OR_Gate BSel1 is placed but not wired
  or BSel0 (BSel[0], Ori, Lw, Sw, Lui, sh, lb);
  // OR_Gate ALUop4 is placed but not wired
  // OR_Gate ALUop3 is placed but not wired
  or ALUop2 (ALUop[2], sll, \and );
  or ALUop1 (ALUop[1], Ori, Lui);
  or ALUop0 (ALUop[0], Subu, Lui, sll);
  or u_DMWE (DMWE, Sw, sh);
  buf DMtype1 (DMtype[1], lb);  // OR_Gate
  buf DMtype0 (DMtype[0], sh);  // OR_Gate
  // OR_Gate judgeovwrflow has open pins: out=\判断溢出 
  // OR_Gate ASel1 is placed but not wired
  buf ASel0 (ASel[0], sll);  // OR_Gate

  assign ALUop[4:3] = 2'b00;
  assign ASel[1] = 1'b0;
  assign BSel[1] = 1'b0;
  assign EXTOp[1] = 1'b0;
endmodule

module RF (
  input  in_1,
  input  in_2,
  input  in_3,
  input  [4:0] in_4,
  input  [4:0] in_5,
  input  [4:0] in_6,
  input  [31:0] in_7,
  output [31:0] out_8,
  output [31:0] RD2
);

  wire [31:0] S0, S1, S2, S3, S4, S5, S6, S7, S8, S9, S10, S11, S12, S13, S14, S15, S16, S17, S18, S19, S20,
       S21, S22, S23, S24, S25, S26, S27, S28, S29, S30, S31, wd0, wd1, wd2, wd3, wd4, wd5, wd6, wd7, wd8,
       wd9, wd10, wd11, wd12, wd13, wd14, wd15, wd16, wd17, wd18, wd19, wd20, wd21, wd22, wd23, wd24, wd25,
       wd26, wd27, wd28, wd29, wd30, wd31;

  Register #(.width(32)) register_1 (.D(wd1), .en(in_3), .Q(S1), .clk(in_1), .clr(in_2));
  Register #(.width(32)) register_2 (.D(wd2), .en(in_3), .Q(S2), .clk(in_1), .clr(in_2));
  Register #(.width(32)) register_3 (.D(wd3), .en(in_3), .Q(S3), .clk(in_1), .clr(in_2));
  Register #(.width(32)) register_4 (.D(wd4), .en(in_3), .Q(S4), .clk(in_1), .clr(in_2));
  // Probe on {32{1'b0}}
  // Probe on S1
  // Probe on S2
  // Probe on S3
  // Probe on S4
  // Probe on S5
  // Probe on S6
  // Probe on S7
  // Probe on S8
  // Probe on S9
  // Probe on S10
  // Probe on S11
  // Probe on S12
  // Probe on S13
  // Probe on S14
  // Probe on S15
  Register #(.width(32)) register_5 (.D(wd5), .en(in_3), .Q(S5), .clk(in_1), .clr(in_2));
  Register #(.width(32)) register_6 (.D(wd6), .en(in_3), .Q(S6), .clk(in_1), .clr(in_2));
  Register #(.width(32)) register_7 (.D(wd7), .en(in_3), .Q(S7), .clk(in_1), .clr(in_2));
  Register #(.width(32)) register_8 (.D(wd8), .en(in_3), .Q(S8), .clk(in_1), .clr(in_2));
  // Probe on S16
  // Probe on S17
  // Probe on S18
  // Probe on S19
  // Probe on S20
  // Probe on S21
  // Probe on S22
  // Probe on S23
  // Probe on S24
  // Probe on S25
  // Probe on S26
  // Probe on S27
  // Probe on S28
  // Probe on S29
  // Probe on S30
  // Probe on S31
  Register #(.width(32)) register_9 (.D(wd9), .en(in_3), .Q(S9), .clk(in_1), .clr(in_2));
  Register #(.width(32)) register_10 (.D(wd10), .en(in_3), .Q(S10), .clk(in_1), .clr(in_2));
  Register #(.width(32)) register_11 (.D(wd11), .en(in_3), .Q(S11), .clk(in_1), .clr(in_2));
  Register #(.width(32)) register_12 (.D(wd12), .en(in_3), .Q(S12), .clk(in_1), .clr(in_2));
  Register #(.width(32)) register_13 (.D(wd13), .en(in_3), .Q(S13), .clk(in_1), .clr(in_2));
  Register #(.width(32)) register_14 (.D(wd14), .en(in_3), .Q(S14), .clk(in_1), .clr(in_2));
  Register #(.width(32)) register_15 (.D(wd15), .en(in_3), .Q(S15), .clk(in_1), .clr(in_2));
  Register #(.width(32)) register_16 (.D(wd16), .en(in_3), .Q(S16), .clk(in_1), .clr(in_2));
  Multiplexer #(.select(5), .width(32)) multiplexer_1 (
    .in0({32{1'b0}}), .in1(S1), .in2(S2), .in3(S3), .in4(S4), .in5(S5), .in6(S6), .in7(S7), .in8(S8),
    .in9(S9), .in10(S10), .in11(S11), .in12(S12), .in13(S13), .in14(S14), .in15(S15), .in16(S16), .in17(S17),
    .in18(S18), .in19(S19), .in20(S20), .in21(S21), .in22(S22), .in23(S23), .in24(S24), .in25(S25),
    .in26(S26), .in27(S27), .in28(S28), .in29(S29), .in30(S30), .in31(S31), .out(out_8), .sel(in_4));  // open: en
  Register #(.width(32)) register_17 (.D(wd17), .en(in_3), .Q(S17), .clk(in_1), .clr(in_2));
  Register #(.width(32)) register_18 (.D(wd18), .en(in_3), .Q(S18), .clk(in_1), .clr(in_2));
  Register #(.width(32)) register_19 (.D(wd19), .en(in_3), .Q(S19), .clk(in_1), .clr(in_2));
  Register #(.width(32)) register_20 (.D(wd20), .en(in_3), .Q(S20), .clk(in_1), .clr(in_2));
  Register #(.width(32)) register_21 (.D(wd21), .en(in_3), .Q(S21), .clk(in_1), .clr(in_2));
  Register #(.width(32)) register_22 (.D(wd22), .en(in_3), .Q(S22), .clk(in_1), .clr(in_2));
  Register #(.width(32)) register_23 (.D(wd23), .en(in_3), .Q(S23), .clk(in_1), .clr(in_2));
  Register #(.width(32)) register_24 (.D(wd24), .en(in_3), .Q(S24), .clk(in_1), .clr(in_2));
  Register #(.width(32)) register_25 (.D(wd25), .en(in_3), .Q(S25), .clk(in_1), .clr(in_2));
  Register #(.width(32)) register_26 (.D(wd26), .en(in_3), .Q(S26), .clk(in_1), .clr(in_2));
  Register #(.width(32)) register_27 (.D(wd27), .en(in_3), .Q(S27), .clk(in_1), .clr(in_2));
  Register #(.width(32)) register_28 (.D(wd28), .en(in_3), .Q(S28), .clk(in_1), .clr(in_2));
  Multiplexer #(.select(5), .width(32)) multiplexer_2 (
    .in0({32{1'b0}}), .in1(S1), .in2(S2), .in3(S3), .in4(S4), .in5(S5), .in6(S6), .in7(S7), .in8(S8),
    .in9(S9), .in10(S10), .in11(S11), .in12(S12), .in13(S13), .in14(S14), .in15(S15), .in16(S16), .in17(S17),
    .in18(S18), .in19(S19), .in20(S20), .in21(S21), .in22(S22), .in23(S23), .in24(S24), .in25(S25),
    .in26(S26), .in27(S27), .in28(S28), .in29(S29), .in30(S30), .in31(S31), .out(RD2), .sel(in_5));  // open: en
  Register #(.width(32)) register_29 (.D(wd29), .en(in_3), .Q(S29), .clk(in_1), .clr(in_2));
  Register #(.width(32)) register_30 (.D(wd30), .en(in_3), .Q(S30), .clk(in_1), .clr(in_2));
  Register #(.width(32)) register_31 (.D(wd31), .en(in_3), .Q(S31), .clk(in_1), .clr(in_2));
  Register #(.width(32)) register_32 (.D(wd0), .en(1'b0), .Q(S0), .clk(in_1), .clr(in_2));
  Demultiplexer #(.select(5), .width(32), .tristate("true")) demultiplexer_1 (
    .out0(wd0), .out1(wd1), .out2(wd2), .out3(wd3), .out4(wd4), .out5(wd5), .out6(wd6), .out7(wd7),
    .out8(wd8), .out9(wd9), .out10(wd10), .out11(wd11), .out12(wd12), .out13(wd13), .out14(wd14),
    .out15(wd15), .out16(wd16), .out17(wd17), .out18(wd18), .out19(wd19), .out20(wd20), .out21(wd21),
    .out22(wd22), .out23(wd23), .out24(wd24), .out25(wd25), .out26(wd26), .out27(wd27), .out28(wd28),
    .out29(wd29), .out30(wd30), .out31(wd31), .in(in_7), .sel(in_6), .en(in_3));

  // Other names for the same wires on the sheet: A1[4:0] = in_4; A2[4:0] = in_5; A3[4:0] = in_6; clk = in_1;
  //   reset = in_2; WD[31:0] = in_7; we = in_3
endmodule

module ALU (
  input  [31:0] A,
  input  [4:0] ALUop,
  input  [31:0] B,
  output Zero,
  output overflow,
  output [31:0] Res
);

  wire [4:0] bit_extender_1_out;
  wire [31:0] A_B, A_B_t, A_B_t_t, A_B_t_t_t, \B逻辑左移16位 , \B逻辑左移A位 ;

  Adder #(.width(32)) adder_1 (.a(A), .b(B), .out(A_B_t));  // open: cin, cout
  Subtractor #(.width(32)) subtractor_1 (.a(A), .b(B), .out(A_B_t_t));  // open: bin, bout
  Shifter #(.width(32)) shifter_1 (.in(B), .\dist (5'b10000), .out(\B逻辑左移16位 ));
  Shifter #(.width(32)) shifter_2 (.in(B), .\dist (bit_extender_1_out), .out(\B逻辑左移A位 ));
  Bit_Extender #(.in_width(32), .out_width(5)) bit_extender_1 (.in(A), .out(bit_extender_1_out));
  Comparator #(.width(32)) comparator_1 (.a(A_B_t_t), .b({32{1'b0}}), .eq(Zero));  // open: gt, lt
  assign A_B_t_t_t = A | B;  // OR_Gate or_1, 32 bits wide
  assign A_B = A & B;  // AND_Gate and_1, 32 bits wide
  Overflow overflow_1 (.opa(A), .opb(B), .res(Res), .overflow(overflow));
  Multiplexer #(.select(5), .width(32)) multiplexer_1 (
    .in0(A_B_t), .in1(A_B_t_t), .in2(A_B_t_t_t), .in3(\B逻辑左移16位 ), .in4(A_B), .in5(\B逻辑左移A位 ), .out(Res),
    .sel(ALUop));  // open: in6, in7, in8, in9, in10, in11, in12, in13, in14, in15, in16, in17, in18, in19, in20, in21, in22, in23, in24, in25, in26, in27, in28, in29, in30, in31, en
endmodule

// overflow
module Overflow (
  input  [31:0] opa,
  input  [31:0] opb,
  input  [31:0] res,
  output overflow
);

  wire and_1_out, and_2_out, not_1_out, not_2_out, not_3_out;

  not not_1 (not_1_out, opa[31]);
  not not_2 (not_2_out, opb[31]);
  not not_3 (not_3_out, res[31]);
  and and_1 (and_1_out, not_1_out, not_2_out, res[31]);
  and and_2 (and_2_out, opa[31], opb[31], not_3_out);
  or or_1 (overflow, and_1_out, and_2_out);
endmodule

module EXT (
  input  [1:0] EXTOp,
  input  [15:0] Imm_Offset,
  output [31:0] Out
);

  wire [31:0] bit_extender_1_out, bit_extender_2_out;

  assign bit_extender_1_out = {{16{1'b0}}, Imm_Offset};  // Bit_Extender bit_extender_1
  assign bit_extender_2_out = {{16{Imm_Offset[15]}}, Imm_Offset};  // Bit_Extender bit_extender_2
  Multiplexer #(.select(2), .width(32)) multiplexer_1 (
    .in0(bit_extender_1_out), .in1(bit_extender_2_out), .out(Out), .sel(EXTOp));  // open: in2, in3, en
endmodule

module DM (
  input  [31:0] WD,
  input  [1:0] DMtype,
  input  Clk,
  input  Reset,
  input  DMWE,
  input  [31:0] Address,
  output [31:0] NRD
);

  wire [23:0] bit_extender_1_out;
  wire [31:0] bit_extender_2_out, bit_extender_3_out, bit_extender_4_out, bit_extender_5_out,
       bit_extender_6_out, bit_extender_7_out, multiplexer_1_out, multiplexer_2_out, multiplexer_3_out, NWD8,
       NWD16, RD, shifter_1_out;

  change8 change8 (.RD(RD), .WD(WD), .in_1(Address[1:0]), .NWD8(NWD8));
  change16 change16 (.RD(RD), .WD(WD), .in_1(Address[1]), .NWD16(NWD16));
  Shifter #(.width(32), .shift("lr")) shifter_1 (.in(Address), .\dist (5'b00010), .out(shifter_1_out));
  Multiplexer #(.select(2), .width(32)) multiplexer_1 (
    .in0(WD), .in1(NWD16), .in2(NWD8), .out(multiplexer_1_out), .sel(DMtype));  // open: in3, en
  Bit_Extender #(.in_width(32), .out_width(24)) bit_extender_1 (.in(shifter_1_out), .out(bit_extender_1_out));
  RAM #(.addrWidth(24), .dataWidth(32), .bus("separate")) ram_1 (
    .addr(bit_extender_1_out), .din(multiplexer_1_out), .data(RD), .str(DMWE), .clk(Clk), .clr(Reset));  // open: sel, ld
  assign bit_extender_2_out = {{16{RD[15]}}, RD[15:0]};  // Bit_Extender bit_extender_2
  assign bit_extender_3_out = {{16{RD[31]}}, RD[31:16]};  // Bit_Extender bit_extender_3
  assign bit_extender_4_out = {{24{RD[7]}}, RD[7:0]};  // Bit_Extender bit_extender_4
  assign bit_extender_5_out = {{24{RD[15]}}, RD[15:8]};  // Bit_Extender bit_extender_5
  assign bit_extender_6_out = {{24{RD[23]}}, RD[23:16]};  // Bit_Extender bit_extender_6
  assign bit_extender_7_out = {{24{RD[31]}}, RD[31:24]};  // Bit_Extender bit_extender_7
  Multiplexer #(.select(2), .width(32)) multiplexer_2 (
    .in0(bit_extender_4_out), .in1(bit_extender_5_out), .in2(bit_extender_6_out), .in3(bit_extender_7_out),
    .out(multiplexer_2_out), .sel(Address[1:0]));  // open: en
  Multiplexer #(.width(32)) multiplexer_3 (
    .in0(bit_extender_2_out), .in1(bit_extender_3_out), .out(multiplexer_3_out), .sel(Address[1]));  // open: en
  Multiplexer #(.select(2), .width(32)) multiplexer_4 (
    .in0(RD), .in1(multiplexer_3_out), .in2(multiplexer_2_out), .out(NRD), .sel(DMtype));  // open: in3, en

  // Other names for the same wires on the sheet: change8[1:0] = Address[1:0]; change16 = Address[1]
endmodule

module change8 (
  input  [1:0] in_1,
  input  [31:0] RD,
  input  [31:0] WD,
  output [31:0] NWD8
);

  Multiplexer #(.select(2), .width(32)) multiplexer_1 (
    .in0({RD[31:8], WD[7:0]}), .in1({RD[31:16], WD[7:0], RD[7:0]}), .in2({RD[31:24], WD[7:0], RD[15:0]}),
    .in3({WD[7:0], RD[23:0]}), .out(NWD8), .sel(in_1));  // open: en

  // Other names for the same wires on the sheet: RD3[7:0] = RD[31:24]; RD0[7:0] = RD[7:0]; RD1[7:0] = RD[15:8];
  //   RD2[7:0] = RD[23:16]; WD_t[7:0] = WD[7:0]
endmodule

module change16 (
  input  in_1,
  input  [31:0] RD,
  input  [31:0] WD,
  output [31:0] NWD16
);

  Multiplexer #(.width(32)) multiplexer_1 (
    .in0({RD[31:16], WD[15:0]}), .in1({WD[15:0], RD[15:0]}), .out(NWD16), .sel(in_1));  // open: en
endmodule

module \初始地址为3000的PC  (
  input  Clk,
  input  Reset,
  input  [31:0] Addressin,
  output [31:0] Addressout
);

  wire comparator_1_eq;
  wire [31:0] adder_1_out, register_1_q;

  Register #(.width(32)) register_1 (.D(Addressin), .Q(register_1_q), .clk(Clk), .clr(Reset));  // open: en
  Comparator #(.width(32)) comparator_1 (.a({32{1'b0}}), .b(register_1_q), .eq(comparator_1_eq));  // open: gt, lt
  Adder #(.width(32)) adder_1 (.a(register_1_q), .b(32'h3000), .out(adder_1_out));  // open: cin, cout
  // Probe on Addressout
  Multiplexer #(.width(32)) multiplexer_1 (
    .in0(register_1_q), .in1(adder_1_out), .out(Addressout), .sel(comparator_1_eq));  // open: en
endmodule

module \DM第一版  (
  input  Clk,
  input  Reset,
  input  DMWE,
  input  [31:0] Address,
  input  [31:0] WD,
  output [31:0] RD
);

  wire [23:0] bit_extender_1_out;
  wire [31:0] shifter_1_out;

  Shifter #(.width(32), .shift("lr")) shifter_1 (.in(Address), .\dist (5'b00010), .out(shifter_1_out));
  Bit_Extender #(.in_width(32), .out_width(24)) bit_extender_1 (.in(shifter_1_out), .out(bit_extender_1_out));
  RAM #(.addrWidth(24), .dataWidth(32), .bus("separate")) ram_1 (
    .addr(bit_extender_1_out), .din(WD), .data(RD), .str(DMWE), .clk(Clk), .clr(Reset));  // open: sel, ld
endmodule
