// Logisim project CPU1testmips1.circ as structural Verilog: 11 circuits, main circuit PC
module main (
  input  in_1,
  output [31:0] out_2,
  output out_3,
  output [4:0] out_4,
  output [31:0] out_5,
  output out_6,
  output [4:0] out_7,
  output [31:0] out_8
);

  wire Br, BSel, Clk, EXTOp, WDSel, WRSel, Zero;
  wire [1:0] ALUOp;
  wire [26:0] alu_1_c;
  wire [31:0] dm_1_rd, ext_1_ext, grf_1_rd1, multiplexer_3_out, npc_1_npc, pc_2_do;

  Clock clock_1 (.out(Clk));
  NPC npc_1 (.Br(Br), .Zero(Zero), .PC(pc_2_do), .imm(out_2[15:0]), .NPC(npc_1_npc));
  // Probe on out_4
  // Probe on out_7
  // Probe on pc_2_do
  PC pc_2 (.init(32'h3000), .DO(pc_2_do), .DI(npc_1_npc), .Clk(Clk), .Reset(in_1));
  // Probe on out_2
  // Probe on out_5
  // Probe on out_8
  IM im_1 (.Addr(pc_2_do), .Inst(out_2));
  Controller controller_1 (
    .opcode(out_2[31:26]), .funct(out_2[5:0]), .out_3(Br), .out_4(out_3), .out_5(EXTOp), .out_9(ALUOp),
    .out_6(out_6), .out_7(BSel), .out_10(WDSel), .out_8(WRSel));
  // Probe on out_2[25:21]
  EXT ext_1 (.EXTOp(EXTOp), .imm(out_2[15:0]), .ext(ext_1_ext));
  Multiplexer #(.width(5), .enable("false")) multiplexer_1 (
    .in0(out_2[20:16]), .in1(out_2[15:11]), .out(out_4), .sel(WRSel));
  Multiplexer #(.width(32), .enable("false")) multiplexer_2 (
    .in0({alu_1_c[26:2], out_7, alu_1_c[1:0]}), .in1(dm_1_rd), .out(out_5), .sel(WDSel));
  GRF grf_1 (
    .in_1(Clk), .in_2(out_2[25:21]), .in_3(in_1), .in_4(out_2[20:16]), .in_5(out_3), .in_6(out_4),
    .in_7(out_5), .RD1(grf_1_rd1), .RD2(out_8));
  Multiplexer #(.width(32), .enable("false")) multiplexer_3 (
    .in0(out_8), .in1(ext_1_ext), .out(multiplexer_3_out), .sel(BSel));
  ALU alu_1 (
    .ALUOp(ALUOp), .A(grf_1_rd1), .B(multiplexer_3_out), .Zero(Zero), .C({alu_1_c[26:2], out_7, alu_1_c[1:0]}));
  DM dm_1 (.Addr({alu_1_c[26:2], out_7, alu_1_c[1:0]}), .WE(out_6), .Clk(Clk), .WD(out_8), .Reset(in_1), .RD(dm_1_rd));

  // Other names for the same wires on the sheet: MemAddr[4:0] = out_7; imm16[15:0] = out_2[15:0];
  //   imm26[25:0] = out_2[25:0]; Instr[31:0] = out_2; rd[4:0] = out_2[15:11]; rt[4:0] = out_2[20:16];
  //   rs[4:0] = out_2[25:21]; MemData[31:0] = out_8; DMWr = out_6; MemWrite = out_6; RegAddr[4:0] = out_4;
  //   RegData[31:0] = out_5; GRFWr = out_3; RegWrite = out_3; Reset = in_1
endmodule

module PC (
  input  [31:0] init,
  input  [31:0] DI,
  input  Clk,
  input  Reset,
  output [31:0] DO
);

  wire counter_1_carry;
  wire [31:0] PC_q;

  Register #(.width(32)) PC (.D(DI), .Q(PC_q), .clk(Clk), .clr(Reset));  // open: en
  Pull_Resistor pull_resistor_1 (.node(init));
  Counter #(.width(1), .max('h1), .ongoal("stay")) counter_1 (
    .carry(counter_1_carry), .clk(Clk), .clr(Reset));  // open: load, D, count, Q
  Multiplexer #(.width(32), .enable("false")) multiplexer_1 (.in0(init), .in1(PC_q), .out(DO), .sel(counter_1_carry));
endmodule

module NPC (
  input  Br,
  input  Zero,
  input  [31:0] PC,
  input  [15:0] imm,
  output [31:0] NPC
);

  wire and_1_out;
  wire [31:0] adder_1_out, adder_2_out, bit_extender_1_out, shifter_1_out;

  and and_1 (and_1_out, Br, Zero);
  assign bit_extender_1_out = {{16{imm[15]}}, imm};  // Bit_Extender bit_extender_1
  Adder #(.width(32)) adder_1 (.a(32'h4), .b(PC), .out(adder_1_out));  // open: cin, cout
  Shifter #(.width(32)) shifter_1 (.in(bit_extender_1_out), .\dist (5'b00010), .out(shifter_1_out));
  Adder #(.width(32)) adder_2 (.a(adder_1_out), .b(shifter_1_out), .out(adder_2_out));  // open: cin, cout
  Multiplexer #(.width(32), .enable("false")) multiplexer_1 (
    .in0(adder_1_out), .in1(adder_2_out), .out(NPC), .sel(and_1_out));
endmodule

module IM (
  input  [31:0] Addr,
  output [31:0] Inst
);

  wire [31:0] subtractor_1_out;

  Subtractor #(.width(32)) subtractor_1 (.a(Addr), .b(32'h3000), .out(subtractor_1_out));  // open: bin, bout
  ROM #(.addrWidth(24), .dataWidth(32)) rom_1 (.addr(subtractor_1_out[25:2]), .data(Inst));  // open: sel

  // Notes on the sheet:
  //   contents of rom_1 (hex, n*v repeats v):
  //   34010043 3412001b 340d002a 340f0068 34140015 34190074 34150010 3407001c 8dee017c 1370004e 00000000
  //   362be0e2 3c0088ba 34f64755 02e08823 00b9d023 00d4b823 3c033267 8e4e01d5 8df0ffc8 3c171c95 3c1a3524
  //   1293000d 02982823 af320068 8c2001a9 0080b023 00000000 13390002 8f200134 027b4821 8c2000f1 03710023
  //   00e71023 34a0e15c 3629d5cd 120b0029 ac200089 00115821 aeaa0060 1276001d 00000000 11550031 8e8a013b
  //   8f23fff0 8e80ffef 00753021 02b77021 3c102921 01c93021 ae59ffe9 00000000 02d9c023 00000000 8c3b0085
  //   3c1acdeb 000fd823 acf10194 12d80015 01d38023 00000000 adbb011e adb2ffda ae80fff3 001a7023 35736570
  //   00000000 00000000 3c175376 0309c021 0150b023 00b91821 12950029 8e9000c7 8da5fffe aea7001c 3540a712
  //   3c0e9e6d aeb90138 36569a4d 13750008 10d50028 00000000 02f96023 8da60116 0173d821 02c08821 02a38823
  //   3c068dd3 8c310149 02347023 10800017 00c6b821 3c0e5547 10590007 af240070 aeb80120 024e8021 00000000
  //   00000000 3c118c05 00a2b823 adb60176 01b33021 00000000 8c2b0035 adf90088 12b4000f 36201fc6 00000000
  //   8ce20114 13580005 3409553c 00a0b821 00000000 8cf60034 ae97017f adfbffe0 009a0023 024d2821 37601cc9
  //   8e9601d3 3c1114e3 00ce7023 ac30009d 02fb8021 367bfbd4 00000000
endmodule

module GRF (
  input  in_1,
  input  [4:0] in_2,
  input  in_3,
  input  [4:0] in_4,
  input  in_5,
  input  [4:0] in_6,
  input  [31:0] in_7,
  output [31:0] RD1,
  output [31:0] RD2
);

  wire [31:0] d0, d1, d2, d3, d4, d5, d6, d7, d8, d9, d10, d11, d12, d13, d14, d15, d16, d17, d18, d19, d20,
       d21, d22, d23, d24, d25, d26, d27, d28, d29, d30, d31, q0, q1, q2, q3, q4, q5, q6, q7, q8, q9, q10,
       q11, q12, q13, q14, q15, q16, q17, q18, q19, q20, q21, q22, q23, q24, q25, q26, q27, q28, q29, q30,
       q31;

  Multiplexer #(.select(5), .width(32)) multiplexer_1 (
    .in0(q0), .in1(q1), .in2(q2), .in3(q3), .in4(q4), .in5(q5), .in6(q6), .in7(q7), .in8(q8), .in9(q9),
    .in10(q10), .in11(q11), .in12(q12), .in13(q13), .in14(q14), .in15(q15), .in16(q16), .in17(q17),
    .in18(q18), .in19(q19), .in20(q20), .in21(q21), .in22(q22), .in23(q23), .in24(q24), .in25(q25),
    .in26(q26), .in27(q27), .in28(q28), .in29(q29), .in30(q30), .in31(q31), .out(RD1), .sel(in_2));  // open: en
  Multiplexer #(.select(5), .width(32)) multiplexer_2 (
    .in0(q0), .in1(q1), .in2(q2), .in3(q3), .in4(q4), .in5(q5), .in6(q6), .in7(q7), .in8(q8), .in9(q9),
    .in10(q10), .in11(q11), .in12(q12), .in13(q13), .in14(q14), .in15(q15), .in16(q16), .in17(q17),
    .in18(q18), .in19(q19), .in20(q20), .in21(q21), .in22(q22), .in23(q23), .in24(q24), .in25(q25),
    .in26(q26), .in27(q27), .in28(q28), .in29(q29), .in30(q30), .in31(q31), .out(RD2), .sel(in_4));  // open: en
  Demultiplexer #(.select(5), .width(32), .tristate("true")) demultiplexer_1 (
    .out0(d0), .out1(d1), .out2(d2), .out3(d3), .out4(d4), .out5(d5), .out6(d6), .out7(d7), .out8(d8),
    .out9(d9), .out10(d10), .out11(d11), .out12(d12), .out13(d13), .out14(d14), .out15(d15), .out16(d16),
    .out17(d17), .out18(d18), .out19(d19), .out20(d20), .out21(d21), .out22(d22), .out23(d23), .out24(d24),
    .out25(d25), .out26(d26), .out27(d27), .out28(d28), .out29(d29), .out30(d30), .out31(d31), .in(in_7),
    .sel(in_6), .en(in_5));
  Register #(.width(32)) _0 (.D(d0), .en(in_5), .Q(q0), .clk(in_1), .clr(1'b1));
  Register #(.width(32)) _4 (.D(d4), .en(in_5), .Q(q4), .clk(in_1), .clr(in_3));
  Register #(.width(32)) _8 (.D(d8), .en(in_5), .Q(q8), .clk(in_1), .clr(in_3));
  Register #(.width(32)) _12 (.D(d12), .en(in_5), .Q(q12), .clk(in_1), .clr(in_3));
  Register #(.width(32)) _16 (.D(d16), .en(in_5), .Q(q16), .clk(in_1), .clr(in_3));
  Register #(.width(32)) _20 (.D(d20), .en(in_5), .Q(q20), .clk(in_1), .clr(in_3));
  Register #(.width(32)) _24 (.D(d24), .en(in_5), .Q(q24), .clk(in_1), .clr(in_3));
  Register #(.width(32)) _28 (.D(d28), .en(in_5), .Q(q28), .clk(in_1), .clr(in_3));
  Register #(.width(32)) _1 (.D(d1), .en(in_5), .Q(q1), .clk(in_1), .clr(in_3));
  Register #(.width(32)) _5 (.D(d5), .en(in_5), .Q(q5), .clk(in_1), .clr(in_3));
  Register #(.width(32)) _9 (.D(d9), .en(in_5), .Q(q9), .clk(in_1), .clr(in_3));
  Register #(.width(32)) _13 (.D(d13), .en(in_5), .Q(q13), .clk(in_1), .clr(in_3));
  Register #(.width(32)) _17 (.D(d17), .en(in_5), .Q(q17), .clk(in_1), .clr(in_3));
  Register #(.width(32)) _21 (.D(d21), .en(in_5), .Q(q21), .clk(in_1), .clr(in_3));
  Register #(.width(32)) _25 (.D(d25), .en(in_5), .Q(q25), .clk(in_1), .clr(in_3));
  Register #(.width(32)) _29 (.D(d29), .en(in_5), .Q(q29), .clk(in_1), .clr(in_3));
  Register #(.width(32)) _2 (.D(d2), .en(in_5), .Q(q2), .clk(in_1), .clr(in_3));
  Register #(.width(32)) _6 (.D(d6), .en(in_5), .Q(q6), .clk(in_1), .clr(in_3));
  Register #(.width(32)) _10 (.D(d10), .en(in_5), .Q(q10), .clk(in_1), .clr(in_3));
  Register #(.width(32)) _14 (.D(d14), .en(in_5), .Q(q14), .clk(in_1), .clr(in_3));
  Register #(.width(32)) _18 (.D(d18), .en(in_5), .Q(q18), .clk(in_1), .clr(in_3));
  Register #(.width(32)) _22 (.D(d22), .en(in_5), .Q(q22), .clk(in_1), .clr(in_3));
  Register #(.width(32)) _26 (.D(d26), .en(in_5), .Q(q26), .clk(in_1), .clr(in_3));
  Register #(.width(32)) _30 (.D(d30), .en(in_5), .Q(q30), .clk(in_1), .clr(in_3));
  Register #(.width(32)) _3 (.D(d3), .en(in_5), .Q(q3), .clk(in_1), .clr(in_3));
  Register #(.width(32)) _7 (.D(d7), .en(in_5), .Q(q7), .clk(in_1), .clr(in_3));
  Register #(.width(32)) _11 (.D(d11), .en(in_5), .Q(q11), .clk(in_1), .clr(in_3));
  Register #(.width(32)) _15 (.D(d15), .en(in_5), .Q(q15), .clk(in_1), .clr(in_3));
  Register #(.width(32)) _19 (.D(d19), .en(in_5), .Q(q19), .clk(in_1), .clr(in_3));
  Register #(.width(32)) _23 (.D(d23), .en(in_5), .Q(q23), .clk(in_1), .clr(in_3));
  Register #(.width(32)) _27 (.D(d27), .en(in_5), .Q(q27), .clk(in_1), .clr(in_3));
  Register #(.width(32)) _31 (.D(d31), .en(in_5), .Q(q31), .clk(in_1), .clr(in_3));

  // Other names for the same wires on the sheet: A1[4:0] = in_2; A2[4:0] = in_4; A3[4:0] = in_6; clk = in_1;
  //   reset = in_3; WD[31:0] = in_7; WE = in_5
endmodule

module ALU (
  input  [1:0] ALUOp,
  input  [31:0] A,
  input  [31:0] B,
  output Zero,
  output [31:0] C
);

  wire alu_sel_1_cin, alu_sel_1_m1sel, or_2_out;
  wire [2:0] alu_sel_1_m2sel0;
  wire [31:0] adder_1_out, multiplexer_1_out, not_1_out, or_1_out, shifter_1_out;

  ALU_Sel alu_sel_1 (
    .ALUOp1(ALUOp[1]), .M1Sel(alu_sel_1_m1sel), .ALUOp0(ALUOp[0]), .Cin(alu_sel_1_cin),
    .M2Sel2(alu_sel_1_m2sel0[2]), .M2Sel1(alu_sel_1_m2sel0[1]), .M2Sel0(alu_sel_1_m2sel0[0]));
  assign not_1_out = ~B;  // NOT_Gate not_1, 32 bits wide
  Multiplexer #(.width(32), .enable("false")) multiplexer_1 (
    .in0(B), .in1(not_1_out), .out(multiplexer_1_out), .sel(alu_sel_1_m1sel));
  assign or_1_out = B | A;  // OR_Gate or_1, 32 bits wide
  Shifter #(.width(32)) shifter_1 (.in(B), .\dist (5'b10000), .out(shifter_1_out));
  Adder #(.width(32)) adder_1 (.a(A), .b(multiplexer_1_out), .out(adder_1_out), .cin(alu_sel_1_cin));  // open: cout
  Multiplexer #(.select(3), .width(32), .enable("false")) multiplexer_2 (
    .in0(adder_1_out), .in1(or_1_out), .in2(shifter_1_out), .out(C), .sel(alu_sel_1_m2sel0));  // open: in3, in4, in5, in6, in7
  not not_2 (Zero, or_2_out);
  or or_2 (or_2_out, adder_1_out[0], adder_1_out[1], adder_1_out[2], adder_1_out[3], adder_1_out[4], adder_1_out[5], adder_1_out[6], adder_1_out[7], adder_1_out[8], adder_1_out[9], adder_1_out[10], adder_1_out[11], adder_1_out[12], adder_1_out[13], adder_1_out[14], adder_1_out[15], adder_1_out[17], adder_1_out[18], adder_1_out[19], adder_1_out[20], adder_1_out[21], adder_1_out[22], adder_1_out[23], adder_1_out[24], adder_1_out[25], adder_1_out[26], adder_1_out[27], adder_1_out[28], adder_1_out[29], adder_1_out[30], adder_1_out[31], adder_1_out[16]);
endmodule

module ALU_Sel (
  input  ALUOp1,
  input  ALUOp0,
  output M1Sel,
  output Cin,
  output M2Sel2,
  output M2Sel1,
  output M2Sel0
);

  wire not_1_out;

  or or_1 (M1Sel, ALUOp0, ALUOp1);
  or or_2 (Cin, ALUOp0, ALUOp1);
  and and_1 (M2Sel1, ALUOp1, ALUOp0);
  not not_1 (not_1_out, ALUOp0);
  and and_2 (M2Sel0, ALUOp1, not_1_out);

  assign M2Sel2 = 1'b0;
endmodule

module DM (
  input  [31:0] Addr,
  input  WE,
  input  Clk,
  input  [31:0] WD,
  input  Reset,
  output [31:0] RD
);

  RAM #(.addrWidth(24), .dataWidth(32), .bus("separate")) ram_1 (
    .addr(Addr[25:2]), .din(WD), .data(RD), .str(WE), .clk(Clk), .clr(Reset));  // open: sel, ld
endmodule

module EXT (
  input  EXTOp,
  input  [15:0] imm,
  output [31:0] ext
);

  wire [31:0] bit_extender_1_out, bit_extender_2_out;

  assign bit_extender_1_out = {{16{1'b0}}, imm};  // Bit_Extender bit_extender_1
  assign bit_extender_2_out = {{16{imm[15]}}, imm};  // Bit_Extender bit_extender_2
  Multiplexer #(.width(32), .enable("false")) multiplexer_1 (
    .in0(bit_extender_1_out), .in1(bit_extender_2_out), .out(ext), .sel(EXTOp));
endmodule

module Controller (
  input  [5:0] opcode,
  input  [5:0] funct,
  output out_3,
  output out_4,
  output out_5,
  output out_6,
  output out_7,
  output out_8,
  output [1:0] out_9,
  output out_10
);

  wire addu_out, ALUOp00_out, ALUOp01_out, beq_out, lui_out, lw_out, not_1_out, not_2_out, not_3_out,
       not_4_out, not_5_out, not_6_out, not_7_out, not_8_out, not_9_out, not_10_out, not_11_out, not_12_out,
       op_0, ori_out, subu_out, sw_out;

  Comparator #(.width(6), .mode("unsigned")) comparator_1 (.a(opcode), .b({6{1'b0}}), .eq(op_0));  // open: gt, lt
  not not_1 (not_1_out, opcode[4]);
  not not_2 (not_2_out, opcode[5]);
  not not_3 (not_3_out, opcode[2]);
  not not_4 (not_4_out, opcode[3]);
  not not_5 (not_5_out, opcode[0]);
  not not_6 (not_6_out, opcode[1]);
  and ori (ori_out, not_2_out, not_1_out, opcode[3], opcode[2], not_6_out, opcode[0]);
  and lw (lw_out, opcode[5], not_1_out, not_4_out, not_3_out, opcode[1], opcode[0]);
  and sw (sw_out, opcode[5], not_1_out, opcode[3], not_3_out, opcode[1], opcode[0]);
  and beq (beq_out, not_2_out, not_1_out, not_4_out, opcode[2], not_6_out, not_5_out);
  and lui (lui_out, not_2_out, not_1_out, opcode[3], opcode[2], opcode[1], opcode[0]);
  buf Br (out_3, beq_out);  // OR_Gate
  or GRFWr (out_4, addu_out, subu_out, ori_out, lw_out, lui_out);
  or EXTOp (out_5, lw_out, beq_out, sw_out);
  or ALUOp00 (ALUOp00_out, addu_out, lw_out, sw_out);
  Controller_ALUOp controller_aluop_1 (
    .a00(ALUOp00_out), .a01(ALUOp01_out), .a10(ori_out), .a11(lui_out), .ALUOp1(out_9[1]), .ALUOp0(out_9[0]));
  or ALUOp01 (ALUOp01_out, subu_out, beq_out);
  buf DMWr (out_6, sw_out);  // OR_Gate
  or BSel (out_7, ori_out, lw_out, sw_out, lui_out);
  buf WDSel (out_10, lw_out);  // OR_Gate
  or WRSel (out_8, addu_out, subu_out, beq_out);
  and addu (addu_out, funct[5], not_9_out, not_8_out, op_0, not_10_out, not_11_out, funct[0]);
  and subu (subu_out, funct[5], not_9_out, not_8_out, op_0, not_10_out, funct[1], funct[0]);
  not not_7 (not_7_out, funct[5]);
  not not_8 (not_8_out, funct[3]);
  not not_9 (not_9_out, funct[4]);
  not not_10 (not_10_out, funct[2]);
  not not_11 (not_11_out, funct[1]);
  not not_12 (not_12_out, funct[0]);

  // Notes on the sheet:
  //   beq
  //   lui
  //   addu
  //   subu
  //   ori
  //   lw
  //   sw
endmodule

module Controller_ALUOp (
  input  a00,
  input  a01,
  input  a10,
  input  a11,
  output ALUOp1,
  output ALUOp0
);

  wire not_1_out, not_2_out, not_3_out, not_4_out;

  not not_1 (not_1_out, a00);
  and and_1 (ALUOp1, not_1_out, not_2_out);
  not not_2 (not_2_out, a01);
  not not_3 (not_3_out, a00);
  and and_2 (ALUOp0, not_3_out, not_4_out);
  not not_4 (not_4_out, a10);
endmodule
