// Logisim project main - 副本.circ as structural Verilog: 26 circuits, main circuit main
module main (
  input  in_1,
  output [31:0] out_2,
  output out_3,
  output [4:0] out_4,
  output [31:0] out_5,
  output out_6,
  output [4:0] out_7,
  output [31:0] out_8
);

  wire clock_1_out;
  wire [2:0] centrol_processing_unit_1_out_8;
  wire [31:0] centrol_processing_unit_1_out_11, data_memory_1_out_7, instruction_memory_1_out_2;

  Clock clock_1 (.out(clock_1_out));
  instruction_memory instruction_memory_1 (.in_1(out_2), .out_2(instruction_memory_1_out_2));
  centrol_processing_unit centrol_processing_unit_1 (
    .in_2(clock_1_out), .in_3(instruction_memory_1_out_2), .out_10(out_2), .in_4(data_memory_1_out_7),
    .out_6(out_6), .out_8(centrol_processing_unit_1_out_8),
    .out_11({centrol_processing_unit_1_out_11[31:7], out_7, centrol_processing_unit_1_out_11[1:0]}),
    .out_12(out_8), .in_1(in_1), .out_5(out_3), .out_7(out_4), .out_13(out_5));  // open: out_9
  data_memory data_memory_1 (
    .in_5({centrol_processing_unit_1_out_11[31:7], out_7, centrol_processing_unit_1_out_11[1:0]}),
    .in_6(out_8), .out_7(data_memory_1_out_7), .in_1(centrol_processing_unit_1_out_8), .in_2(clock_1_out),
    .in_3(out_6), .in_4(in_1));
endmodule

module alu_select (
  input  [1:0] in_1,
  input  [31:0] in_2,
  input  [31:0] in_3,
  input  [31:0] in_4,
  output [31:0] out_5,
  output [31:0] out_6
);

  Multiplexer #(.width(32), .enable("false")) multiplexer_1 (.in0(in_2), .in1(in_4), .out(out_5), .sel(in_1[1]));
  Multiplexer #(.width(32), .enable("false")) multiplexer_2 (.in0(in_3), .in1(in_4), .out(out_6), .sel(in_1[0]));
endmodule

module arithmetic_logical_unit (
  input  [4:0] in_1,
  input  [31:0] in_2,
  input  [31:0] in_3,
  output out_4,
  output out_5,
  output [31:0] out_6
);

  wire comparator_1_lt, comparator_2_lt;
  wire [31:0] In0, In1, In2, In3, In4, In5, In6, In7, In8, In9, In10, In11, In12, In13, In14, In15, xor_2_out;

  assign In0 = in_3 & in_2;  // AND_Gate and_1, 32 bits wide
  assign In1 = in_3 | in_2;  // OR_Gate or_1, 32 bits wide
  Adder #(.width(32)) adder_1 (.a(in_3), .b(in_2), .out(In2));  // open: cin, cout
  assign In3 = in_3 ^ in_2;  // XOR_Gate xor_1, 32 bits wide
  Subtractor #(.width(32)) subtractor_1 (.a(in_3), .b(in_2), .out(In6));  // open: bin, bout
  Comparator #(.width(32)) comparator_1 (.a(in_3), .b(in_2), .lt(comparator_1_lt));  // open: gt, eq
  assign In7 = {{31{1'b0}}, comparator_1_lt};  // Bit_Extender bit_extender_1
  Shifter #(.width(32)) shifter_1 (.in(in_2), .\dist (in_3[4:0]), .out(In9));
  Shifter #(.width(32), .shift("lr")) shifter_2 (.in(in_2), .\dist (in_3[4:0]), .out(In10));
  Shifter #(.width(32), .shift("ar")) shifter_3 (.in(in_2), .\dist (in_3[4:0]), .out(In11));
  big_than big_than_1 (.in_1(in_3), .in_2({32{1'b0}}), .out_3(In4));
  small_than small_than_1 (.in_1(in_3), .in_2({32{1'b0}}), .out_3(In5));
  bigeq_than bigeq_than_1 (.in_1(in_3), .in_2({32{1'b0}}), .out_3(In8));
  assign In12 = ~(in_3 | in_2);  // NOR_Gate nor_1, 32 bits wide
  assign xor_2_out = in_3 ^ in_2;  // XOR_Gate xor_2, 32 bits wide
  Comparator #(.width(32), .mode("unsigned")) comparator_2 (.a(in_3), .b(in_2), .lt(comparator_2_lt));  // open: gt, eq
  is_zero is_zero_1 (.in_1(xor_2_out), .out_2(In13));
  assign In14 = {{31{1'b0}}, comparator_2_lt};  // Bit_Extender bit_extender_2
  smalleq_than smalleq_than_1 (.in_1(in_3), .in_2({32{1'b0}}), .out_3(In15));
  Multiplexer #(.select(5), .width(32), .enable("false")) multiplexer_1 (
    .in0(In0), .in1(In1), .in2(In2), .in3(In3), .in4(In4), .in5(In5), .in6(In6), .in7(In7), .in8(In8),
    .in9(In9), .in10(In10), .in11(In11), .in12(In12), .in13(In13), .in14(In14), .in15(In15),
    .in16({in_2[15:0], {16{1'b0}}}), .in17({32{1'b1}}), .in18({32{1'b1}}), .in19({32{1'b1}}),
    .in20({32{1'b1}}), .in21({32{1'b1}}), .in22({32{1'b1}}), .in23({32{1'b1}}), .in24({32{1'b1}}),
    .in25({32{1'b1}}), .in26({32{1'b1}}), .in27({32{1'b1}}), .in28({32{1'b1}}), .in29({32{1'b1}}),
    .in30({32{1'b1}}), .in31({32{1'b1}}), .out(out_6), .sel(in_1));
  overflow overflow_1 (.in_1(in_2), .in_2(in_3), .out_4(out_4), .in_3(out_6));
  nor nor_2 (out_5, out_6[0], out_6[1], out_6[2], out_6[3], out_6[4], out_6[5], out_6[6], out_6[7], out_6[8], out_6[9], out_6[10], out_6[11], out_6[12], out_6[13], out_6[14], out_6[15], out_6[16], out_6[17], out_6[18], out_6[19], out_6[20], out_6[21], out_6[22], out_6[23], out_6[24], out_6[25], out_6[26], out_6[27], out_6[28], out_6[29], out_6[30], out_6[31]);

  // Other names for the same wires on the sheet: In16[31:16] = in_2[15:0]
endmodule

module bit_extender (
  input  [1:0] in_1,
  input  [15:0] in_2,
  output [31:0] out_3
);

  wire [31:0] bit_extender_1_out, bit_extender_2_out, bit_extender_3_out;

  assign bit_extender_1_out = {{16{in_2[15]}}, in_2};  // Bit_Extender bit_extender_1
  assign bit_extender_2_out = {{16{1'b0}}, in_2};  // Bit_Extender bit_extender_2
  assign bit_extender_3_out = {{27{1'b0}}, in_2[10:6]};  // Bit_Extender bit_extender_3
  Multiplexer #(.select(2), .width(32), .enable("false")) multiplexer_1 (
    .in0(bit_extender_1_out), .in1(bit_extender_2_out), .in2(bit_extender_3_out), .in3({32{1'b1}}),
    .out(out_3), .sel(in_1));
endmodule

module centrol_processing_unit (
  input  in_1,
  input  in_2,
  input  [31:0] in_3,
  input  [31:0] in_4,
  output out_5,
  output out_6,
  output [4:0] out_7,
  output [2:0] out_8,
  output out_9,
  output [31:0] out_10,
  output [31:0] out_11,
  output [31:0] out_12,
  output [31:0] out_13
);

  wire _31, and_1_out, arithmetic_logical_unit_1_out_4, arithmetic_logical_unit_1_out_5,
       control_unit_1_out_5, control_unit_1_out_7, control_unit_1_out_9, control_unit_1_out_12,
       control_unit_1_out_16;
  wire [1:0] control_unit_1_out_4, control_unit_1_out_11, control_unit_1_out_15;
  wire [4:0] ADDR, control_unit_1_out_10, line_spliter_1_out_4, line_spliter_1_out_5, line_spliter_1_out_6;
  wire [5:0] line_spliter_1_out_2, line_spliter_1_out_3;
  wire [15:0] line_spliter_1_out_7;
  wire [27:0] line_spliter_1_out_8;
  wire [31:0] adder_1_out, alu_select_1_out_5, alu_select_1_out_6, bit_extender_1_out_3, multiplexer_3_out,
       program_counter_1_out_9, register_file_1_out_9, shifter_1_out;

  program_counter program_counter_1 (
    .in_5(adder_1_out), .in_6(register_file_1_out_9), .out_8(out_10), .out_9(program_counter_1_out_9),
    .in_1(and_1_out), .in_2(control_unit_1_out_4), .in_3(in_2), .in_7(line_spliter_1_out_8), .in_4(in_1));
  line_spliter line_spliter_1 (
    .in_1(in_3), .out_2(line_spliter_1_out_2), .out_3(line_spliter_1_out_3), .out_4(line_spliter_1_out_4),
    .out_5(line_spliter_1_out_5), .out_6(line_spliter_1_out_6), .out_7(line_spliter_1_out_7),
    .out_8(line_spliter_1_out_8));
  Multiplexer #(.width(32), .enable("false")) multiplexer_1 (
    .in0(multiplexer_3_out), .in1(program_counter_1_out_9), .out(out_13), .sel(control_unit_1_out_5));
  control_unit control_unit_1 (
    .out_4(control_unit_1_out_4), .out_5(control_unit_1_out_5), .out_6(_31), .in_1(line_spliter_1_out_2),
    .in_2(line_spliter_1_out_3), .in_3(line_spliter_1_out_5), .out_7(control_unit_1_out_7), .out_8(out_6),
    .out_9(control_unit_1_out_9), .out_10(control_unit_1_out_10), .out_11(control_unit_1_out_11),
    .out_12(control_unit_1_out_12), .out_13(out_5), .out_14(out_8), .out_15(control_unit_1_out_15),
    .out_16(control_unit_1_out_16));
  register_file register_file_1 (
    .in_5(line_spliter_1_out_4), .in_6(line_spliter_1_out_5), .in_7(ADDR), .in_8(out_13),
    .out_9(register_file_1_out_9), .out_10(out_12), .in_1(_31), .in_3(in_2), .in_4(out_5), .in_2(in_1));
  Multiplexer #(.width(5), .enable("false")) multiplexer_2 (
    .in0(line_spliter_1_out_5), .in1(line_spliter_1_out_6), .out(ADDR), .sel(control_unit_1_out_12));
  bit_extender bit_extender_1 (.in_2(line_spliter_1_out_7), .in_1(control_unit_1_out_15), .out_3(bit_extender_1_out_3));
  alu_select alu_select_1 (
    .in_2(register_file_1_out_9), .in_3(out_12), .in_4(bit_extender_1_out_3), .out_5(alu_select_1_out_5),
    .out_6(alu_select_1_out_6), .in_1(control_unit_1_out_11));
  arithmetic_logical_unit arithmetic_logical_unit_1 (
    .in_2(alu_select_1_out_6), .in_3(alu_select_1_out_5), .out_5(arithmetic_logical_unit_1_out_5),
    .out_6(out_11), .in_1(control_unit_1_out_10), .out_4(arithmetic_logical_unit_1_out_4));
  Shifter #(.width(32)) shifter_1 (.in(bit_extender_1_out_3), .\dist (5'b00010), .out(shifter_1_out));
  Adder #(.width(32)) adder_1 (.a(shifter_1_out), .b(program_counter_1_out_9), .out(adder_1_out));  // open: cin, cout
  and and_1 (and_1_out, control_unit_1_out_9, arithmetic_logical_unit_1_out_5);
  Multiplexer #(.width(32), .enable("false")) multiplexer_3 (
    .in0(out_11), .in1(in_4), .out(multiplexer_3_out), .sel(control_unit_1_out_7));
  Multiplexer #(.width(5), .enable("false")) multiplexer_4 (.in0(ADDR), .in1({5{1'b1}}), .out(out_7), .sel(_31));
  and and_2 (out_9, control_unit_1_out_16, arithmetic_logical_unit_1_out_4);

  // Other names for the same wires on the sheet: CLK = in_2; RST = in_1; RW = out_5

  // Notes on the sheet:
  //   MemtoReg
  //   MemWrite
  //   Branch
  //   ALU
  //   ALUSrc
  //   RegDst
  //   RegWrite
  //   HAndD
  //   Extend
endmodule

module control_unit (
  input  [5:0] in_1,
  input  [5:0] in_2,
  input  [4:0] in_3,
  output [1:0] out_4,
  output out_5,
  output out_6,
  output out_7,
  output out_8,
  output out_9,
  output [4:0] out_10,
  output [1:0] out_11,
  output out_12,
  output out_13,
  output [2:0] out_14,
  output [1:0] out_15,
  output out_16
);

  wire select_type_1_out_2, select_type_1_out_3;
  wire [21:0] lower_six_1_out_7, middle_five_1_out_6, multiplexer_1_out, upper_six_1_out_7;

  select_type select_type_1 (.in_1(in_1), .out_2(select_type_1_out_2), .out_3(select_type_1_out_3));
  upper_six upper_six_1 (
    .In0(in_1[5]), .In1(in_1[4]), .In2(in_1[3]), .In3(in_1[2]), .In4(in_1[1]), .In5(in_1[0]),
    .out_7(upper_six_1_out_7));
  lower_six lower_six_1 (
    .In0(in_2[5]), .In1(in_2[4]), .In2(in_2[3]), .In3(in_2[2]), .In4(in_2[1]), .In5(in_2[0]),
    .out_7(lower_six_1_out_7));
  middle_five middle_five_1 (
    .In0(in_3[4]), .In1(in_3[3]), .In2(in_3[2]), .In3(in_3[1]), .In4(in_3[0]), .out_6(middle_five_1_out_6));
  Multiplexer #(.width(22), .enable("false")) multiplexer_1 (
    .in0(upper_six_1_out_7), .in1(lower_six_1_out_7), .out(multiplexer_1_out), .sel(select_type_1_out_2));
  Multiplexer #(.width(22), .enable("false")) multiplexer_2 (
    .in0(multiplexer_1_out), .in1(middle_five_1_out_6),
    .out({out_16, out_6, out_5, out_4[0], out_4[1], out_15[0], out_15[1], out_14[0], out_14[1], out_14[2], out_13, out_12, out_11[0], out_11[1], out_10[0], out_10[1], out_10[2], out_10[3], out_10[4], out_9, out_8, out_7}),
    .sel(select_type_1_out_3));
endmodule

module data_memory (
  input  [2:0] in_1,
  input  in_2,
  input  in_3,
  input  in_4,
  input  [31:0] in_5,
  input  [31:0] in_6,
  output [31:0] out_7
);

  wire [31:0] changer_8_1_out_4, changer_16_1_out_4, extender_8_1_out_3, extender_8_2_out_3,
       extender_8_3_out_3, extender_8_4_out_3, extender_16_1_out_3, extender_16_2_out_3, multiplexer_1_out,
       multiplexer_2_out, multiplexer_3_out, multiplexer_4_out, ram_1_data;

  changer_16 changer_16_1 (.in_2(ram_1_data), .in_3(in_6), .out_4(changer_16_1_out_4), .in_1(in_5[1]));
  changer_8 changer_8_1 (.in_2(ram_1_data), .in_3(in_6), .out_4(changer_8_1_out_4), .in_1(in_5[1:0]));
  RAM #(.addrWidth(24), .dataWidth(32), .bus("separate")) ram_1 (
    .addr(in_5[25:2]), .din(multiplexer_1_out), .data(ram_1_data), .str(in_3), .clk(in_2), .ld(1'b1),
    .clr(in_4));  // open: sel
  Multiplexer #(.select(2), .width(32), .enable("false")) multiplexer_1 (
    .in0(in_6), .in1(changer_16_1_out_4), .in2(changer_8_1_out_4), .in3({32{1'b1}}), .out(multiplexer_1_out),
    .sel(in_1[2:1]));
  extender_16 extender_16_1 (.in_2(ram_1_data[15:0]), .out_3(extender_16_1_out_3), .in_1(in_1[0]));
  extender_16 extender_16_2 (.in_2(ram_1_data[31:16]), .out_3(extender_16_2_out_3), .in_1(in_1[0]));
  extender_8 extender_8_1 (.in_2(ram_1_data[7:0]), .out_3(extender_8_1_out_3), .in_1(in_1[0]));
  extender_8 extender_8_2 (.in_2(ram_1_data[15:8]), .out_3(extender_8_2_out_3), .in_1(in_1[0]));
  extender_8 extender_8_3 (.in_2(ram_1_data[23:16]), .out_3(extender_8_3_out_3), .in_1(in_1[0]));
  extender_8 extender_8_4 (.in_2(ram_1_data[31:24]), .out_3(extender_8_4_out_3), .in_1(in_1[0]));
  Multiplexer #(.width(32), .enable("false")) multiplexer_2 (
    .in0(extender_16_1_out_3), .in1(extender_16_2_out_3), .out(multiplexer_2_out), .sel(in_5[1]));
  Multiplexer #(.select(2), .width(32), .enable("false")) multiplexer_3 (
    .in0(extender_8_1_out_3), .in1(extender_8_2_out_3), .in2(extender_8_3_out_3), .in3(extender_8_4_out_3),
    .out(multiplexer_3_out), .sel(in_5[1:0]));
  Multiplexer #(.select(2), .width(32), .enable("false")) multiplexer_4 (
    .in0(ram_1_data), .in1(multiplexer_2_out), .in2(multiplexer_3_out), .in3({32{1'b1}}),
    .out(multiplexer_4_out), .sel(in_1[2:1]));
  Multiplexer #(.width(32), .enable("false")) multiplexer_5 (
    .in0(multiplexer_4_out), .out(out_7), .sel(in_3));  // open: in1
endmodule

module instruction_memory (
  input  [31:0] in_1,
  output [31:0] out_2
);

  wire [31:0] subtractor_1_out;

  Subtractor #(.width(32)) subtractor_1 (.a(in_1), .b(32'h3000), .out(subtractor_1_out));  // open: bin, bout
  // Probe on subtractor_1_out[25:2]
  ROM #(.addrWidth(24), .dataWidth(32)) rom_1 (.addr(subtractor_1_out[25:2]), .data(out_2));  // open: sel

  // Notes on the sheet:
  //   contents of rom_1 (hex, n*v repeats v):
  //   20215b25 20425b25 20635b25 20845b25 20a55b25 20c65b25 20e75b25 21085b25 21295b25 214a5b25 216b5b25
  //   218c5b25 21ad5b25 21ce5b25 21ef5b25 22105b25 22315b25 22525b25 22735b25 22945b25 22b55b25 22d65b25
  //   22f75b25 23185b25 23395b25 235a5b25 237b5b25 239c5b25 23bd5b25 23de5b25 23ff5b25 20110000 20090000
  //   312a0000 ae2a0000 22310004 20090000 312a0001 ae2a0000 22310004 20090000 3c01ffff 3421ffff 1215024
  //   ae2a0000 22310004 20090000 3c017fff 3421ffff 1215024 ae2a0000 22310004 20090000 3c018000 34210000
  //   1215024 ae2a0000 22310004 20090000 3c010002 34210cb5 1215024 ae2a0000 22310004 20090000 3c01fcdf
  //   3421e5bd 1215024 ae2a0000 22310004 20090001 312a0000 ae2a0000 22310004 20090001 312a0001 ae2a0000
  //   22310004 20090001 3c01ffff 3421ffff 1215024 ae2a0000 22310004 20090001 3c017fff 3421ffff 1215024
  //   ae2a0000 22310004 20090001 3c018000 34210000 1215024 ae2a0000 22310004 20090001 3c010002 34210cb5
  //   1215024 ae2a0000 22310004 20090001 3c01fcdf 3421e5bd 1215024 ae2a0000 22310004 2009ffff 312a0000
  //   ae2a0000 22310004 2009ffff 312a0001 ae2a0000 22310004 2009ffff 3c01ffff 3421ffff 1215024 ae2a0000
  //   22310004 2009ffff 3c017fff 3421ffff 1215024 ae2a0000 22310004 2009ffff 3c018000 34210000 1215024
  //   ae2a0000 22310004 2009ffff 3c010002 34210cb5 1215024 ae2a0000 22310004 2009ffff 3c01fcdf 3421e5bd
  //   1215024 ae2a0000 22310004 3c017fff 3421ffff 14820 312a0000 ae2a0000 22310004 3c017fff 3421ffff 14820
  //   312a0001 ae2a0000 22310004 3c017fff 3421ffff 14820 3c01ffff 3421ffff 1215024 ae2a0000 22310004
  //   3c017fff 3421ffff 14820 3c017fff 3421ffff 1215024 ae2a0000 22310004 3c017fff 3421ffff 14820 3c018000
  //   34210000 1215024 ae2a0000 22310004 3c017fff 3421ffff 14820 3c010002 34210cb5 1215024 ae2a0000
  //   22310004 3c017fff 3421ffff 14820 3c01fcdf 3421e5bd 1215024 ae2a0000 22310004 3c018000 34210000 14820
  //   312a0000 ae2a0000 22310004 3c018000 34210000 14820 312a0001 ae2a0000 22310004 3c018000 34210000
  //   14820 3c01ffff 3421ffff 1215024 ae2a0000 22310004 3c018000 34210000 14820 3c017fff 3421ffff 1215024
  //   ae2a0000 22310004 3c018000 34210000 14820 3c018000 34210000 1215024 ae2a0000 22310004 3c018000
  //   34210000 14820 3c010002 34210cb5 1215024 ae2a0000 22310004 3c018000 34210000 14820 3c01fcdf 3421e5bd
  //   1215024 ae2a0000 22310004 3c010002 34210cb5 14820 312a0000 ae2a0000 22310004 3c010002 34210cb5 14820
  //   312a0001 ae2a0000 22310004 3c010002 34210cb5 14820 3c01ffff 3421ffff 1215024 ae2a0000 22310004
  //   3c010002 34210cb5 14820 3c017fff 3421ffff 1215024 ae2a0000 22310004 3c010002 34210cb5 14820 3c018000
  //   34210000 1215024 ae2a0000 22310004 3c010002 34210cb5 14820 3c010002 34210cb5 1215024 ae2a0000
  //   22310004 3c010002 34210cb5 14820 3c01fcdf 3421e5bd 1215024 ae2a0000 22310004 3c01fcdf 3421e5bd 14820
  //   312a0000 ae2a0000 22310004 3c01fcdf 3421e5bd 14820 312a0001 ae2a0000 22310004 3c01fcdf 3421e5bd
  //   14820 3c01ffff 3421ffff 1215024 ae2a0000 22310004 3c01fcdf 3421e5bd 14820 3c017fff 3421ffff 1215024
  //   ae2a0000 22310004 3c01fcdf 3421e5bd 14820 3c018000 34210000 1215024 ae2a0000 22310004 3c01fcdf
  //   3421e5bd 14820 3c010002 34210cb5 1215024 ae2a0000 22310004 3c01fcdf 3421e5bd 14820 3c01fcdf 3421e5bd
  //   1215024 ae2a0000 22310004 20090000 352a0000 ae2a0000 22310004 20090000 352a0001 ae2a0000 22310004
  //   20090000 3c01ffff 3421ffff 1215025 ae2a0000 22310004 20090000 3c017fff 3421ffff 1215025 ae2a0000
  //   22310004 20090000 3c018000 34210000 1215025 ae2a0000 22310004 20090000 3c010002 34210cb5 1215025
  //   ae2a0000 22310004 20090000 3c01fcdf 3421e5bd 1215025 ae2a0000 22310004 20090001 352a0000 ae2a0000
  //   22310004 20090001 352a0001 ae2a0000 22310004 20090001 3c01ffff 3421ffff 1215025 ae2a0000 22310004
  //   20090001 3c017fff 3421ffff 1215025 ae2a0000 22310004 20090001 3c018000 34210000 1215025 ae2a0000
  //   22310004 20090001 3c010002 34210cb5 1215025 ae2a0000 22310004 20090001 3c01fcdf 3421e5bd 1215025
  //   ae2a0000 22310004 2009ffff 352a0000 ae2a0000 22310004 2009ffff 352a0001 ae2a0000 22310004 2009ffff
  //   3c01ffff 3421ffff 1215025 ae2a0000 22310004 2009ffff 3c017fff 3421ffff 1215025 ae2a0000 22310004
  //   2009ffff 3c018000 34210000 1215025 ae2a0000 22310004 2009ffff 3c010002 34210cb5 1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
endmodule

module line_spliter (
  input  [31:0] in_1,
  output [5:0] out_2,
  output [5:0] out_3,
  output [4:0] out_4,
  output [4:0] out_5,
  output [4:0] out_6,
  output [15:0] out_7,
  output [27:0] out_8
);

  assign out_8 = {{2{1'b0}}, in_1[25:0]};  // Bit_Extender bit_extender_1

  assign out_2 = in_1[31:26];
  assign out_3 = in_1[5:0];
  assign out_4 = in_1[25:21];
  assign out_5 = in_1[20:16];
  assign out_6 = in_1[15:11];
  assign out_7 = in_1[15:0];
endmodule

module program_counter (
  input  in_1,
  input  [1:0] in_2,
  input  in_3,
  input  in_4,
  input  [31:0] in_5,
  input  [31:0] in_6,
  input  [27:0] in_7,
  output [31:0] out_8,
  output [31:0] out_9
);

  wire counter_1_q;
  wire [27:0] shifter_1_out;
  wire [31:0] multiplexer_1_out, multiplexer_2_out, register_1_q;

  Multiplexer #(.width(32), .enable("false")) multiplexer_1 (
    .in0(out_9), .in1(in_5), .out(multiplexer_1_out), .sel(in_1));
  Multiplexer #(.select(2), .width(32), .enable("false")) multiplexer_2 (
    .in0(multiplexer_1_out), .in1({out_9[31:28], shifter_1_out}), .in2(in_6), .in3({32{1'b1}}),
    .out(multiplexer_2_out), .sel(in_2));
  Shifter #(.width(28)) shifter_1 (.in(in_7), .\dist (5'b00010), .out(shifter_1_out));
  Register #(.width(32)) register_1 (.D(multiplexer_2_out), .Q(register_1_q), .clk(in_3), .clr(in_4));  // open: en
  Counter #(.width(1), .max('h1), .ongoal("stay")) counter_1 (
    .Q(counter_1_q), .clk(in_3), .clr(in_4));  // open: load, D, count, carry
  Multiplexer #(.width(32), .enable("false")) multiplexer_3 (
    .in0(32'h3000), .in1(register_1_q), .out(out_8), .sel(counter_1_q));
  Adder #(.width(32)) adder_1 (.a(out_8), .b(32'h4), .out(out_9));  // open: cin, cout
endmodule

module register_file (
  input  in_1,
  input  in_2,
  input  in_3,
  input  in_4,
  input  [4:0] in_5,
  input  [4:0] in_6,
  input  [4:0] in_7,
  input  [31:0] in_8,
  output [31:0] out_9,
  output [31:0] out_10
);

  wire decoder_1_out0, decoder_1_out1, decoder_1_out2, decoder_1_out3, decoder_1_out4, decoder_1_out5,
       decoder_1_out6, decoder_1_out7, decoder_1_out8, decoder_1_out9, decoder_1_out10, decoder_1_out11,
       decoder_1_out12, decoder_1_out13, decoder_1_out14, decoder_1_out15, decoder_1_out16, decoder_1_out17,
       decoder_1_out18, decoder_1_out19, decoder_1_out20, decoder_1_out21, decoder_1_out22, decoder_1_out23,
       decoder_1_out24, decoder_1_out25, decoder_1_out26, decoder_1_out27, decoder_1_out28, decoder_1_out29,
       decoder_1_out30, decoder_1_out31;
  wire [4:0] multiplexer_1_out;
  wire [31:0] n32_reg_1_out_37, n32_reg_1_out_38, n32_reg_1_out_39, n32_reg_1_out_40, n32_reg_1_out_41,
       n32_reg_1_out_42, n32_reg_1_out_43, n32_reg_1_out_44, n32_reg_1_out_45, n32_reg_1_out_46,
       n32_reg_1_out_47, n32_reg_1_out_48, n32_reg_1_out_49, n32_reg_1_out_50, n32_reg_1_out_51,
       n32_reg_1_out_52, n32_reg_1_out_53, n32_reg_1_out_54, n32_reg_1_out_55, n32_reg_1_out_56,
       n32_reg_1_out_57, n32_reg_1_out_58, n32_reg_1_out_59, n32_reg_1_out_60, n32_reg_1_out_61,
       n32_reg_1_out_62, n32_reg_1_out_63, n32_reg_1_out_64, n32_reg_1_out_65, n32_reg_1_out_66,
       n32_reg_1_out_67, n32_reg_1_out_68;

  Multiplexer #(.width(5), .enable("false")) multiplexer_1 (
    .in0(in_7), .in1({5{1'b1}}), .out(multiplexer_1_out), .sel(in_1));
  Decoder #(.select(5), .enable("false")) decoder_1 (
    .out0(decoder_1_out0), .out1(decoder_1_out1), .out2(decoder_1_out2), .out3(decoder_1_out3),
    .out4(decoder_1_out4), .out5(decoder_1_out5), .out6(decoder_1_out6), .out7(decoder_1_out7),
    .out8(decoder_1_out8), .out9(decoder_1_out9), .out10(decoder_1_out10), .out11(decoder_1_out11),
    .out12(decoder_1_out12), .out13(decoder_1_out13), .out14(decoder_1_out14), .out15(decoder_1_out15),
    .out16(decoder_1_out16), .out17(decoder_1_out17), .out18(decoder_1_out18), .out19(decoder_1_out19),
    .out20(decoder_1_out20), .out21(decoder_1_out21), .out22(decoder_1_out22), .out23(decoder_1_out23),
    .out24(decoder_1_out24), .out25(decoder_1_out25), .out26(decoder_1_out26), .out27(decoder_1_out27),
    .out28(decoder_1_out28), .out29(decoder_1_out29), .out30(decoder_1_out30), .out31(decoder_1_out31),
    .sel(multiplexer_1_out));
  _32_reg u_32_reg_1 (
    .in_1(decoder_1_out0), .in_2(decoder_1_out1), .in_3(decoder_1_out2), .in_4(decoder_1_out3),
    .in_5(decoder_1_out4), .in_6(decoder_1_out5), .in_7(decoder_1_out6), .in_8(decoder_1_out7),
    .in_9(decoder_1_out8), .in_10(decoder_1_out9), .in_11(decoder_1_out10), .in_12(decoder_1_out11),
    .in_13(decoder_1_out12), .in_14(decoder_1_out13), .in_15(decoder_1_out14), .in_16(decoder_1_out15),
    .in_17(in_8), .in_18(decoder_1_out16), .in_19(decoder_1_out17), .in_23(decoder_1_out18),
    .in_24(decoder_1_out19), .in_25(decoder_1_out20), .in_26(decoder_1_out21), .in_27(decoder_1_out22),
    .in_28(decoder_1_out23), .in_29(decoder_1_out24), .in_30(decoder_1_out25), .in_31(decoder_1_out26),
    .in_32(decoder_1_out27), .in_33(decoder_1_out28), .in_34(decoder_1_out29), .in_35(decoder_1_out30),
    .in_36(decoder_1_out31), .out_37(n32_reg_1_out_37), .out_38(n32_reg_1_out_38), .out_39(n32_reg_1_out_39),
    .out_40(n32_reg_1_out_40), .out_41(n32_reg_1_out_41), .out_42(n32_reg_1_out_42),
    .out_43(n32_reg_1_out_43), .out_44(n32_reg_1_out_44), .out_45(n32_reg_1_out_45),
    .out_46(n32_reg_1_out_46), .out_47(n32_reg_1_out_47), .out_48(n32_reg_1_out_48),
    .out_49(n32_reg_1_out_49), .out_50(n32_reg_1_out_50), .out_51(n32_reg_1_out_51),
    .out_52(n32_reg_1_out_52), .out_53(n32_reg_1_out_53), .out_54(n32_reg_1_out_54),
    .out_55(n32_reg_1_out_55), .out_56(n32_reg_1_out_56), .out_57(n32_reg_1_out_57),
    .out_58(n32_reg_1_out_58), .out_59(n32_reg_1_out_59), .out_60(n32_reg_1_out_60),
    .out_61(n32_reg_1_out_61), .out_62(n32_reg_1_out_62), .out_63(n32_reg_1_out_63),
    .out_64(n32_reg_1_out_64), .out_65(n32_reg_1_out_65), .out_66(n32_reg_1_out_66),
    .out_67(n32_reg_1_out_67), .out_68(n32_reg_1_out_68), .in_20(in_3), .in_22(in_4), .in_21(in_2));
  Multiplexer #(.select(5), .width(32), .enable("false")) multiplexer_2 (
    .in0(n32_reg_1_out_37), .in1(n32_reg_1_out_38), .in2(n32_reg_1_out_39), .in3(n32_reg_1_out_40),
    .in4(n32_reg_1_out_41), .in5(n32_reg_1_out_42), .in6(n32_reg_1_out_43), .in7(n32_reg_1_out_44),
    .in8(n32_reg_1_out_45), .in9(n32_reg_1_out_46), .in10(n32_reg_1_out_47), .in11(n32_reg_1_out_48),
    .in12(n32_reg_1_out_49), .in13(n32_reg_1_out_50), .in14(n32_reg_1_out_51), .in15(n32_reg_1_out_52),
    .in16(n32_reg_1_out_53), .in17(n32_reg_1_out_54), .in18(n32_reg_1_out_55), .in19(n32_reg_1_out_56),
    .in20(n32_reg_1_out_57), .in21(n32_reg_1_out_58), .in22(n32_reg_1_out_59), .in23(n32_reg_1_out_60),
    .in24(n32_reg_1_out_61), .in25(n32_reg_1_out_62), .in26(n32_reg_1_out_63), .in27(n32_reg_1_out_64),
    .in28(n32_reg_1_out_65), .in29(n32_reg_1_out_66), .in30(n32_reg_1_out_67), .in31(n32_reg_1_out_68),
    .out(out_9), .sel(in_5));
  Multiplexer #(.select(5), .width(32), .enable("false")) multiplexer_3 (
    .in0(n32_reg_1_out_37), .in1(n32_reg_1_out_38), .in2(n32_reg_1_out_39), .in3(n32_reg_1_out_40),
    .in4(n32_reg_1_out_41), .in5(n32_reg_1_out_42), .in6(n32_reg_1_out_43), .in7(n32_reg_1_out_44),
    .in8(n32_reg_1_out_45), .in9(n32_reg_1_out_46), .in10(n32_reg_1_out_47), .in11(n32_reg_1_out_48),
    .in12(n32_reg_1_out_49), .in13(n32_reg_1_out_50), .in14(n32_reg_1_out_51), .in15(n32_reg_1_out_52),
    .in16(n32_reg_1_out_53), .in17(n32_reg_1_out_54), .in18(n32_reg_1_out_55), .in19(n32_reg_1_out_56),
    .in20(n32_reg_1_out_57), .in21(n32_reg_1_out_58), .in22(n32_reg_1_out_59), .in23(n32_reg_1_out_60),
    .in24(n32_reg_1_out_61), .in25(n32_reg_1_out_62), .in26(n32_reg_1_out_63), .in27(n32_reg_1_out_64),
    .in28(n32_reg_1_out_65), .in29(n32_reg_1_out_66), .in30(n32_reg_1_out_67), .in31(n32_reg_1_out_68),
    .out(out_10), .sel(in_6));

  // Other names for the same wires on the sheet: data[31:0] = in_8; sel1[4:0] = in_5; sel2[4:0] = in_6;
  //   sel3[4:0] = in_7
endmodule

module is_zero (
  input  [31:0] in_1,
  output [31:0] out_2
);

  wire not_1_out, or_1_out;

  or or_1 (or_1_out, in_1[0], in_1[1], in_1[2], in_1[3], in_1[4], in_1[5], in_1[6], in_1[7], in_1[8], in_1[9], in_1[10], in_1[11], in_1[12], in_1[13], in_1[14], in_1[15], in_1[16], in_1[17], in_1[18], in_1[19], in_1[20], in_1[21], in_1[22], in_1[23], in_1[24], in_1[25], in_1[26], in_1[27], in_1[28], in_1[29], in_1[30], in_1[31]);
  not not_1 (not_1_out, or_1_out);
  assign out_2 = {{31{1'b0}}, not_1_out};  // Bit_Extender bit_extender_1
endmodule

module overflow (
  input  [31:0] in_1,
  input  [31:0] in_2,
  input  [31:0] in_3,
  output out_4
);

  wire and_1_out, and_2_out, not_1_out, not_2_out, not_3_out;

  not not_1 (not_1_out, in_2[31]);
  not not_2 (not_2_out, in_1[31]);
  not not_3 (not_3_out, in_3[31]);
  and and_1 (and_1_out, not_1_out, not_2_out, in_3[31]);
  and and_2 (and_2_out, in_1[31], in_2[31], not_3_out);
  or or_1 (out_4, and_1_out, and_2_out);
endmodule

module big_than (
  input  [31:0] in_1,
  input  [31:0] in_2,
  output [31:0] out_3
);

  wire comparator_1_gt, not_1_out;

  Comparator #(.width(32)) comparator_1 (.a(in_1), .b(in_2), .gt(comparator_1_gt));  // open: eq, lt
  not not_1 (not_1_out, comparator_1_gt);
  assign out_3 = {{31{1'b0}}, not_1_out};  // Bit_Extender bit_extender_1
endmodule

module small_than (
  input  [31:0] in_1,
  input  [31:0] in_2,
  output [31:0] out_3
);

  wire comparator_1_lt, not_1_out;

  not not_1 (not_1_out, comparator_1_lt);
  Comparator #(.width(32)) comparator_1 (.a(in_1), .b(in_2), .lt(comparator_1_lt));  // open: gt, eq
  assign out_3 = {{31{1'b0}}, not_1_out};  // Bit_Extender bit_extender_1
endmodule

module bigeq_than (
  input  [31:0] in_1,
  input  [31:0] in_2,
  output [31:0] out_3
);

  wire comparator_1_eq, comparator_1_gt, not_1_out, or_1_out;

  Comparator #(.width(32)) comparator_1 (.a(in_1), .b(in_2), .gt(comparator_1_gt), .eq(comparator_1_eq));  // open: lt
  or or_1 (or_1_out, comparator_1_gt, comparator_1_eq);
  not not_1 (not_1_out, or_1_out);
  assign out_3 = {{31{1'b0}}, not_1_out};  // Bit_Extender bit_extender_1
endmodule

module smalleq_than (
  input  [31:0] in_1,
  input  [31:0] in_2,
  output [31:0] out_3
);

  wire comparator_1_eq, comparator_1_lt, not_1_out, or_1_out;

  Comparator #(.width(32)) comparator_1 (.a(in_1), .b(in_2), .eq(comparator_1_eq), .lt(comparator_1_lt));  // open: gt
  or or_1 (or_1_out, comparator_1_eq, comparator_1_lt);
  assign out_3 = {{31{1'b0}}, not_1_out};  // Bit_Extender bit_extender_1
  not not_1 (not_1_out, or_1_out);
endmodule

module upper_six (
  input  In0,
  input  In1,
  input  In2,
  input  In3,
  input  In4,
  input  In5,
  output [21:0] out_7
);

  wire and_5_out, and_6_out, and_7_out, and_8_out, and_9_out, and_10_out, and_11_out, and_12_out, and_13_out,
       and_14_out, and_15_out, and_16_out, and_17_out, and_18_out, and_20_out, and_21_out, not_1_out,
       not_2_out, not_3_out, not_4_out, not_5_out, not_6_out, not_7_out, not_8_out, not_9_out, not_10_out,
       not_11_out, not_12_out, not_13_out, not_14_out, not_15_out, not_16_out, not_17_out, not_18_out,
       not_19_out, not_20_out, not_21_out, not_22_out, not_23_out, not_24_out, not_25_out, not_26_out,
       not_27_out, not_28_out, not_29_out, not_30_out, not_31_out, not_33_out, not_35_out, not_36_out,
       not_37_out, not_38_out, not_39_out, not_40_out, not_41_out, not_42_out, not_43_out, not_44_out,
       not_45_out, not_46_out, not_47_out;

  not not_1 (not_1_out, In1);
  not not_2 (not_2_out, In2);
  not not_3 (not_3_out, In0);
  not not_4 (not_4_out, In2);
  not not_5 (not_5_out, In0);
  not not_6 (not_6_out, In2);
  not not_7 (not_7_out, In4);
  not not_8 (not_8_out, In2);
  not not_9 (not_9_out, In5);
  not not_10 (not_10_out, In0);
  not not_11 (not_11_out, In3);
  not not_12 (not_12_out, In0);
  not not_13 (not_13_out, In2);
  not not_14 (not_14_out, In0);
  not not_15 (not_15_out, In3);
  not not_16 (not_16_out, In2);
  not not_17 (not_17_out, In5);
  not not_18 (not_18_out, In2);
  not not_19 (not_19_out, In5);
  not not_20 (not_20_out, In3);
  not not_21 (not_21_out, In5);
  not not_22 (not_22_out, In0);
  not not_23 (not_23_out, In2);
  not not_24 (not_24_out, In4);
  not not_25 (not_25_out, In5);
  not not_26 (not_26_out, In0);
  not not_27 (not_27_out, In4);
  not not_28 (not_28_out, In2);
  not not_29 (not_29_out, In3);
  not not_30 (not_30_out, In0);
  not not_31 (not_31_out, In2);
  not not_32 (out_7[12], In5);
  not not_33 (not_33_out, In4);
  not not_34 (out_7[14], In3);
  not not_35 (not_35_out, In4);
  not not_36 (not_36_out, In5);
  not not_37 (not_37_out, In0);
  not not_38 (not_38_out, In2);
  not not_39 (not_39_out, In3);
  not not_40 (not_40_out, In0);
  not not_41 (not_41_out, In2);
  not not_42 (not_42_out, In0);
  not not_43 (not_43_out, In2);
  not not_44 (not_44_out, In0);
  not not_45 (not_45_out, In3);
  not not_46 (not_46_out, In4);
  not not_47 (not_47_out, In5);
  and and_1 (out_7[0], In0, not_1_out, not_2_out);
  and and_2 (out_7[1], In0, In2);
  and and_3 (out_7[2], not_3_out, not_4_out);
  and and_4 (out_7[3], In2, In3, In4, In5);
  and and_5 (and_5_out, not_5_out, not_6_out, not_7_out, In5);
  and and_6 (and_6_out, not_8_out, In4, not_9_out);
  and and_7 (and_7_out, not_10_out, not_11_out, In4, In5);
  and and_8 (and_8_out, not_12_out, not_13_out, In5);
  and and_9 (and_9_out, not_14_out, not_15_out, In4);
  and and_10 (and_10_out, not_16_out, In4, not_17_out);
  and and_11 (and_11_out, not_18_out, not_19_out);
  and and_12 (and_12_out, In4, not_21_out);
  and and_13 (and_13_out, not_22_out, not_23_out, not_24_out);
  and and_14 (and_14_out, In4, not_25_out);
  and and_15 (and_15_out, not_26_out, In3, not_27_out, In5);
  or or_1 (out_7[9], In2, In0);
  and and_16 (and_16_out, not_28_out, not_29_out, In5);
  and and_17 (and_17_out, not_30_out, In2);
  and and_18 (and_18_out, In0, not_31_out);
  and and_19 (out_7[13], not_33_out, In5);
  and and_20 (and_20_out, In2, In3, not_35_out);
  and and_21 (and_21_out, In2, In3, not_36_out);
  and and_22 (out_7[18], not_37_out, not_38_out, not_39_out);
  and and_23 (out_7[19], not_40_out, not_41_out);
  and and_24 (out_7[20], not_42_out, not_43_out);
  and and_25 (out_7[21], not_44_out, not_45_out, not_46_out, not_47_out);
  or or_2 (out_7[4], and_5_out, and_6_out, and_7_out);
  or or_3 (out_7[5], and_8_out, and_9_out, and_10_out);
  or or_4 (out_7[6], and_11_out, not_20_out, and_12_out, In0);
  or or_5 (out_7[7], and_13_out, and_14_out, and_15_out);
  or or_6 (out_7[11], and_16_out, and_17_out, and_18_out);
  or or_7 (out_7[16], and_20_out, and_21_out);

  assign {out_7[17], out_7[15], out_7[10], out_7[8]} = 4'b0000;
endmodule

module lower_six (
  input  In0,
  input  In1,
  input  In2,
  input  In3,
  input  In4,
  input  In5,
  output [21:0] out_7
);

  wire and_1_out, and_2_out, and_3_out, and_4_out, and_5_out, and_6_out, and_7_out, and_8_out, and_9_out,
       and_10_out, and_11_out, and_12_out, not_1_out, not_2_out, not_3_out, not_4_out, not_5_out, not_6_out,
       not_7_out, not_8_out, not_9_out, not_10_out, not_11_out, not_12_out, not_13_out, not_14_out,
       not_15_out, not_16_out, not_17_out, not_18_out, not_19_out;

  not not_1 (not_1_out, In0);
  not not_2 (not_2_out, In3);
  not not_3 (not_3_out, In0);
  not not_4 (not_4_out, In5);
  not not_5 (not_5_out, In3);
  not not_6 (not_6_out, In0);
  not not_7 (not_7_out, In4);
  not not_8 (not_8_out, In0);
  not not_9 (not_9_out, In4);
  not not_10 (not_10_out, In5);
  not not_11 (not_11_out, In5);
  not not_12 (not_12_out, In0);
  not not_13 (not_13_out, In3);
  not not_14 (not_14_out, In2);
  not not_15 (not_15_out, In4);
  not not_16 (not_16_out, In4);
  not not_17 (not_17_out, In2);
  not not_18 (not_18_out, In3);
  not not_19 (not_19_out, In5);
  and and_1 (and_1_out, In3, In4, In5);
  and and_2 (and_2_out, In2, In5);
  and and_3 (and_3_out, In0, not_2_out, In4);
  and and_4 (and_4_out, In0, In4, In5);
  and and_5 (and_5_out, not_3_out, In4);
  and and_6 (and_6_out, In4, not_4_out);
  and and_7 (and_7_out, In0, not_5_out);
  and and_8 (and_8_out, not_6_out, not_7_out);
  and and_9 (and_9_out, not_8_out, In5);
  and and_10 (and_10_out, In3, not_9_out, In5);
  and and_11 (and_11_out, In2, not_10_out);
  and and_12 (and_12_out, In0, In3, In4, not_11_out);
  and and_13 (out_7[8], not_12_out, not_13_out);
  or or_1 (out_7[11], not_14_out, In5, In4);
  and and_14 (out_7[17], In2, not_15_out);
  and and_15 (out_7[19], In2, not_16_out);
  and and_16 (out_7[21], In0, not_17_out, not_18_out, not_19_out);
  or or_2 (out_7[4], not_1_out, and_1_out, and_2_out);
  or or_3 (out_7[5], and_3_out, and_4_out);
  or or_4 (out_7[6], and_5_out, and_6_out, and_7_out);
  or or_5 (out_7[7], and_8_out, and_9_out, and_10_out, and_11_out, and_12_out);

  assign {out_7[20], out_7[18], out_7[16:12], out_7[10:9], out_7[3:0]} = 13'h220;
endmodule

module middle_five (
  input  In0,
  input  In1,
  input  In2,
  input  In3,
  input  In4,
  output [21:0] out_6
);

  not not_1 (out_6[5], In4);
  not not_2 (out_6[7], In4);

  assign {out_6[21:8], out_6[6], out_6[4:0]} = {{15{1'b0}}, In4, 4'b0100};
endmodule

module select_type (
  input  [5:0] in_1,
  output out_2,
  output out_3
);

  wire not_1_out, or_1_out, or_2_out;

  not not_1 (not_1_out, in_1[0]);
  or or_1 (or_1_out, in_1[5], in_1[4], in_1[3], in_1[2], in_1[1], in_1[0]);
  or or_2 (or_2_out, in_1[5], in_1[4], in_1[3], in_1[2], in_1[1], not_1_out);
  not not_2 (out_2, or_1_out);
  not not_3 (out_3, or_2_out);
endmodule

module extender_16 (
  input  in_1,
  input  [15:0] in_2,
  output [31:0] out_3
);

  wire [31:0] bit_extender_1_out, bit_extender_2_out;

  assign bit_extender_1_out = {{16{1'b0}}, in_2};  // Bit_Extender bit_extender_1
  assign bit_extender_2_out = {{16{in_2[15]}}, in_2};  // Bit_Extender bit_extender_2
  Multiplexer #(.width(32), .enable("false")) multiplexer_1 (
    .in0(bit_extender_1_out), .in1(bit_extender_2_out), .out(out_3), .sel(in_1));
endmodule

module extender_8 (
  input  in_1,
  input  [7:0] in_2,
  output [31:0] out_3
);

  wire [31:0] bit_extender_1_out, bit_extender_2_out;

  assign bit_extender_1_out = {{24{1'b0}}, in_2};  // Bit_Extender bit_extender_1
  assign bit_extender_2_out = {{24{in_2[7]}}, in_2};  // Bit_Extender bit_extender_2
  Multiplexer #(.width(32), .enable("false")) multiplexer_1 (
    .in0(bit_extender_1_out), .in1(bit_extender_2_out), .out(out_3), .sel(in_1));
endmodule

module changer_16 (
  input  in_1,
  input  [31:0] in_2,
  input  [31:0] in_3,
  output [31:0] out_4
);

  Multiplexer #(.width(32), .enable("false")) multiplexer_1 (
    .in0({in_2[31:16], in_3[15:0]}), .in1({in_3[15:0], in_2[15:0]}), .out(out_4), .sel(in_1));
endmodule

module changer_8 (
  input  [1:0] in_1,
  input  [31:0] in_2,
  input  [31:0] in_3,
  output [31:0] out_4
);

  Multiplexer #(.select(2), .width(32), .enable("false")) multiplexer_1 (
    .in0({in_2[31:8], in_3[7:0]}), .in1({in_2[31:16], in_3[7:0], in_2[7:0]}),
    .in2({in_2[31:24], in_3[7:0], in_2[15:0]}), .in3({in_3[7:0], in_2[23:0]}), .out(out_4), .sel(in_1));
endmodule

module _32_reg (
  input  in_1,
  input  in_2,
  input  in_3,
  input  in_4,
  input  in_5,
  input  in_6,
  input  in_7,
  input  in_8,
  input  in_9,
  input  in_10,
  input  in_11,
  input  in_12,
  input  in_13,
  input  in_14,
  input  in_15,
  input  in_16,
  input  [31:0] in_17,
  input  in_18,
  input  in_19,
  input  in_20,
  input  in_21,
  input  in_22,
  input  in_23,
  input  in_24,
  input  in_25,
  input  in_26,
  input  in_27,
  input  in_28,
  input  in_29,
  input  in_30,
  input  in_31,
  input  in_32,
  input  in_33,
  input  in_34,
  input  in_35,
  input  in_36,
  output [31:0] out_37,
  output [31:0] out_38,
  output [31:0] out_39,
  output [31:0] out_40,
  output [31:0] out_41,
  output [31:0] out_42,
  output [31:0] out_43,
  output [31:0] out_44,
  output [31:0] out_45,
  output [31:0] out_46,
  output [31:0] out_47,
  output [31:0] out_48,
  output [31:0] out_49,
  output [31:0] out_50,
  output [31:0] out_51,
  output [31:0] out_52,
  output [31:0] out_53,
  output [31:0] out_54,
  output [31:0] out_55,
  output [31:0] out_56,
  output [31:0] out_57,
  output [31:0] out_58,
  output [31:0] out_59,
  output [31:0] out_60,
  output [31:0] out_61,
  output [31:0] out_62,
  output [31:0] out_63,
  output [31:0] out_64,
  output [31:0] out_65,
  output [31:0] out_66,
  output [31:0] out_67,
  output [31:0] out_68
);

  wire I0, I1, I2, I3, I4, I5, I6, I7, I8, I9, I10, I11, I12, I13, I14, I15, I16, I17, I18, I19, I20, I21,
       I22, I23, I24, I25, I26, I27, I28, I29, I30, I31;

  and and_1 (I0, in_1, 1'b0, in_22);
  and and_2 (I8, in_9, in_22);
  and and_3 (I16, in_18, in_22);
  and and_4 (I24, in_29, in_22);
  Register #(.width(32)) register_1 (.D(in_17), .en(I0), .Q(out_37), .clk(in_20), .clr(in_21));
  Register #(.width(32)) register_2 (.D(in_17), .en(I8), .Q(out_45), .clk(in_20), .clr(in_21));
  Register #(.width(32)) register_3 (.D(in_17), .en(I16), .Q(out_53), .clk(in_20), .clr(in_21));
  Register #(.width(32)) register_4 (.D(in_17), .en(I24), .Q(out_61), .clk(in_20), .clr(in_21));
  and and_5 (I1, in_2, in_22);
  and and_6 (I9, in_10, in_22);
  and and_7 (I17, in_19, in_22);
  and and_8 (I25, in_30, in_22);
  Register #(.width(32)) register_5 (.D(in_17), .en(I1), .Q(out_38), .clk(in_20), .clr(in_21));
  Register #(.width(32)) register_6 (.D(in_17), .en(I9), .Q(out_46), .clk(in_20), .clr(in_21));
  Register #(.width(32)) register_7 (.D(in_17), .en(I17), .Q(out_54), .clk(in_20), .clr(in_21));
  Register #(.width(32)) register_8 (.D(in_17), .en(I25), .Q(out_62), .clk(in_20), .clr(in_21));
  and and_9 (I2, in_3, in_22);
  and and_10 (I10, in_11, in_22);
  and and_11 (I18, in_23, in_22);
  and and_12 (I26, in_31, in_22);
  Register #(.width(32)) register_9 (.D(in_17), .en(I2), .Q(out_39), .clk(in_20), .clr(in_21));
  Register #(.width(32)) register_10 (.D(in_17), .en(I10), .Q(out_47), .clk(in_20), .clr(in_21));
  Register #(.width(32)) register_11 (.D(in_17), .en(I18), .Q(out_55), .clk(in_20), .clr(in_21));
  Register #(.width(32)) register_12 (.D(in_17), .en(I26), .Q(out_63), .clk(in_20), .clr(in_21));
  and and_13 (I3, in_4, in_22);
  and and_14 (I11, in_12, in_22);
  and and_15 (I19, in_24, in_22);
  and and_16 (I27, in_32, in_22);
  Register #(.width(32)) register_13 (.D(in_17), .en(I3), .Q(out_40), .clk(in_20), .clr(in_21));
  Register #(.width(32)) register_14 (.D(in_17), .en(I11), .Q(out_48), .clk(in_20), .clr(in_21));
  Register #(.width(32)) register_15 (.D(in_17), .en(I19), .Q(out_56), .clk(in_20), .clr(in_21));
  Register #(.width(32)) register_16 (.D(in_17), .en(I27), .Q(out_64), .clk(in_20), .clr(in_21));
  and and_17 (I4, in_5, in_22);
  and and_18 (I12, in_13, in_22);
  and and_19 (I20, in_25, in_22);
  and and_20 (I28, in_33, in_22);
  and and_21 (I5, in_6, in_22);
  and and_22 (I13, in_14, in_22);
  and and_23 (I21, in_26, in_22);
  and and_24 (I29, in_34, in_22);
  Register #(.width(32)) register_17 (.D(in_17), .en(I4), .Q(out_41), .clk(in_20), .clr(in_21));
  Register #(.width(32)) register_18 (.D(in_17), .en(I12), .Q(out_49), .clk(in_20), .clr(in_21));
  Register #(.width(32)) register_19 (.D(in_17), .en(I20), .Q(out_57), .clk(in_20), .clr(in_21));
  Register #(.width(32)) register_20 (.D(in_17), .en(I28), .Q(out_65), .clk(in_20), .clr(in_21));
  and and_25 (I6, in_7, in_22);
  and and_26 (I14, in_15, in_22);
  and and_27 (I22, in_27, in_22);
  and and_28 (I30, in_35, in_22);
  Register #(.width(32)) register_21 (.D(in_17), .en(I5), .Q(out_42), .clk(in_20), .clr(in_21));
  Register #(.width(32)) register_22 (.D(in_17), .en(I13), .Q(out_50), .clk(in_20), .clr(in_21));
  Register #(.width(32)) register_23 (.D(in_17), .en(I21), .Q(out_58), .clk(in_20), .clr(in_21));
  Register #(.width(32)) register_24 (.D(in_17), .en(I29), .Q(out_66), .clk(in_20), .clr(in_21));
  and and_29 (I7, in_8, in_22);
  and and_30 (I15, in_16, in_22);
  and and_31 (I23, in_28, in_22);
  and and_32 (I31, in_36, in_22);
  Register #(.width(32)) register_25 (.D(in_17), .en(I6), .Q(out_43), .clk(in_20), .clr(in_21));
  Register #(.width(32)) register_26 (.D(in_17), .en(I14), .Q(out_51), .clk(in_20), .clr(in_21));
  Register #(.width(32)) register_27 (.D(in_17), .en(I22), .Q(out_59), .clk(in_20), .clr(in_21));
  Register #(.width(32)) register_28 (.D(in_17), .en(I30), .Q(out_67), .clk(in_20), .clr(in_21));
  Register #(.width(32)) register_29 (.D(in_17), .en(I7), .Q(out_44), .clk(in_20), .clr(in_21));
  Register #(.width(32)) register_30 (.D(in_17), .en(I15), .Q(out_52), .clk(in_20), .clr(in_21));
  Register #(.width(32)) register_31 (.D(in_17), .en(I23), .Q(out_60), .clk(in_20), .clr(in_21));
  Register #(.width(32)) register_32 (.D(in_17), .en(I31), .Q(out_68), .clk(in_20), .clr(in_21));

  // Other names for the same wires on the sheet: _0[31:0] = out_37; _1[31:0] = out_38; _2[31:0] = out_39;
  //   _3[31:0] = out_40; _4[31:0] = out_41; _5[31:0] = out_42; _6[31:0] = out_43; _7[31:0] = out_44;
  //   _8[31:0] = out_45; _9[31:0] = out_46; _10[31:0] = out_47; _11[31:0] = out_48; _12[31:0] = out_49;
  //   _13[31:0] = out_50; _14[31:0] = out_51; _15[31:0] = out_52; _16[31:0] = out_53; _17[31:0] = out_54;
  //   _18[31:0] = out_55; _19[31:0] = out_56; _20[31:0] = out_57; _21[31:0] = out_58; _22[31:0] = out_59;
  //   _23[31:0] = out_60; _24[31:0] = out_61; _25[31:0] = out_62; _26[31:0] = out_63; _27[31:0] = out_64;
  //   _28[31:0] = out_65; _29[31:0] = out_66; _30[31:0] = out_67; _31[31:0] = out_68; S0 = in_1; S1 = in_2; S2 = in_3;
  //   S3 = in_4; S4 = in_5; S5 = in_6; S6 = in_7; S7 = in_8; S8 = in_9; S9 = in_10; S10 = in_11; S11 = in_12;
  //   S12 = in_13; S13 = in_14; S14 = in_15; S15 = in_16; S16 = in_18; S17 = in_19; S18 = in_23; S19 = in_24;
  //   S20 = in_25; S21 = in_26; S22 = in_27; S23 = in_28; S24 = in_29; S25 = in_30; S26 = in_31; S27 = in_32;
  //   S28 = in_33; S29 = in_34; S30 = in_35; S31 = in_36
endmodule
