// Logisim project cpu -cache -流水线寄存器F-D.circ as structural Verilog: 4 circuits, main circuit F_D_reg
module F_D_reg (
  input  in_1,
  input  in_2,
  input  [31:0] instr_i,
  input  [31:0] pc_i,
  input  in_5,
  output [31:0] instr_o,
  output [31:0] pc_o
);

  wire clk_prime, not_1_out, not_2_out;

  not not_1 (not_1_out, in_5);
  not not_2 (not_2_out, in_5);
  buf and_1 (clk_prime, in_1);  // AND_Gate
  Register #(.width(32)) register_1 (.D(instr_i), .en(not_1_out), .Q(instr_o), .clk(clk_prime), .clr(in_2));
  Register #(.width(32)) register_2 (.D(pc_i), .en(not_2_out), .Q(pc_o), .clk(clk_prime), .clr(in_2));

  // Other names for the same wires on the sheet: clk = in_1; F_D_stall = in_5; reset = in_2
endmodule

module D_E_reg (
  input  in_1,
  input  in_2,
  input  [31:0] pc_i,
  input  [31:0] RD1_i,
  input  [31:0] pc_4_i,
  input  [31:0] RD2_i,
  input  [31:0] pc_8_i,
  input  [4:0] rs_i,
  input  [31:0] EXTresult_i,
  input  [4:0] rt_i,
  input  [4:0] rd_i,
  input  [1:0] regdst,
  input  memwrite,
  input  regwrite,
  input  in_15,
  input  alusrc,
  input  memreacd,
  input  [1:0] memtoreg,
  input  [2:0] aluctrl,
  input  [31:0] instr_i,
  output [31:0] pc_o,
  output [31:0] RD1_o,
  output [31:0] pc_4_o,
  output [31:0] RD2_o,
  output [31:0] pc_8_o,
  output [4:0] rs_o,
  output [31:0] EXTresult_o,
  output [4:0] rt_o,
  output [4:0] rd_o,
  output [1:0] out_30,
  output out_31,
  output out_32,
  output out_33,
  output out_34,
  output [1:0] out_35,
  output [2:0] out_36,
  output [31:0] out_37
);

  wire multiplexer_2_out, multiplexer_3_out, multiplexer_4_out, multiplexer_5_out;
  wire [1:0] multiplexer_1_out, multiplexer_6_out;
  wire [2:0] multiplexer_7_out;
  wire [4:0] multiplexer_10_out, multiplexer_11_out, multiplexer_12_out;
  wire [31:0] multiplexer_8_out, multiplexer_9_out, multiplexer_13_out, multiplexer_14_out,
       multiplexer_15_out, multiplexer_16_out, multiplexer_17_out;

  Multiplexer #(.width(2), .enable("false")) multiplexer_1 (
    .in0(regdst), .in1(2'b00), .out(multiplexer_1_out), .sel(in_15));
  Multiplexer #(.enable("false")) multiplexer_2 (.in0(memwrite), .in1(1'b0), .out(multiplexer_2_out), .sel(in_15));
  Multiplexer #(.enable("false")) multiplexer_3 (.in0(regwrite), .in1(1'b0), .out(multiplexer_3_out), .sel(in_15));
  Multiplexer #(.enable("false")) multiplexer_4 (.in0(alusrc), .in1(1'b0), .out(multiplexer_4_out), .sel(in_15));
  Multiplexer #(.enable("false")) multiplexer_5 (.in0(memreacd), .in1(1'b0), .out(multiplexer_5_out), .sel(in_15));
  Multiplexer #(.width(2), .enable("false")) multiplexer_6 (
    .in0(memtoreg), .in1(2'b00), .out(multiplexer_6_out), .sel(in_15));
  Multiplexer #(.width(3), .enable("false")) multiplexer_7 (
    .in0(aluctrl), .in1(3'b000), .out(multiplexer_7_out), .sel(in_15));
  Register #(.width(2)) register_1 (.D(multiplexer_1_out), .Q(out_30), .clk(in_1), .clr(in_2));  // open: en
  Register #(.width(1)) register_2 (.D(multiplexer_2_out), .Q(out_31), .clk(in_1), .clr(in_2));  // open: en
  Register #(.width(1)) register_3 (.D(multiplexer_3_out), .Q(out_32), .clk(in_1), .clr(in_2));  // open: en
  Register #(.width(1)) register_4 (.D(multiplexer_4_out), .Q(out_33), .clk(in_1), .clr(in_2));  // open: en
  Register #(.width(1)) register_5 (.D(multiplexer_5_out), .Q(out_34), .clk(in_1), .clr(in_2));  // open: en
  Register #(.width(2)) register_6 (.D(multiplexer_6_out), .Q(out_35), .clk(in_1), .clr(in_2));  // open: en
  Register #(.width(3)) register_7 (.D(multiplexer_7_out), .Q(out_36), .clk(in_1), .clr(in_2));  // open: en
  Multiplexer #(.width(32), .enable("false")) multiplexer_8 (
    .in0(RD1_i), .in1({32{1'b0}}), .out(multiplexer_8_out), .sel(in_15));
  Multiplexer #(.width(32), .enable("false")) multiplexer_9 (
    .in0(RD2_i), .in1({32{1'b0}}), .out(multiplexer_9_out), .sel(in_15));
  Multiplexer #(.width(5), .enable("false")) multiplexer_10 (
    .in0(rs_i), .in1({5{1'b0}}), .out(multiplexer_10_out), .sel(in_15));
  Multiplexer #(.width(5), .enable("false")) multiplexer_11 (
    .in0(rt_i), .in1({5{1'b0}}), .out(multiplexer_11_out), .sel(in_15));
  Multiplexer #(.width(5), .enable("false")) multiplexer_12 (
    .in0(rd_i), .in1({5{1'b0}}), .out(multiplexer_12_out), .sel(in_15));
  Register #(.width(32)) register_8 (.D(multiplexer_8_out), .Q(RD1_o), .clk(in_1), .clr(in_2));  // open: en
  Register #(.width(32)) register_9 (.D(multiplexer_9_out), .Q(RD2_o), .clk(in_1), .clr(in_2));  // open: en
  Register #(.width(5)) register_10 (.D(multiplexer_10_out), .Q(rs_o), .clk(in_1), .clr(in_2));  // open: en
  Register #(.width(5)) register_11 (.D(multiplexer_11_out), .Q(rt_o), .clk(in_1), .clr(in_2));  // open: en
  Register #(.width(5)) register_12 (.D(multiplexer_12_out), .Q(rd_o), .clk(in_1), .clr(in_2));  // open: en
  Multiplexer #(.width(32), .enable("false")) multiplexer_13 (
    .in0(instr_i), .in1({32{1'b0}}), .out(multiplexer_13_out), .sel(in_15));
  Register #(.width(32)) register_13 (.D(multiplexer_13_out), .Q(out_37), .clk(in_1), .clr(in_2));  // open: en
  Multiplexer #(.width(32), .enable("false")) multiplexer_14 (
    .in0(pc_i), .in1({32{1'b0}}), .out(multiplexer_14_out), .sel(in_15));
  Multiplexer #(.width(32), .enable("false")) multiplexer_15 (
    .in0(pc_4_i), .in1({32{1'b0}}), .out(multiplexer_15_out), .sel(in_15));
  Multiplexer #(.width(32), .enable("false")) multiplexer_16 (
    .in0(pc_8_i), .in1({32{1'b0}}), .out(multiplexer_16_out), .sel(in_15));
  Multiplexer #(.width(32), .enable("false")) multiplexer_17 (
    .in0(EXTresult_i), .in1({32{1'b0}}), .out(multiplexer_17_out), .sel(in_15));
  Register #(.width(32)) register_14 (.D(multiplexer_14_out), .Q(pc_o), .clk(in_1), .clr(in_2));  // open: en
  Register #(.width(32)) register_15 (.D(multiplexer_15_out), .Q(pc_4_o), .clk(in_1), .clr(in_2));  // open: en
  Register #(.width(32)) register_16 (.D(multiplexer_16_out), .Q(pc_8_o), .clk(in_1), .clr(in_2));  // open: en
  Register #(.width(32)) register_17 (.D(multiplexer_17_out), .Q(EXTresult_o), .clk(in_1), .clr(in_2));  // open: en

  // Other names for the same wires on the sheet: clk = in_1; clk_prime = in_1; flush = in_15; Reset = in_2
endmodule

module E_M_reg (
  input  in_1,
  input  in_2,
  input  memwrite,
  input  regwrite,
  input  memreacd,
  input  [1:0] memtoreg,
  input  [31:0] aluresult_i,
  input  [31:0] writedata_i,
  input  [4:0] writereg_i,
  input  [31:0] pc_i,
  input  [31:0] pc_4_i,
  input  [31:0] pc_8_i,
  input  [31:0] instr_i,
  output out_14,
  output out_15,
  output out_16,
  output [1:0] out_17,
  output [31:0] out_18,
  output [31:0] out_19,
  output [4:0] out_20,
  output [31:0] pc_o,
  output [31:0] pc_4_o,
  output [31:0] pc_8_o,
  output [31:0] out_24
);

  Register #(.width(1)) register_1 (.D(memwrite), .Q(out_14), .clk(in_1), .clr(in_2));  // open: en
  Register #(.width(1)) register_2 (.D(regwrite), .Q(out_15), .clk(in_1), .clr(in_2));  // open: en
  Register #(.width(1)) register_3 (.D(memreacd), .Q(out_16), .clk(in_1), .clr(in_2));  // open: en
  Register #(.width(2)) register_4 (.D(memtoreg), .Q(out_17), .clk(in_1), .clr(in_2));  // open: en
  Register #(.width(32)) register_5 (.D(aluresult_i), .Q(out_18), .clk(in_1), .clr(in_2));  // open: en
  Register #(.width(32)) register_6 (.D(writedata_i), .Q(out_19), .clk(in_1), .clr(in_2));  // open: en
  Register #(.width(5)) register_7 (.D(writereg_i), .Q(out_20), .clk(in_1), .clr(in_2));  // open: en
  Register #(.width(32)) register_8 (.D(pc_i), .Q(pc_o), .clk(in_1), .clr(in_2));  // open: en
  Register #(.width(32)) register_9 (.D(pc_4_i), .Q(pc_4_o), .clk(in_1), .clr(in_2));  // open: en
  Register #(.width(32)) register_10 (.D(pc_8_i), .Q(pc_8_o), .clk(in_1), .clr(in_2));  // open: en
  Register #(.width(32)) register_11 (.D(instr_i), .Q(out_24), .clk(in_1), .clr(in_2));  // open: en

  // Other names for the same wires on the sheet: clk = in_1; clk_prime = in_1; Reset = in_2
endmodule

module M_W_reg (
  input  in_1,
  input  in_2,
  input  regwrite,
  input  [1:0] memtoreg,
  input  [4:0] writereg_i,
  input  [31:0] aluresult_i,
  input  [31:0] writedata_i,
  input  [31:0] readdata_i,
  input  [31:0] pc_i,
  input  [31:0] pc_4_i,
  input  [31:0] pc_8_i,
  input  [31:0] instr_i,
  input  [31:0] memaddr,
  input  [31:0] memdata,
  input  memwrite,
  output out_16,
  output [1:0] out_17,
  output [4:0] out_18,
  output [31:0] out_19,
  output [31:0] out_20,
  output [31:0] out_21,
  output [31:0] pc_o,
  output [31:0] pc_4_o,
  output [31:0] pc_8_o,
  output [31:0] out_25,
  output [31:0] out_26,
  output [31:0] out_27,
  output out_28
);

  Register #(.width(1)) register_1 (.D(regwrite), .Q(out_16), .clk(in_1), .clr(in_2));  // open: en
  Register #(.width(2)) register_2 (.D(memtoreg), .Q(out_17), .clk(in_1), .clr(in_2));  // open: en
  Register #(.width(5)) register_3 (.D(writereg_i), .Q(out_18), .clk(in_1), .clr(in_2));  // open: en
  Register #(.width(32)) register_4 (.D(aluresult_i), .Q(out_19), .clk(in_1), .clr(in_2));  // open: en
  Register #(.width(32)) register_5 (.D(writedata_i), .Q(out_20), .clk(in_1), .clr(in_2));  // open: en
  Register #(.width(32)) register_6 (.D(readdata_i), .Q(out_21), .clk(in_1), .clr(in_2));  // open: en
  Register #(.width(32)) register_7 (.D(pc_i), .Q(pc_o), .clk(in_1), .clr(in_2));  // open: en
  Register #(.width(32)) register_8 (.D(pc_4_i), .Q(pc_4_o), .clk(in_1), .clr(in_2));  // open: en
  Register #(.width(32)) register_9 (.D(pc_8_i), .Q(pc_8_o), .clk(in_1), .clr(in_2));  // open: en
  Register #(.width(32)) register_10 (.D(instr_i), .Q(out_25), .clk(in_1), .clr(in_2));  // open: en
  Register #(.width(32)) register_11 (.D(memaddr), .Q(out_26), .clk(in_1), .clr(in_2));  // open: en
  Register #(.width(32)) register_12 (.D(memdata), .Q(out_27), .clk(in_1), .clr(in_2));  // open: en
  Register #(.width(1)) register_13 (.D(memwrite), .Q(out_28), .clk(in_1), .clr(in_2));  // open: en

  // Other names for the same wires on the sheet: clk = in_1; clk_prime = in_1; Reset = in_2
endmodule
