// Logisim project CPU_copy.circ as structural Verilog: 8 circuits, main circuit main
module main (
  input  Reset,
  output [31:0] out_2,
  output out_3,
  output [4:0] out_4,
  output [31:0] out_5,
  output out_6,
  output [4:0] out_7,
  output [31:0] out_8
);

  wire alu_1_zero, clock_1_out, ctrl_1_alusrc, ctrl_1_memtoreg, ctrl_1_npc_sel, ctrl_1_regdst;
  wire [1:0] ctrl_1_aluctr, ctrl_1_extop;
  wire [31:0] alu_1_c, dm_1_out_6, ext_1_extout, grf_1_rd1, multiplexer_2_out;

  Multiplexer #(.width(5)) multiplexer_1 (
    .in0(out_2[20:16]), .in1(out_2[15:11]), .out(out_4), .sel(ctrl_1_regdst));  // open: en
  GRF grf_1 (
    .A1(out_2[25:21]), .A2(out_2[20:16]), .A3(out_4), .WD(out_5), .RD1(grf_1_rd1), .RD2(out_8),
    .clk(clock_1_out), .Reset(Reset), .WE(out_3));
  EXT ext_1 (.Imm(out_2[15:0]), .EXTop(ctrl_1_extop), .EXTout(ext_1_extout));
  ALU alu_1 (
    .A(grf_1_rd1), .B(multiplexer_2_out), .ALUctr(ctrl_1_aluctr), .C({alu_1_c[31:7], out_7, alu_1_c[1:0]}),
    .zero(alu_1_zero));
  Multiplexer #(.width(32)) multiplexer_2 (
    .in0(out_8), .in1(ext_1_extout), .out(multiplexer_2_out), .sel(ctrl_1_alusrc));  // open: en
  IFU ifu_1 (.nPC_sel(ctrl_1_npc_sel), .zero(alu_1_zero), .clk(clock_1_out), .Reset(Reset), .DO(out_2));
  CTRL ctrl_1 (
    .op5(out_2[31]), .op4(out_2[30]), .op3(out_2[29]), .op2(out_2[28]), .op1(out_2[27]), .op0(out_2[26]),
    .func5(out_2[5]), .func4(out_2[4]), .func3(out_2[3]), .func2(out_2[2]), .func1(out_2[1]),
    .func0(out_2[0]), .RegDst(ctrl_1_regdst), .AluSrc(ctrl_1_alusrc), .MemtoReg(ctrl_1_memtoreg),
    .RegWrite(out_3), .MemWrite(out_6), .nPC_sel(ctrl_1_npc_sel), .ExtOp(ctrl_1_extop), .ALUctr(ctrl_1_aluctr));
  Clock clock_1 (.out(clock_1_out));
  DM dm_1 (.Ad(out_7), .DIn(out_8), .MemWrite(out_6), .clk(clock_1_out), .reset(Reset), .out_6(dm_1_out_6));
  Multiplexer #(.width(32)) multiplexer_3 (
    .in0({alu_1_c[31:7], out_7, alu_1_c[1:0]}), .in1(dm_1_out_6), .out(out_5), .sel(ctrl_1_memtoreg));  // open: en

  // Other names for the same wires on the sheet: MemAddr[4:0] = out_7; Instr[31:0] = out_2; MemData[31:0] = out_8;
  //   MemWrite = out_6; RegAddr[4:0] = out_4; RegData[31:0] = out_5; RegWrite = out_3
endmodule

module IFU (
  input  nPC_sel,
  input  zero,
  input  clk,
  input  Reset,
  output [31:0] DO
);

  wire and_1_out;
  wire [31:0] adder_1_out, adder_2_out, bit_extender_1_out, multiplexer_1_out, multiplier_1_out, PC_q;

  assign bit_extender_1_out = {{16{1'b0}}, DO[15:0]};  // Bit_Extender bit_extender_1
  and and_1 (and_1_out, nPC_sel, zero);
  Adder #(.width(32)) adder_1 (.a(32'h4), .b(PC_q), .out(adder_1_out));  // open: cin, cout
  Multiplier #(.width(32)) multiplier_1 (.a(32'h4), .b(bit_extender_1_out), .out(multiplier_1_out));  // open: cin, cout
  Adder #(.width(32)) adder_2 (.a(adder_1_out), .b(multiplier_1_out), .out(adder_2_out));  // open: cin, cout
  Multiplexer #(.width(32)) multiplexer_1 (
    .in0(adder_1_out), .in1(adder_2_out), .out(multiplexer_1_out), .sel(and_1_out));  // open: en
  Register #(.width(32)) PC (.D(multiplexer_1_out), .Q(PC_q), .clk(clk), .clr(Reset));  // open: en
  ROM #(.addrWidth(5), .dataWidth(32)) rom_1 (.addr(PC_q[6:2]), .data(DO));  // open: sel

  // Notes on the sheet:
  //   contents of rom_1 (hex, n*v repeats v):
  //   34040100 34850123 3c0601c8 3c07ffff 34e7ffff 868021 878821 e7a021 869023 879823 ac040000 ac050004
  //   ac060008 ac07000c ac100010 ac110014 ac120018 ac13002c ac140030 8c040000 8c05000c ac04001c ac050020
  //   34040001 34050002 34060001 10850001 10860001 ad040024 ad050028
endmodule

module GRF (
  input  clk,
  input  Reset,
  input  WE,
  input  [4:0] A1,
  input  [4:0] A2,
  input  [4:0] A3,
  input  [31:0] WD,
  output [31:0] RD1,
  output [31:0] RD2
);

  wire _100, _101, _102, _103, _104, _105, _106, _107, _108, _109, _110, _111, _112, _113, _114, _115, _116,
       _117, _118, _119, _120, _121, _122, _123, _124, _125, _126, _127, _128, _129, _130, _131;
  wire [31:0] _00, _01, _02, _03, _04, _05, _06, _07, _08, _09, _10, _11, _12, _13, _14, _15, _16, _17, _18,
       _19, _20, _21, _22, _23, _24, _25, _26, _27, _28, _29, _30, _31;

  Register #(.width(32)) u__01 (.Q(_00));  // open: D, en, clk, clr
  Register #(.width(32)) _01_2 (.D(WD), .en(_101), .Q(_01), .clk(clk), .clr(Reset));
  Register #(.width(32)) u__02 (.D(WD), .en(_102), .Q(_02), .clk(clk), .clr(Reset));
  Register #(.width(32)) u__03 (.D(WD), .en(_103), .Q(_03), .clk(clk), .clr(Reset));
  Multiplexer #(.select(5), .width(32)) multiplexer_1 (
    .in0(_00), .in1(_01), .in2(_02), .in3(_03), .in4(_04), .in5(_05), .in6(_06), .in7(_07), .in8(_08),
    .in9(_09), .in10(_10), .in11(_11), .in12(_12), .in13(_13), .in14(_14), .in15(_15), .in16(_16),
    .in17(_17), .in18(_18), .in19(_19), .in20(_20), .in21(_21), .in22(_22), .in23(_23), .in24(_24),
    .in25(_25), .in26(_26), .in27(_27), .in28(_28), .in29(_29), .in30(_30), .in31(_31), .out(RD1), .sel(A1));  // open: en
  Register #(.width(32)) u__04 (.D(WD), .en(_104), .Q(_04), .clk(clk), .clr(Reset));
  Register #(.width(32)) u__05 (.D(WD), .en(_105), .Q(_05), .clk(clk), .clr(Reset));
  Register #(.width(32)) u__06 (.D(WD), .en(_106), .Q(_06), .clk(clk), .clr(Reset));
  Register #(.width(32)) u__07 (.D(WD), .en(_107), .Q(_07), .clk(clk), .clr(Reset));
  Register #(.width(32)) u__08 (.D(WD), .en(_108), .Q(_08), .clk(clk), .clr(Reset));
  Register #(.width(32)) u__09 (.D(WD), .en(_109), .Q(_09), .clk(clk), .clr(Reset));
  Register #(.width(32)) u__10 (.D(WD), .en(_110), .Q(_10), .clk(clk), .clr(Reset));
  Register #(.width(32)) u__11 (.D(WD), .en(_111), .Q(_11), .clk(clk), .clr(Reset));
  Multiplexer #(.select(5), .width(32)) multiplexer_2 (
    .in0(_00), .in1(_01), .in2(_02), .in3(_03), .in4(_04), .in5(_05), .in6(_06), .in7(_07), .in8(_08),
    .in9(_09), .in10(_10), .in11(_11), .in12(_12), .in13(_13), .in14(_14), .in15(_15), .in16(_16),
    .in17(_17), .in18(_18), .in19(_19), .in20(_20), .in21(_21), .in22(_22), .in23(_23), .in24(_24),
    .in25(_25), .in26(_26), .in27(_27), .in28(_28), .in29(_29), .in30(_30), .in31(_31), .out(RD2), .sel(A2));  // open: en
  Register #(.width(32)) u__12 (.D(WD), .en(_112), .Q(_12), .clk(clk), .clr(Reset));
  Register #(.width(32)) u__13 (.D(WD), .en(_113), .Q(_13), .clk(clk), .clr(Reset));
  Register #(.width(32)) u__14 (.D(WD), .en(_114), .Q(_14), .clk(clk), .clr(Reset));
  Register #(.width(32)) u__15 (.D(WD), .en(_115), .Q(_15), .clk(clk), .clr(Reset));
  Register #(.width(32)) u__16 (.D(WD), .en(_116), .Q(_16), .clk(clk), .clr(Reset));
  Register #(.width(32)) u__17 (.D(WD), .en(_117), .Q(_17), .clk(clk), .clr(Reset));
  Register #(.width(32)) u__18 (.D(WD), .en(_118), .Q(_18), .clk(clk), .clr(Reset));
  Register #(.width(32)) u__19 (.D(WD), .en(_119), .Q(_19), .clk(clk), .clr(Reset));
  Demultiplexer #(.select(5)) demultiplexer_1 (
    .out0(_100), .out1(_101), .out2(_102), .out3(_103), .out4(_104), .out5(_105), .out6(_106), .out7(_107),
    .out8(_108), .out9(_109), .out10(_110), .out11(_111), .out12(_112), .out13(_113), .out14(_114),
    .out15(_115), .out16(_116), .out17(_117), .out18(_118), .out19(_119), .out20(_120), .out21(_121),
    .out22(_122), .out23(_123), .out24(_124), .out25(_125), .out26(_126), .out27(_127), .out28(_128),
    .out29(_129), .out30(_130), .out31(_131), .in(WE), .sel(A3));  // open: en
  Register #(.width(32)) u__20 (.D(WD), .en(_120), .Q(_20), .clk(clk), .clr(Reset));
  Register #(.width(32)) u__21 (.D(WD), .en(_121), .Q(_21), .clk(clk), .clr(Reset));
  Register #(.width(32)) u__22 (.D(WD), .en(_122), .Q(_22), .clk(clk), .clr(Reset));
  Register #(.width(32)) u__23 (.D(WD), .en(_123), .Q(_23), .clk(clk), .clr(Reset));
  Register #(.width(32)) u__24 (.D(WD), .en(_124), .Q(_24), .clk(clk), .clr(Reset));
  Register #(.width(32)) u__25 (.D(WD), .en(_125), .Q(_25), .clk(clk), .clr(Reset));
  Register #(.width(32)) u__26 (.D(WD), .en(_126), .Q(_26), .clk(clk), .clr(Reset));
  Register #(.width(32)) u__27 (.D(WD), .en(_127), .Q(_27), .clk(clk), .clr(Reset));
  Register #(.width(32)) u__28 (.D(WD), .en(_128), .Q(_28), .clk(clk), .clr(Reset));
  Register #(.width(32)) u__29 (.D(WD), .en(_129), .Q(_29), .clk(clk), .clr(Reset));
  Register #(.width(32)) u__30 (.D(WD), .en(_130), .Q(_30), .clk(clk), .clr(Reset));
  Register #(.width(32)) u__31 (.D(WD), .en(_131), .Q(_31), .clk(clk), .clr(Reset));
endmodule

module EXT (
  input  [15:0] Imm,
  input  [1:0] EXTop,
  output [31:0] EXTout
);

  wire [31:0] bit_extender_1_out, bit_extender_2_out;

  assign bit_extender_1_out = {{16{1'b0}}, Imm};  // Bit_Extender bit_extender_1
  assign bit_extender_2_out = {{16{Imm[15]}}, Imm};  // Bit_Extender bit_extender_2
  Multiplexer #(.select(2), .width(32)) multiplexer_1 (
    .in0(bit_extender_1_out), .in1(bit_extender_2_out), .in2({Imm, {16{1'b0}}}), .out(EXTout), .sel(EXTop));  // open: in3, en
endmodule

module ALU (
  input  [31:0] A,
  input  [31:0] B,
  input  [1:0] ALUctr,
  output [31:0] C,
  output zero
);

  wire [31:0] adder_1_out, or_1_out, subtractor_1_out;

  Adder #(.width(32)) adder_1 (.a(A), .b(B), .out(adder_1_out));  // open: cin, cout
  Subtractor #(.width(32)) subtractor_1 (.a(A), .b(B), .out(subtractor_1_out));  // open: bin, bout
  assign or_1_out = A | B;  // OR_Gate or_1, 32 bits wide
  Comparator #(.width(32)) comparator_1 (.a(A), .b(B), .eq(zero));  // open: gt, lt
  Multiplexer #(.select(2), .width(32)) multiplexer_1 (
    .in0(adder_1_out), .in1(subtractor_1_out), .in2(or_1_out), .out(C), .sel(ALUctr));  // open: in3, en
endmodule

module DM (
  input  [4:0] Ad,
  input  [31:0] DIn,
  input  MemWrite,
  input  clk,
  input  reset,
  output [31:0] out_6
);

  RAM #(.addrWidth(5), .dataWidth(32), .bus("separate")) ram_1 (
    .addr(Ad), .din(DIn), .data(out_6), .str(MemWrite), .clk(clk), .clr(reset));  // open: sel, ld
endmodule

module CTRL (
  input  op5,
  input  op4,
  input  op3,
  input  op2,
  input  op1,
  input  op0,
  input  func5,
  input  func4,
  input  func3,
  input  func2,
  input  func1,
  input  func0,
  output RegDst,
  output AluSrc,
  output MemtoReg,
  output RegWrite,
  output MemWrite,
  output nPC_sel,
  output [1:0] ExtOp,
  output [1:0] ALUctr
);

  wire addu, and_1_out, nop, not_1_out, not_2_out, not_3_out, not_4_out, not_5_out, not_6_out, not_7_out,
       not_8_out, not_9_out, not_10_out, not_11_out, not_12_out, subu;

  not not_1 (not_1_out, op5);
  not not_2 (not_2_out, op3);
  not not_3 (not_3_out, op4);
  or or_1 (RegDst, addu, subu);
  not not_4 (not_4_out, op2);
  not not_5 (not_5_out, op1);
  or or_2 (AluSrc, ALUctr[1], MemtoReg, MemWrite, ExtOp[1]);
  not not_6 (not_6_out, op0);
  or or_3 (RegWrite, addu, subu, ALUctr[1], MemtoReg, ExtOp[1]);
  and and_1 (and_1_out, not_1_out, not_3_out, not_2_out, not_4_out, not_5_out, not_6_out);
  and ori (ALUctr[1], not_1_out, not_3_out, op3, op2, not_5_out, op0);
  and lw (MemtoReg, op5, not_3_out, not_2_out, not_4_out, op1, op0);
  and sw (MemWrite, op5, not_3_out, op3, not_4_out, op1, op0);
  and beq (nPC_sel, not_1_out, not_3_out, not_2_out, op2, not_5_out, not_6_out);
  and lui (ExtOp[1], not_1_out, not_3_out, op3, op2, op1, op0);
  not not_7 (not_7_out, func5);
  not not_8 (not_8_out, func4);
  or or_4 (ExtOp[0], MemtoReg, MemWrite);
  not not_9 (not_9_out, func2);
  not not_10 (not_10_out, func3);
  or or_5 (ALUctr[0], subu, nPC_sel);
  not not_11 (not_11_out, func1);
  not not_12 (not_12_out, func0);
  and u_addu (addu, func5, not_8_out, not_10_out, and_1_out, not_9_out, not_11_out, func0);
  and u_subu (subu, func5, not_8_out, not_10_out, and_1_out, not_9_out, func1, func0);
  and u_nop (nop, not_7_out, not_8_out, not_10_out, and_1_out, not_9_out, not_11_out, not_12_out);

  // Other names for the same wires on the sheet: ori = ALUctr[1]; beq = nPC_sel; lui = ExtOp[1]; lw = MemtoReg;
  //   sw = MemWrite
endmodule

module test (
  input  op_5,
  input  op_4,
  input  op_3,
  input  op_2,
  input  op_1,
  input  op_0,
  input  func_5,
  input  func_4,
  input  func_3,
  input  func_2,
  input  func_1,
  input  func_0,
  output RegDst,
  output AluSrc,
  output MemtoReg,
  output RegWrite,
  output MemWrite,
  output nPCsel,
  output ExtOp1,
  output ExtOp0,
  output ALUctr1,
  output ALUctr0
);


  assign AluSrc = 1'b1;
  assign MemtoReg = func_0;
  assign RegDst = 1'b0;
  assign RegWrite = 1'b1;
endmodule
