// Logisim project cccpu.circ as structural Verilog: 7 circuits, main circuit main
module main (
  input  reset,
  output [31:0] lnstr,
  output RegWrite,
  output [4:0] RegAddr,
  output [31:0] RegData,
  output MemWrite,
  output [4:0] MemAddr,
  output [31:0] MemData
);

  wire alu_1_zero, clock_1_out, controller_1_alusrc, controller_1_memtoreg, controller_1_npc_sel,
       controller_1_regdst;
  wire [1:0] controller_1_aluctr, controller_1_extop;
  wire [31:0] alu_1_aluout, dm_1_dataout, ext_1_extout, grf_1_busa, multiplexer_2_out;

  IFU ifu_1 (
    .npc_sel(controller_1_npc_sel), .zero(alu_1_zero), .in_3(lnstr[15:0]), .clk(clock_1_out), .clr(reset),
    .instr(lnstr));
  Multiplexer #(.width(5)) multiplexer_1 (
    .in0(lnstr[20:16]), .in1(lnstr[15:11]), .out(RegAddr), .sel(controller_1_regdst));  // open: en
  Clock clock_1 (.out(clock_1_out));
  GRF grf_1 (
    .rs(lnstr[25:21]), .rt(lnstr[20:16]), .rt_rd(RegAddr), .RegWrite(RegWrite), .busW(RegData),
    .clk(clock_1_out), .busA(grf_1_busa), .busB(MemData));
  Controller controller_1 (
    .op31_26(lnstr[31:26]), ._5_0(lnstr[5:0]), .RegDst(controller_1_regdst), .AluSrc(controller_1_alusrc),
    .MemtoReg(controller_1_memtoreg), .RegWrite(RegWrite), .MemWrite(MemWrite),
    .npc_sel(controller_1_npc_sel), .ExtOp(controller_1_extop), .ALUctr(controller_1_aluctr));
  EXT ext_1 (.imm(lnstr[15:0]), .EXTop(controller_1_extop), .EXTout(ext_1_extout));
  Multiplexer #(.width(32)) multiplexer_2 (
    .in0(MemData), .in1(ext_1_extout), .out(multiplexer_2_out), .sel(controller_1_alusrc));  // open: en
  ALU alu_1 (
    .busA(grf_1_busa), .busB(multiplexer_2_out), .ALUctr(controller_1_aluctr), .zero(alu_1_zero),
    .ALUout({alu_1_aluout[31:7], MemAddr, alu_1_aluout[1:0]}));
  DM dm_1 (
    .Addr(MemAddr), .Data__in(MemData), .MemWrite(MemWrite), .clk(clock_1_out), .reset(reset),
    .Dataout(dm_1_dataout));
  Multiplexer #(.width(32)) multiplexer_3 (
    .in0({alu_1_aluout[31:7], MemAddr, alu_1_aluout[1:0]}), .in1(dm_1_dataout), .out(RegData),
    .sel(controller_1_memtoreg));  // open: en
endmodule

module Controller (
  input  [5:0] op31_26,
  input  [5:0] _5_0,
  output RegDst,
  output AluSrc,
  output MemtoReg,
  output RegWrite,
  output MemWrite,
  output npc_sel,
  output [1:0] ExtOp,
  output [1:0] ALUctr
);

  wire addu, and_1_out, nop, not_1_out, not_2_out, not_3_out, not_4_out, not_5_out, not_6_out, not_7_out,
       not_8_out, not_9_out, not_10_out, not_11_out, not_12_out, subu;

  not not_1 (not_1_out, op31_26[5]);
  or u_RegDst (RegDst, addu, subu);
  not not_2 (not_2_out, op31_26[4]);
  not not_3 (not_3_out, op31_26[3]);
  or u_AluSrc (AluSrc, ALUctr[1], MemtoReg, MemWrite, ExtOp[1]);
  not not_4 (not_4_out, op31_26[2]);
  not not_5 (not_5_out, op31_26[0]);
  not not_6 (not_6_out, op31_26[1]);
  or u_RegWrite (RegWrite, addu, subu, ALUctr[1], MemtoReg, ExtOp[1]);
  and and_1 (and_1_out, not_1_out, not_2_out, not_3_out, not_4_out, not_6_out, not_5_out);
  and ori (ALUctr[1], not_1_out, not_2_out, op31_26[3], op31_26[2], not_6_out, op31_26[0]);
  and lw (MemtoReg, op31_26[5], not_2_out, not_3_out, not_4_out, op31_26[1], op31_26[0]);
  and sw (MemWrite, op31_26[5], not_2_out, op31_26[3], not_4_out, op31_26[1], op31_26[0]);
  and beq (npc_sel, not_1_out, not_2_out, not_3_out, op31_26[2], not_6_out, not_5_out);
  and lui (ExtOp[1], not_1_out, not_2_out, op31_26[3], op31_26[2], op31_26[1], op31_26[0]);
  or or_1 (ExtOp[0], MemtoReg, MemWrite);
  not not_7 (not_7_out, _5_0[5]);
  not not_8 (not_8_out, _5_0[3]);
  not not_9 (not_9_out, _5_0[4]);
  or or_2 (ALUctr[0], subu, npc_sel);
  not not_10 (not_10_out, _5_0[2]);
  not not_11 (not_11_out, _5_0[1]);
  not not_12 (not_12_out, _5_0[0]);
  and u_addu (addu, and_1_out, _5_0[5], not_9_out, not_8_out, not_10_out, not_11_out, _5_0[0]);
  and u_subu (subu, and_1_out, _5_0[5], not_9_out, not_8_out, not_10_out, _5_0[1], _5_0[0]);
  and u_nop (nop, and_1_out, not_7_out, not_9_out, not_8_out, not_10_out, not_11_out, not_12_out);

  // Other names for the same wires on the sheet: ori = ALUctr[1]; beq = npc_sel; lui = ExtOp[1]; lw = MemtoReg;
  //   sw = MemWrite
endmodule

module ALU (
  input  [31:0] busA,
  input  [31:0] busB,
  input  [1:0] ALUctr,
  output zero,
  output [31:0] ALUout
);

  wire [31:0] adder_1_out, or_1_out, subtractor_1_out;

  Comparator #(.width(32)) comparator_1 (.a(busB), .b(busA), .eq(zero));  // open: gt, lt
  Adder #(.width(32)) adder_1 (.a(busA), .b(busB), .out(adder_1_out));  // open: cin, cout
  Subtractor #(.width(32)) subtractor_1 (.a(busA), .b(busB), .out(subtractor_1_out));  // open: bin, bout
  assign or_1_out = busA | busB;  // OR_Gate or_1, 32 bits wide
  Multiplexer #(.select(2), .width(32)) multiplexer_1 (
    .in0(adder_1_out), .in1(subtractor_1_out), .in2(or_1_out), .out(ALUout), .sel(ALUctr));  // open: in3, en
endmodule

module EXT (
  input  [15:0] imm,
  input  [1:0] EXTop,
  output [31:0] EXTout
);

  wire [15:0] and_1_out, not_1_out;
  wire [31:0] bit_extender_1_out, bit_extender_2_out;

  assign not_1_out = ~imm;  // NOT_Gate not_1, 16 bits wide
  assign and_1_out = imm & not_1_out;  // AND_Gate and_1, 16 bits wide
  assign bit_extender_1_out = {{16{1'b0}}, imm};  // Bit_Extender bit_extender_1
  assign bit_extender_2_out = {{16{imm[15]}}, imm};  // Bit_Extender bit_extender_2
  Multiplexer #(.select(2), .width(32)) multiplexer_1 (
    .in0(bit_extender_1_out), .in1(bit_extender_2_out), .in2({imm, and_1_out}), .out(EXTout), .sel(EXTop));  // open: in3, en
endmodule

module IFU (
  input  npc_sel,
  input  zero,
  input  [15:0] in_3,
  input  clk,
  input  clr,
  output [31:0] instr
);

  wire and_1_out;
  wire [31:0] adder_1_out, adder_2_out, bit_extender_1_out, multiplexer_1_out, multiplier_1_out, PC_q;

  and and_1 (and_1_out, npc_sel, zero);
  assign bit_extender_1_out = {{16{in_3[15]}}, in_3};  // Bit_Extender bit_extender_1
  Adder #(.width(32)) adder_1 (.a(32'h4), .b(PC_q), .out(adder_1_out));  // open: cin, cout
  Multiplier #(.width(32)) multiplier_1 (.a(bit_extender_1_out), .b(32'h4), .out(multiplier_1_out));  // open: cin, cout
  Adder #(.width(32)) adder_2 (.a(adder_1_out), .b(multiplier_1_out), .out(adder_2_out));  // open: cin, cout
  Multiplexer #(.width(32)) multiplexer_1 (
    .in0(adder_1_out), .in1(adder_2_out), .out(multiplexer_1_out), .sel(and_1_out));  // open: en
  Register #(.width(32)) PC (.D(multiplexer_1_out), .Q(PC_q), .clk(clk), .clr(clr));  // open: en
  ROM #(.addrWidth(5), .dataWidth(32)) rom_1 (.addr(PC_q[6:2]), .data(instr));  // open: sel

  // Notes on the sheet:
  //   contents of rom_1 (hex, n*v repeats v):
  //   0 35090002 3c010000 34210001 1215023 3c0b000a ad890000 14a5021 112a0001 1294821 35690005 8d8b0004
endmodule

// 1
module GRF (
  input  [4:0] rs,
  input  [4:0] rt,
  input  [4:0] rt_rd,
  input  RegWrite,
  input  [31:0] busW,
  input  clk,
  output [31:0] busA,
  output [31:0] busB
);

  wire decoder_1_out0, decoder_1_out1, decoder_1_out2, decoder_1_out3, decoder_1_out4, decoder_1_out5,
       decoder_1_out6, decoder_1_out7, decoder_1_out8, decoder_1_out9, decoder_1_out10, decoder_1_out11,
       decoder_1_out12, decoder_1_out13, decoder_1_out14, decoder_1_out15, decoder_1_out16, decoder_1_out17,
       decoder_1_out18, decoder_1_out19, decoder_1_out20, decoder_1_out21, decoder_1_out22, decoder_1_out23,
       decoder_1_out24, decoder_1_out25, decoder_1_out26, decoder_1_out27, decoder_1_out28, decoder_1_out29,
       decoder_1_out30, decoder_1_out31, RegWrite0, RegWrite1, RegWrite2, RegWrite3, RegWrite4, RegWrite5,
       RegWrite6, RegWrite7, RegWrite8, RegWrite9, RegWrite10, RegWrite11, RegWrite12, RegWrite13,
       RegWrite14, RegWrite15, RegWrite16, RegWrite17, RegWrite18, RegWrite19, RegWrite20, RegWrite21,
       RegWrite22, RegWrite23, RegWrite24, RegWrite25, RegWrite26, RegWrite27, RegWrite28, RegWrite29,
       RegWrite30, RegWrite31;
  wire [31:0] _0, _0_minus, _1, _1_minus, _2, _2_minus, _3, _3_minus, _4, _4_minus, _5, _5_minus, _6,
       _6_minus, _7, _7_minus, _8, _8_minus, _9, _9_minus, _10, _10_minus, _11, _11_minus, _12, _12_minus,
       _13, _13_minus, _14, _14_minus, _15, _15_minus, _16, _16_minus, _17, _17_minus, _18, _18_minus, _19,
       _19_minus, _20, _20_minus, _21, _21_minus, _22, _22_minus, _23, _23_minus, _24, _24_minus, _25,
       _25_minus, _26, _26_minus, _27, _27_minus, _28, _28_minus, _29, _29_minus, _30, _30_minus, _31,
       _31_minus;

  Register #(.width(32)) register_1 (.D(_0_minus), .en(RegWrite0), .Q(_0), .clk(clk), .clr(1'b1));
  Register #(.width(32)) register_2 (.D(_8_minus), .en(RegWrite8), .Q(_8), .clk(clk));  // open: clr
  Register #(.width(32)) register_3 (.D(_16_minus), .en(RegWrite16), .Q(_16), .clk(clk));  // open: clr
  Register #(.width(32)) register_4 (.D(_24_minus), .en(RegWrite24), .Q(_24), .clk(clk));  // open: clr
  Register #(.width(32)) register_5 (.D(_1_minus), .en(RegWrite1), .Q(_1), .clk(clk));  // open: clr
  Register #(.width(32)) register_6 (.D(_9_minus), .en(RegWrite9), .Q(_9), .clk(clk));  // open: clr
  Register #(.width(32)) register_7 (.D(_17_minus), .en(RegWrite17), .Q(_17), .clk(clk));  // open: clr
  Register #(.width(32)) register_8 (.D(_25_minus), .en(RegWrite25), .Q(_25), .clk(clk));  // open: clr
  Multiplexer #(.select(5), .width(32)) multiplexer_1 (
    .in0(_0), .in1(_1), .in2(_2), .in3(_3), .in4(_4), .in5(_5), .in6(_6), .in7(_7), .in8(_8), .in9(_9),
    .in10(_10), .in11(_11), .in12(_12), .in13(_13), .in14(_14), .in15(_15), .in16(_16), .in17(_17),
    .in18(_18), .in19(_19), .in20(_20), .in21(_21), .in22(_22), .in23(_23), .in24(_24), .in25(_25),
    .in26(_26), .in27(_27), .in28(_28), .in29(_29), .in30(_30), .in31(_31), .out(busA), .sel(rs));  // open: en
  Register #(.width(32)) register_9 (.D(_2_minus), .en(RegWrite2), .Q(_2), .clk(clk));  // open: clr
  Register #(.width(32)) register_10 (.D(_10_minus), .en(RegWrite10), .Q(_10), .clk(clk));  // open: clr
  Register #(.width(32)) register_11 (.D(_18_minus), .en(RegWrite18), .Q(_18), .clk(clk));  // open: clr
  Register #(.width(32)) register_12 (.D(_26_minus), .en(RegWrite26), .Q(_26), .clk(clk));  // open: clr
  Register #(.width(32)) register_13 (.D(_3_minus), .en(RegWrite3), .Q(_3), .clk(clk));  // open: clr
  Register #(.width(32)) register_14 (.D(_11_minus), .en(RegWrite11), .Q(_11), .clk(clk));  // open: clr
  Register #(.width(32)) register_15 (.D(_19_minus), .en(RegWrite19), .Q(_19), .clk(clk));  // open: clr
  Register #(.width(32)) register_16 (.D(_27_minus), .en(RegWrite27), .Q(_27), .clk(clk));  // open: clr
  Multiplexer #(.select(5), .width(32)) multiplexer_2 (
    .in0(_0), .in1(_1), .in2(_2), .in3(_3), .in4(_4), .in5(_5), .in6(_6), .in7(_7), .in8(_8), .in9(_9),
    .in10(_10), .in11(_11), .in12(_12), .in13(_13), .in14(_14), .in15(_15), .in16(_16), .in17(_17),
    .in18(_18), .in19(_19), .in20(_20), .in21(_21), .in22(_22), .in23(_23), .in24(_24), .in25(_25),
    .in26(_26), .in27(_27), .in28(_28), .in29(_29), .in30(_30), .in31(_31), .out(busB), .sel(rt));  // open: en
  Register #(.width(32)) register_17 (.D(_4_minus), .en(RegWrite4), .Q(_4), .clk(clk));  // open: clr
  Register #(.width(32)) register_18 (.D(_12_minus), .en(RegWrite12), .Q(_12), .clk(clk));  // open: clr
  Register #(.width(32)) register_19 (.D(_20_minus), .en(RegWrite20), .Q(_20), .clk(clk));  // open: clr
  Register #(.width(32)) register_20 (.D(_28_minus), .en(RegWrite28), .Q(_28), .clk(clk));  // open: clr
  Demultiplexer #(.select(5), .width(32)) demultiplexer_1 (
    .out0(_0_minus), .out1(_1_minus), .out2(_2_minus), .out3(_3_minus), .out4(_4_minus), .out5(_5_minus),
    .out6(_6_minus), .out7(_7_minus), .out8(_8_minus), .out9(_9_minus), .out10(_10_minus), .out11(_11_minus),
    .out12(_12_minus), .out13(_13_minus), .out14(_14_minus), .out15(_15_minus), .out16(_16_minus),
    .out17(_17_minus), .out18(_18_minus), .out19(_19_minus), .out20(_20_minus), .out21(_21_minus),
    .out22(_22_minus), .out23(_23_minus), .out24(_24_minus), .out25(_25_minus), .out26(_26_minus),
    .out27(_27_minus), .out28(_28_minus), .out29(_29_minus), .out30(_30_minus), .out31(_31_minus), .in(busW),
    .sel(rt_rd));  // open: en
  Register #(.width(32)) register_21 (.D(_5_minus), .en(RegWrite5), .Q(_5), .clk(clk));  // open: clr
  Register #(.width(32)) register_22 (.D(_13_minus), .en(RegWrite13), .Q(_13), .clk(clk));  // open: clr
  Register #(.width(32)) register_23 (.D(_21_minus), .en(RegWrite21), .Q(_21), .clk(clk));  // open: clr
  Register #(.width(32)) register_24 (.D(_29_minus), .en(RegWrite29), .Q(_29), .clk(clk));  // open: clr
  Register #(.width(32)) register_25 (.D(_6_minus), .en(RegWrite6), .Q(_6), .clk(clk));  // open: clr
  Register #(.width(32)) register_26 (.D(_14_minus), .en(RegWrite14), .Q(_14), .clk(clk));  // open: clr
  Register #(.width(32)) register_27 (.D(_22_minus), .en(RegWrite22), .Q(_22), .clk(clk));  // open: clr
  Register #(.width(32)) register_28 (.D(_30_minus), .en(RegWrite30), .Q(_30), .clk(clk));  // open: clr
  Register #(.width(32)) register_29 (.D(_7_minus), .en(RegWrite7), .Q(_7), .clk(clk));  // open: clr
  Register #(.width(32)) register_30 (.D(_15_minus), .en(RegWrite15), .Q(_15), .clk(clk));  // open: clr
  Register #(.width(32)) register_31 (.D(_23_minus), .en(RegWrite23), .Q(_23), .clk(clk));  // open: clr
  Register #(.width(32)) register_32 (.D(_31_minus), .en(RegWrite31), .Q(_31), .clk(clk));  // open: clr
  Decoder #(.select(5)) decoder_1 (
    .out0(decoder_1_out0), .out1(decoder_1_out1), .out2(decoder_1_out2), .out3(decoder_1_out3),
    .out4(decoder_1_out4), .out5(decoder_1_out5), .out6(decoder_1_out6), .out7(decoder_1_out7),
    .out8(decoder_1_out8), .out9(decoder_1_out9), .out10(decoder_1_out10), .out11(decoder_1_out11),
    .out12(decoder_1_out12), .out13(decoder_1_out13), .out14(decoder_1_out14), .out15(decoder_1_out15),
    .out16(decoder_1_out16), .out17(decoder_1_out17), .out18(decoder_1_out18), .out19(decoder_1_out19),
    .out20(decoder_1_out20), .out21(decoder_1_out21), .out22(decoder_1_out22), .out23(decoder_1_out23),
    .out24(decoder_1_out24), .out25(decoder_1_out25), .out26(decoder_1_out26), .out27(decoder_1_out27),
    .out28(decoder_1_out28), .out29(decoder_1_out29), .out30(decoder_1_out30), .out31(decoder_1_out31),
    .sel(rt_rd));  // open: en
  and and_1 (RegWrite0, decoder_1_out0, RegWrite);
  and and_2 (RegWrite1, decoder_1_out1, RegWrite);
  and and_3 (RegWrite2, decoder_1_out2, RegWrite);
  and and_4 (RegWrite3, decoder_1_out3, RegWrite);
  and and_5 (RegWrite4, decoder_1_out4, RegWrite);
  and and_6 (RegWrite5, decoder_1_out5, RegWrite);
  and and_7 (RegWrite6, decoder_1_out6, RegWrite);
  and and_8 (RegWrite7, decoder_1_out7, RegWrite);
  and and_9 (RegWrite8, decoder_1_out8, RegWrite);
  and and_10 (RegWrite9, decoder_1_out9, RegWrite);
  and and_11 (RegWrite10, decoder_1_out10, RegWrite);
  and and_12 (RegWrite11, decoder_1_out11, RegWrite);
  and and_13 (RegWrite12, decoder_1_out12, RegWrite);
  and and_14 (RegWrite13, decoder_1_out13, RegWrite);
  and and_15 (RegWrite14, decoder_1_out14, RegWrite);
  and and_16 (RegWrite15, decoder_1_out15, RegWrite);
  and and_17 (RegWrite16, decoder_1_out16, RegWrite);
  and and_18 (RegWrite17, decoder_1_out17, RegWrite);
  and and_19 (RegWrite18, decoder_1_out18, RegWrite);
  and and_20 (RegWrite19, decoder_1_out19, RegWrite);
  and and_21 (RegWrite20, decoder_1_out20, RegWrite);
  and and_22 (RegWrite21, decoder_1_out21, RegWrite);
  and and_23 (RegWrite22, decoder_1_out22, RegWrite);
  and and_24 (RegWrite23, decoder_1_out23, RegWrite);
  and and_25 (RegWrite24, decoder_1_out24, RegWrite);
  and and_26 (RegWrite25, decoder_1_out25, RegWrite);
  and and_27 (RegWrite26, decoder_1_out26, RegWrite);
  and and_28 (RegWrite27, decoder_1_out27, RegWrite);
  and and_29 (RegWrite28, decoder_1_out28, RegWrite);
  and and_30 (RegWrite29, decoder_1_out29, RegWrite);
  and and_31 (RegWrite30, decoder_1_out30, RegWrite);
  and and_32 (RegWrite31, decoder_1_out31, RegWrite);

  // Other names for the same wires on the sheet: busA_rs[31:0] = busA; busB_rt[31:0] = busB; rs_rt[4:0] = rt_rd
endmodule

module DM (
  input  [4:0] Addr,
  input  [31:0] Data__in,
  input  MemWrite,
  input  clk,
  input  reset,
  output [31:0] Dataout
);

  RAM #(.addrWidth(5), .dataWidth(32), .bus("separate")) ram_1 (
    .addr(Addr), .din(Data__in), .data(Dataout), .str(MemWrite), .clk(clk), .clr(reset));  // open: sel, ld
endmodule
