// Logisim project Logisim_fibonacci2.circ as structural Verilog: 3 circuits, main circuit main
module main (
  input  [31:0] INPUT,
  output [31:0] OUTPUT
);

  wire CLK, comparator_1_eq, comparator_2_eq, comparator_3_gt, comparator_4_gt, counter_1_q, counter_2_q,
       ENABLE, JUDGE_judge;
  wire [31:0] A, A1, B, B1, C, C1, D, D1, JUDGE_currentinput, multiplexer_1_out, multiplexer_2_out,
       multiplexer_3_out, multiplexer_4_out, R1, R2, R3, R4, R11, R22, R33, R44, register_1_q, register_2_q,
       register_3_q, register_4_q, register_5_q, register_6_q, register_7_q, register_8_q;

  Clock clock_1 (.out(CLK));
  Register #(.width(32)) register_1 (.D(A1), .en(ENABLE), .Q(register_1_q), .clk(CLK));  // open: clr
  Register #(.width(32)) register_2 (.D(B1), .en(ENABLE), .Q(register_2_q), .clk(CLK));  // open: clr
  Register #(.width(32)) register_3 (.D(C1), .en(ENABLE), .Q(register_3_q), .clk(CLK));  // open: clr
  Register #(.width(32)) register_4 (.D(D1), .en(ENABLE), .Q(register_4_q), .clk(CLK));  // open: clr
  judge JUDGE (.\input (INPUT), .CLK(CLK), .judge(JUDGE_judge), .CURRENTINPUT(JUDGE_currentinput));
  Counter #(.width(1), .max('h1), .ongoal("stay")) counter_1 (
    .Q(counter_1_q), .clk(CLK));  // open: load, D, count, carry, clr
  Comparator #(.width(1), .mode("unsigned")) comparator_1 (
    .a(JUDGE_judge), .b(1'b1), .eq(comparator_1_eq));  // open: gt, lt
  Comparator #(.width(32), .mode("unsigned")) comparator_2 (
    .a(JUDGE_currentinput), .b({32{1'b0}}), .eq(comparator_2_eq));  // open: gt, lt
  Comparator #(.width(1), .mode("unsigned")) comparator_3 (
    .a(1'b1), .b(counter_1_q), .gt(comparator_3_gt));  // open: eq, lt
  Multiplexer #(.width(32)) multiplexer_1 (
    .in0(32'h1), .in1(A), .out(multiplexer_1_out), .sel(comparator_1_eq));  // open: en
  Multiplexer #(.width(32)) multiplexer_2 (
    .in0({32{1'b0}}), .in1(B), .out(multiplexer_2_out), .sel(comparator_1_eq));  // open: en
  Multiplexer #(.width(32)) multiplexer_3 (
    .in0({32{1'b0}}), .in1(C), .out(multiplexer_3_out), .sel(comparator_1_eq));  // open: en
  Multiplexer #(.width(32)) multiplexer_4 (
    .in0(32'h1), .in1(D), .out(multiplexer_4_out), .sel(comparator_1_eq));  // open: en
  not not_1 (ENABLE, comparator_2_eq);
  Multiplexer #(.width(32)) multiplexer_5 (
    .in0(register_1_q), .in1(32'h1), .out(A), .sel(comparator_3_gt));  // open: en
  Multiplexer #(.width(32)) multiplexer_6 (
    .in0(register_2_q), .in1(32'h1), .out(B), .sel(comparator_3_gt));  // open: en
  Multiplexer #(.width(32)) multiplexer_7 (
    .in0(register_3_q), .in1(32'h1), .out(C), .sel(comparator_3_gt));  // open: en
  Multiplexer #(.width(32)) multiplexer_8 (
    .in0(register_4_q), .in1({32{1'b0}}), .out(D), .sel(comparator_3_gt));  // open: en
  \矩阵乘积  mult (
    .A(multiplexer_1_out), .B(multiplexer_2_out), .C(multiplexer_3_out), .D(multiplexer_4_out), .E(R1),
    .F(R2), .G(R3), .H(R4), .out_9(R11), .out_10(R22), .out_11(R33), .out_12(R44));
  // Probe on R3
  Multiplexer #(.width(32)) multiplexer_9 (.in0(R3), .in1({32{1'b0}}), .out(OUTPUT), .sel(ENABLE));  // open: en
  Register #(.width(32)) register_5 (.D(R11), .en(ENABLE), .Q(register_5_q), .clk(CLK));  // open: clr
  Register #(.width(32)) register_6 (.D(R22), .en(ENABLE), .Q(register_6_q), .clk(CLK));  // open: clr
  Register #(.width(32)) register_7 (.D(R33), .en(ENABLE), .Q(register_7_q), .clk(CLK));  // open: clr
  Register #(.width(32)) register_8 (.D(R44), .en(ENABLE), .Q(register_8_q), .clk(CLK));  // open: clr
  Counter #(.width(1), .max('h1), .ongoal("stay")) counter_2 (
    .Q(counter_2_q), .clk(CLK));  // open: load, D, count, carry, clr
  Comparator #(.width(1), .mode("unsigned")) comparator_4 (
    .a(1'b1), .b(counter_2_q), .gt(comparator_4_gt));  // open: eq, lt
  Multiplexer #(.width(32)) multiplexer_10 (
    .in0(register_5_q), .in1(32'h1), .out(R1), .sel(comparator_4_gt));  // open: en
  Multiplexer #(.width(32)) multiplexer_11 (
    .in0(register_6_q), .in1({32{1'b0}}), .out(R2), .sel(comparator_4_gt));  // open: en
  Multiplexer #(.width(32)) multiplexer_12 (
    .in0(register_7_q), .in1({32{1'b0}}), .out(R3), .sel(comparator_4_gt));  // open: en
  Multiplexer #(.width(32)) multiplexer_13 (
    .in0(register_8_q), .in1(32'h1), .out(R4), .sel(comparator_4_gt));  // open: en
  \矩阵乘积  mult_2 (
    .A(A), .B(B), .C(C), .D(D), .E(A), .F(B), .G(C), .H(D), .out_9(A1), .out_10(B1), .out_11(C1), .out_12(D1));

  // Notes on the sheet:
  //   R矩阵模块，A矩阵模块和input模块都是在第一个周期完成初始化并进行第一次运算
  //   退出条件为currentinput为零
endmodule

module \矩阵乘积  (
  input  [31:0] A,
  input  [31:0] B,
  input  [31:0] C,
  input  [31:0] D,
  input  [31:0] E,
  input  [31:0] F,
  input  [31:0] G,
  input  [31:0] H,
  output [31:0] out_9,
  output [31:0] out_10,
  output [31:0] out_11,
  output [31:0] out_12
);

  wire [31:0] multiplier_1_out, multiplier_2_out, multiplier_3_out, multiplier_4_out, multiplier_5_out,
       multiplier_6_out, multiplier_7_out, multiplier_8_out;

  Multiplier #(.width(32)) multiplier_1 (.a(A), .b(E), .out(multiplier_1_out));  // open: cin, cout
  Multiplier #(.width(32)) multiplier_2 (.a(B), .b(G), .out(multiplier_2_out));  // open: cin, cout
  Multiplier #(.width(32)) multiplier_3 (.a(A), .b(F), .out(multiplier_3_out));  // open: cin, cout
  Multiplier #(.width(32)) multiplier_4 (.a(B), .b(H), .out(multiplier_4_out));  // open: cin, cout
  Multiplier #(.width(32)) multiplier_5 (.a(C), .b(E), .out(multiplier_5_out));  // open: cin, cout
  Multiplier #(.width(32)) multiplier_6 (.a(D), .b(G), .out(multiplier_6_out));  // open: cin, cout
  Multiplier #(.width(32)) multiplier_7 (.a(C), .b(F), .out(multiplier_7_out));  // open: cin, cout
  Multiplier #(.width(32)) multiplier_8 (.a(D), .b(H), .out(multiplier_8_out));  // open: cin, cout
  Adder #(.width(32)) adder_1 (.a(multiplier_1_out), .b(multiplier_2_out), .out(out_9));  // open: cin, cout
  Adder #(.width(32)) adder_2 (.a(multiplier_3_out), .b(multiplier_4_out), .out(out_10));  // open: cin, cout
  Adder #(.width(32)) adder_3 (.a(multiplier_5_out), .b(multiplier_6_out), .out(out_11));  // open: cin, cout
  Adder #(.width(32)) adder_4 (.a(multiplier_7_out), .b(multiplier_8_out), .out(out_12));  // open: cin, cout
endmodule

module judge (
  input  [31:0] \input ,
  input  CLK,
  output judge,
  output [31:0] CURRENTINPUT
);

  wire comparator_2_lt, counter_1_q;
  wire [31:0] register_1_q, shifter_1_out;

  Shifter #(.width(32), .shift("lr")) shifter_1 (.in(CURRENTINPUT), .\dist (5'b00001), .out(shifter_1_out));
  Counter #(.width(1), .max('h1), .ongoal("stay")) counter_1 (
    .Q(counter_1_q), .clk(CLK));  // open: load, D, count, carry, clr
  Comparator #(.width(1)) comparator_1 (.a(CURRENTINPUT[0]), .b(1'b1), .eq(judge));  // open: gt, lt
  Comparator #(.width(1), .mode("unsigned")) comparator_2 (
    .a(counter_1_q), .b(1'b1), .lt(comparator_2_lt));  // open: gt, eq
  Register #(.width(32)) register_1 (.D(shifter_1_out), .Q(register_1_q), .clk(CLK));  // open: en, clr
  Multiplexer #(.width(32)) multiplexer_1 (
    .in0(register_1_q), .in1(\input ), .out(CURRENTINPUT), .sel(comparator_2_lt));  // open: en

  // Other names for the same wires on the sheet: input_t[31:0] = CURRENTINPUT
endmodule
