// Logisim project gu fib challenge new.circ as structural Verilog: 4 circuits, main circuit main
module main (
  input  [31:0] \input ,
  output [31:0] \output 
);

  wire clk, cnt, get_bit_out_bit, halt_flag;
  wire [31:0] get_fib_matrix_fib00, get_fib_matrix_fib01, get_fib_matrix_fib10, get_fib_matrix_fib11,
       matrix_multiplyer_1_c1, matrix_multiplyer_1_c2, matrix_multiplyer_1_c3, matrix_multiplyer_1_c4,
       multiplexer_1_out, multiplexer_2_out, multiplexer_3_out, multiplexer_4_out, multiplexer_5_out,
       multiplexer_6_out, multiplexer_7_out, multiplexer_8_out, register_1_q, register_2_q, register_3_q,
       register_4_q;

  Clock clock_1 (.out(clk));
  Counter #(.width(1), .max('h1), .ongoal("stay")) counter_1 (.Q(cnt), .clk(clk));  // open: load, D, count, carry, clr
  get_bit get_bit (.\input (\input ), .halt_flag(halt_flag), .out_bit(get_bit_out_bit));
  get_fib_matrix get_fib_matrix (
    .sel(get_bit_out_bit), .fib00(get_fib_matrix_fib00), .fib01(get_fib_matrix_fib01),
    .fib10(get_fib_matrix_fib10), .fib11(get_fib_matrix_fib11));
  Multiplexer #(.width(32)) multiplexer_1 (
    .in0(get_fib_matrix_fib00), .in1(32'h1), .out(multiplexer_1_out), .sel(halt_flag));  // open: en
  Multiplexer #(.width(32)) multiplexer_2 (
    .in0(get_fib_matrix_fib01), .in1({32{1'b0}}), .out(multiplexer_2_out), .sel(halt_flag));  // open: en
  Multiplexer #(.width(32)) multiplexer_3 (
    .in0(get_fib_matrix_fib10), .in1({32{1'b0}}), .out(multiplexer_3_out), .sel(halt_flag));  // open: en
  Multiplexer #(.width(32)) multiplexer_4 (
    .in0(get_fib_matrix_fib11), .in1(32'h1), .out(multiplexer_4_out), .sel(halt_flag));  // open: en
  matrix_multiplyer matrix_multiplyer_1 (
    .a1(multiplexer_1_out), .a2(multiplexer_2_out), .a3(multiplexer_3_out), .a4(multiplexer_4_out),
    .b1(multiplexer_5_out), .b2(multiplexer_6_out), .b3(multiplexer_7_out), .b4(multiplexer_8_out),
    .c1(matrix_multiplyer_1_c1), .c2(matrix_multiplyer_1_c2), .c3(matrix_multiplyer_1_c3),
    .c4(matrix_multiplyer_1_c4));
  Register #(.width(32)) register_1 (.D(matrix_multiplyer_1_c1), .Q(register_1_q), .clk(clk));  // open: en, clr
  Register #(.width(32)) register_2 (.D(matrix_multiplyer_1_c2), .Q(register_2_q), .clk(clk));  // open: en, clr
  Register #(.width(32)) register_3 (.D(matrix_multiplyer_1_c3), .Q(register_3_q), .clk(clk));  // open: en, clr
  Register #(.width(32)) register_4 (.D(matrix_multiplyer_1_c4), .Q(register_4_q), .clk(clk));  // open: en, clr
  Multiplexer #(.width(32)) multiplexer_5 (
    .in0(32'h1), .in1(register_1_q), .out(multiplexer_5_out), .sel(cnt));  // open: en
  Multiplexer #(.width(32)) multiplexer_6 (
    .in0({32{1'b0}}), .in1(register_2_q), .out(multiplexer_6_out), .sel(cnt));  // open: en
  Multiplexer #(.width(32)) multiplexer_7 (
    .in0({32{1'b0}}), .in1(register_3_q), .out(multiplexer_7_out), .sel(cnt));  // open: en
  Multiplexer #(.width(32)) multiplexer_8 (
    .in0(32'h1), .in1(register_4_q), .out(multiplexer_8_out), .sel(cnt));  // open: en
  Multiplexer #(.width(32)) multiplexer_9 (
    .in0({32{1'b0}}), .in1(multiplexer_7_out), .out(\output ), .sel(halt_flag));  // open: en
  // Probe on multiplexer_7_out
endmodule

module matrix_multiplyer (
  input  [31:0] a1,
  input  [31:0] a2,
  input  [31:0] a3,
  input  [31:0] a4,
  input  [31:0] b1,
  input  [31:0] b2,
  input  [31:0] b3,
  input  [31:0] b4,
  output [31:0] c1,
  output [31:0] c2,
  output [31:0] c3,
  output [31:0] c4
);

  wire [31:0] multiplier_1_cout, multiplier_1_out, multiplier_2_out, multiplier_3_cout, multiplier_3_out,
       multiplier_4_out, multiplier_5_cout, multiplier_5_out, multiplier_6_out, multiplier_7_cout,
       multiplier_7_out, multiplier_8_out;

  Multiplier #(.width(32)) multiplier_1 (
    .a(a1), .b(b1), .out(multiplier_1_out), .cout(multiplier_1_cout));  // open: cin
  Multiplier #(.width(32)) multiplier_2 (
    .a(a2), .b(b3), .out(multiplier_2_out), .cin(multiplier_1_cout));  // open: cout
  Multiplier #(.width(32)) multiplier_3 (
    .a(a1), .b(b2), .out(multiplier_3_out), .cout(multiplier_3_cout));  // open: cin
  Multiplier #(.width(32)) multiplier_4 (
    .a(a2), .b(b4), .out(multiplier_4_out), .cin(multiplier_3_cout));  // open: cout
  Multiplier #(.width(32)) multiplier_5 (
    .a(a3), .b(b1), .out(multiplier_5_out), .cout(multiplier_5_cout));  // open: cin
  Multiplier #(.width(32)) multiplier_6 (
    .a(a4), .b(b3), .out(multiplier_6_out), .cin(multiplier_5_cout));  // open: cout
  Multiplier #(.width(32)) multiplier_7 (
    .a(a3), .b(b2), .out(multiplier_7_out), .cout(multiplier_7_cout));  // open: cin
  Multiplier #(.width(32)) multiplier_8 (
    .a(a4), .b(b4), .out(multiplier_8_out), .cin(multiplier_7_cout));  // open: cout
  Adder #(.width(32)) adder_1 (.a(multiplier_1_out), .b(multiplier_2_out), .out(c1));  // open: cin, cout
  Adder #(.width(32)) adder_2 (.a(multiplier_3_out), .b(multiplier_4_out), .out(c2));  // open: cin, cout
  Adder #(.width(32)) adder_3 (.a(multiplier_5_out), .b(multiplier_6_out), .out(c3));  // open: cin, cout
  Adder #(.width(32)) adder_4 (.a(multiplier_7_out), .b(multiplier_8_out), .out(c4));  // open: cin, cout
endmodule

module get_bit (
  input  [31:0] \input ,
  output halt_flag,
  output out_bit
);

  wire clk, counter_2_q;
  wire [7:0] counter_1_q;
  wire [31:0] multiplexer_1_out, register_1_q, shifter_1_out;
  wire [31:1] and_1_out;

  Counter #(.ongoal("stay")) counter_1 (.Q(counter_1_q), .clk(clk));  // open: load, D, count, carry, clr
  Multiplexer #(.width(32)) multiplexer_1 (
    .in0(\input ), .in1(register_1_q), .out(multiplexer_1_out), .sel(counter_2_q));  // open: en
  Counter #(.width(1), .max('h1), .ongoal("stay")) counter_2 (
    .Q(counter_2_q), .clk(clk));  // open: load, D, count, carry, clr
  Clock clock_1 (.out(clk));
  Shifter #(.width(32), .shift("lr")) shifter_1 (.in(multiplexer_1_out), .\dist (5'b00001), .out(shifter_1_out));
  Comparator comparator_1 (.a(8'h1f), .b(counter_1_q), .lt(halt_flag));  // open: gt, eq
  assign {and_1_out, out_bit} = multiplexer_1_out & 32'h1;  // AND_Gate and_1, 32 bits wide
  Register #(.width(32)) register_1 (.D(shifter_1_out), .Q(register_1_q), .clk(clk));  // open: en, clr
endmodule

module get_fib_matrix (
  input  sel,
  output [31:0] fib00,
  output [31:0] fib01,
  output [31:0] fib10,
  output [31:0] fib11
);

  wire clk, cnt;
  wire [31:0] matrix_multiplyer_1_c1, matrix_multiplyer_1_c2, matrix_multiplyer_1_c3, matrix_multiplyer_1_c4,
       multiplexer_1_out, multiplexer_2_out, multiplexer_3_out, multiplexer_4_out, multiplexer_5_out,
       multiplexer_6_out, multiplexer_7_out, multiplexer_8_out, register_1_q, register_2_q, register_3_q,
       register_4_q;

  Clock clock_1 (.out(clk));
  Multiplexer #(.width(32)) multiplexer_1 (
    .in0(32'h1), .in1(multiplexer_5_out), .out(multiplexer_1_out), .sel(cnt));  // open: en
  Multiplexer #(.width(32)) multiplexer_2 (
    .in0(32'h1), .in1(multiplexer_6_out), .out(multiplexer_2_out), .sel(cnt));  // open: en
  Multiplexer #(.width(32)) multiplexer_3 (
    .in0(32'h1), .in1(multiplexer_7_out), .out(multiplexer_3_out), .sel(cnt));  // open: en
  Multiplexer #(.width(32)) multiplexer_4 (
    .in0({32{1'b0}}), .in1(multiplexer_8_out), .out(multiplexer_4_out), .sel(cnt));  // open: en
  Counter #(.width(1), .max('h1), .ongoal("stay")) counter_1 (.Q(cnt), .clk(clk));  // open: load, D, count, carry, clr
  matrix_multiplyer matrix_multiplyer_1 (
    .a1(multiplexer_1_out), .a2(multiplexer_2_out), .a3(multiplexer_3_out), .a4(multiplexer_4_out),
    .b1(multiplexer_5_out), .b2(multiplexer_6_out), .b3(multiplexer_7_out), .b4(multiplexer_8_out),
    .c1(matrix_multiplyer_1_c1), .c2(matrix_multiplyer_1_c2), .c3(matrix_multiplyer_1_c3),
    .c4(matrix_multiplyer_1_c4));
  Register #(.width(32)) register_1 (.D(matrix_multiplyer_1_c1), .Q(register_1_q), .clk(clk));  // open: en, clr
  Register #(.width(32)) register_2 (.D(matrix_multiplyer_1_c2), .Q(register_2_q), .clk(clk));  // open: en, clr
  Register #(.width(32)) register_3 (.D(matrix_multiplyer_1_c3), .Q(register_3_q), .clk(clk));  // open: en, clr
  Register #(.width(32)) register_4 (.D(matrix_multiplyer_1_c4), .Q(register_4_q), .clk(clk));  // open: en, clr
  Multiplexer #(.width(32)) multiplexer_5 (
    .in0(multiplexer_1_out), .in1(register_1_q), .out(multiplexer_5_out), .sel(cnt));  // open: en
  Multiplexer #(.width(32)) multiplexer_6 (
    .in0(multiplexer_1_out), .in1(register_2_q), .out(multiplexer_6_out), .sel(cnt));  // open: en
  Multiplexer #(.width(32)) multiplexer_7 (
    .in0(multiplexer_1_out), .in1(register_3_q), .out(multiplexer_7_out), .sel(cnt));  // open: en
  Multiplexer #(.width(32)) multiplexer_8 (
    .in0(multiplexer_4_out), .in1(register_4_q), .out(multiplexer_8_out), .sel(cnt));  // open: en
  Multiplexer #(.width(32)) multiplexer_9 (.in0(32'h1), .in1(multiplexer_5_out), .out(fib00), .sel(sel));  // open: en
  Multiplexer #(.width(32)) multiplexer_10 (
    .in0({32{1'b0}}), .in1(multiplexer_6_out), .out(fib01), .sel(sel));  // open: en
  Multiplexer #(.width(32)) multiplexer_11 (
    .in0({32{1'b0}}), .in1(multiplexer_7_out), .out(fib10), .sel(sel));  // open: en
  Multiplexer #(.width(32)) multiplexer_12 (.in0(32'h1), .in1(multiplexer_8_out), .out(fib11), .sel(sel));  // open: en
endmodule
