// Logisim project register.circ as structural Verilog
module \第一个周期开始前就完成初始化  (
  input  init,
  input  \input ,
  input  enable,
  input  CLK,
  output \output 
);

  wire counter_1_q, register_1_q;

  Register #(.width(1)) register_1 (.D(\input ), .en(enable), .Q(register_1_q), .clk(CLK));  // open: clr
  Multiplexer multiplexer_1 (.in0(init), .in1(register_1_q), .out(\output ), .sel(counter_1_q));  // open: en
  Counter #(.width(1), .max('h1), .ongoal("stay")) counter_1 (
    .Q(counter_1_q), .clk(CLK));  // open: load, D, count, carry, clr
endmodule

module \牺牲第一个周期进行初始化  (
  input  init,
  input  \input ,
  input  enable,
  input  CLK,
  output \output 
);

  wire counter_1_q, multiplexer_1_out;

  Counter #(.width(1), .max('h1), .ongoal("stay")) counter_1 (
    .Q(counter_1_q), .clk(CLK));  // open: load, D, count, carry, clr
  Multiplexer multiplexer_1 (.in0(init), .in1(\input ), .out(multiplexer_1_out), .sel(counter_1_q));  // open: en
  Register #(.width(1)) register_1 (.D(multiplexer_1_out), .en(enable), .Q(\output ), .clk(CLK));  // open: clr
endmodule
