// Logisim project Logisim_4BitSort.circ as structural Verilog: 5 circuits, main circuit 1bit_swap
module _1bit_swap (
  input  in1,
  input  in2,
  input  sort,
  output out1,
  output out2
);

  wire and_1_out, and_2_out, and_3_out, and_4_out, not_1_out, not_2_out;

  not not_1 (not_1_out, sort);
  not not_2 (not_2_out, sort);
  and and_1 (and_1_out, in2, sort);
  and and_2 (and_2_out, in1, not_1_out);
  and and_3 (and_3_out, in2, not_2_out);
  and and_4 (and_4_out, in1, sort);
  or or_1 (out1, and_1_out, and_2_out);
  or or_2 (out2, and_3_out, and_4_out);
endmodule

module _4bit_swap (
  input  [3:0] IN1,
  input  [3:0] IN2,
  input  in_3,
  output [3:0] out_4,
  output [3:0] out_5
);

  _1bit_swap _1bit_swap1 (.in1(IN1[0]), .in2(IN2[0]), .sort(in_3), .out1(out_4[0]), .out2(out_5[0]));
  _1bit_swap _1bit_swap2 (.in1(IN1[1]), .in2(IN2[1]), .sort(in_3), .out1(out_4[1]), .out2(out_5[1]));
  _1bit_swap _1bit_swap3 (.in1(IN1[2]), .in2(IN2[2]), .sort(in_3), .out1(out_4[2]), .out2(out_5[2]));
  _1bit_swap _1bit_swap4 (.in1(IN1[3]), .in2(IN2[3]), .sort(in_3), .out1(out_4[3]), .out2(out_5[3]));
endmodule

module _4bit_sort (
  input  [3:0] A,
  input  [3:0] B,
  input  [3:0] C,
  input  [3:0] D,
  output [3:0] _1,
  output [3:0] _2,
  output [3:0] _3,
  output [3:0] _4
);

  wire [3:0] anotherlargeris_1_out_3, anotherlargeris_1_out_4, anotherlargeris_2_out_3,
       anotherlargeris_2_out_4, anotherlargeris_3_out_3, anotherlargeris_3_out_4, anotherlargeris_4_out_4,
       anotherlargeris_5_out_4;

  anotherlargeris anotherlargeris_1 (
    .in_1(A), .in_2(B), .out_3(anotherlargeris_1_out_3), .out_4(anotherlargeris_1_out_4));
  anotherlargeris anotherlargeris_2 (
    .in_1(anotherlargeris_1_out_3), .in_2(C), .out_3(anotherlargeris_2_out_3), .out_4(anotherlargeris_2_out_4));
  anotherlargeris anotherlargeris_3 (
    .in_1(anotherlargeris_2_out_4), .in_2(anotherlargeris_1_out_4), .out_3(anotherlargeris_3_out_3),
    .out_4(anotherlargeris_3_out_4));
  anotherlargeris anotherlargeris_4 (
    .in_1(anotherlargeris_2_out_3), .in_2(D), .out_3(_4), .out_4(anotherlargeris_4_out_4));
  anotherlargeris anotherlargeris_5 (
    .in_1(anotherlargeris_4_out_4), .in_2(anotherlargeris_3_out_3), .out_3(_3),
    .out_4(anotherlargeris_5_out_4));
  anotherlargeris anotherlargeris_6 (
    .in_1(anotherlargeris_5_out_4), .in_2(anotherlargeris_3_out_4), .out_3(_2), .out_4(_1));
endmodule

module largeris (
  input  [3:0] in_1,
  input  [3:0] in_2,
  output [3:0] out_3,
  output [3:0] out_4
);

  wire comparator_1_lt;

  Comparator #(.width(5)) comparator_1 (.a({1'b0, in_1}), .b({1'b0, in_2}), .lt(comparator_1_lt));  // open: gt, eq
  _4bit_swap u_4bit_swap_1 (.IN1(in_1), .IN2(in_2), .in_3(comparator_1_lt), .out_4(out_3), .out_5(out_4));

  // Notes on the sheet:
  //   向每个数字前面都加上一个零，变成正数之后比较
endmodule

module anotherlargeris (
  input  [3:0] in_1,
  input  [3:0] in_2,
  output [3:0] out_3,
  output [3:0] out_4
);

  wire comparator_1_lt;
  wire [4:0] bit_extender_1_out, bit_extender_2_out;

  assign bit_extender_1_out = {{1{1'b0}}, in_1};  // Bit_Extender bit_extender_1
  assign bit_extender_2_out = {{1{1'b0}}, in_2};  // Bit_Extender bit_extender_2
  Comparator #(.width(5)) comparator_1 (
    .a(bit_extender_1_out), .b(bit_extender_2_out), .lt(comparator_1_lt));  // open: gt, eq
  _4bit_swap u_4bit_swap_1 (.IN1(in_1), .IN2(in_2), .in_3(comparator_1_lt), .out_4(out_3), .out_5(out_4));
endmodule
