// Logisim project Logisim_fibonacci another.circ as structural Verilog: 3 circuits, main circuit main
module main (
  input  [2:0] \input ,
  output [3:0] out_2
);

  wire clock_1_out, \计数逻辑_end ;
  wire [3:0] \计算逻辑_out_3 ;

  count1 \u_计数逻辑  (.\input (\input ), .in_2(clock_1_out), .\end (\计数逻辑_end ));
  Clock clock_1 (.out(clock_1_out));
  calculate1 \u_计算逻辑  (.\end (\计数逻辑_end ), .CLK(clock_1_out), .out_3(\计算逻辑_out_3 ));
  Multiplexer #(.width(4)) multiplexer_1 (
    .in0(4'b0000), .in1(\计算逻辑_out_3 ), .out(out_2), .sel(\计数逻辑_end ));  // open: en
endmodule

module calculate1 (
  input  \end ,
  input  CLK,
  output [3:0] out_3
);

  wire counter_1_q, enable;
  wire [3:0] adder_1_out, multiplexer_1_out, prev;

  Counter #(.width(1), .max('h1), .ongoal("stay")) counter_1 (
    .Q(counter_1_q), .clk(CLK));  // open: load, D, count, carry, clr
  Multiplexer #(.width(4)) multiplexer_1 (
    .in0(4'b0001), .in1(out_3), .out(multiplexer_1_out), .sel(counter_1_q));  // open: en
  not not_1 (enable, \end );
  Register #(.width(4)) register_1 (.D(out_3), .en(enable), .Q(prev), .clk(CLK));  // open: clr
  // Probe on prev
  // Probe on multiplexer_1_out
  // Probe on adder_1_out
  Adder #(.width(4)) adder_1 (.a(prev), .b(multiplexer_1_out), .out(adder_1_out));  // open: cin, cout
  // Probe on out_3
  Register #(.width(4)) register_2 (.D(adder_1_out), .en(enable), .Q(out_3), .clk(CLK));  // open: clr

  // Other names for the same wires on the sheet: now[3:0] = out_3

  // Notes on the sheet:
  //   第一个周期把prev和now分别初始化为F0和F1
endmodule

module count1 (
  input  [2:0] \input ,
  input  in_2,
  output \end 
);

  wire comparator_1_eq, comparator_1_lt;
  wire [3:0] currentcount;
  wire [4:0] aim, bit_extender_2_out;

  assign aim = {{2{1'b0}}, \input };  // Bit_Extender bit_extender_1
  Counter #(.width(4), .max('h8), .ongoal("stay")) counter_1 (
    .Q(currentcount), .clk(in_2));  // open: load, D, count, carry, clr
  assign bit_extender_2_out = {{1{1'b0}}, currentcount};  // Bit_Extender bit_extender_2
  Comparator #(.width(5)) comparator_1 (
    .a(aim), .b(bit_extender_2_out), .eq(comparator_1_eq), .lt(comparator_1_lt));  // open: gt
  or or_1 (\end , comparator_1_eq, comparator_1_lt);

  // Other names for the same wires on the sheet: CLK = in_2
endmodule
