// Logisim project Logisim_fibonacci another2.circ as structural Verilog: 4 circuits, main circuit main
module main (
  input  [2:0] \input ,
  output [3:0] out_2
);

  wire clock_1_out, count1_end;
  wire [3:0] calculate1_output;

  count1 count1 (.\input (\input ), .in_2(clock_1_out), .\end (count1_end));
  Clock clock_1 (.out(clock_1_out));
  calculate1 calculate1 (.\end (count1_end), .CLK(clock_1_out), .\output (calculate1_output));
  Multiplexer #(.width(4)) multiplexer_1 (
    .in0(4'b0000), .in1(calculate1_output), .out(out_2), .sel(count1_end));  // open: en
endmodule

module calculate1 (
  input  \end ,
  input  CLK,
  output [3:0] \output 
);

  wire enable;
  wire [3:0] adder_1_out, now;

  not not_1 (enable, \end );
  Register #(.width(4)) register_1 (.D(now), .en(enable), .Q(\output ), .clk(CLK));  // open: clr
  // Probe on \output 
  // Probe on now
  Adder #(.width(4)) adder_1 (.a(\output ), .b(now), .out(adder_1_out));  // open: cin, cout
  \register封装  register_2 (.init(4'b0001), .Now(adder_1_out), .enable(enable), .out_4(now));

  // Other names for the same wires on the sheet: prev[3:0] = \output 
endmodule

module count1 (
  input  [2:0] \input ,
  input  in_2,
  output \end 
);

  wire comparator_1_eq, comparator_1_lt;
  wire [3:0] currentcount;
  wire [4:0] aim, bit_extender_2_out;

  assign aim = {{2{1'b0}}, \input };  // Bit_Extender bit_extender_1
  Counter #(.width(4), .max('h8), .ongoal("stay")) counter_1 (
    .Q(currentcount), .clk(in_2));  // open: load, D, count, carry, clr
  assign bit_extender_2_out = {{1{1'b0}}, currentcount};  // Bit_Extender bit_extender_2
  Comparator #(.width(5)) comparator_1 (
    .a(aim), .b(bit_extender_2_out), .eq(comparator_1_eq), .lt(comparator_1_lt));  // open: gt
  or or_1 (\end , comparator_1_eq, comparator_1_lt);

  // Other names for the same wires on the sheet: CLK = in_2
endmodule

module \register封装  (
  input  [3:0] init,
  input  [3:0] Now,
  input  enable,
  output [3:0] out_4
);

  wire clock_1_out, counter_1_q;
  wire [3:0] register_1_q;

  Register #(.width(4)) register_1 (.D(Now), .en(enable), .Q(register_1_q), .clk(clock_1_out));  // open: clr
  Counter #(.width(1), .max('h1), .ongoal("stay")) counter_1 (
    .Q(counter_1_q), .clk(clock_1_out));  // open: load, D, count, carry, clr
  Clock clock_1 (.out(clock_1_out));
  Multiplexer #(.width(4)) multiplexer_1 (.in0(init), .in1(register_1_q), .out(out_4), .sel(counter_1_q));  // open: en

  // Notes on the sheet:
  //   带有初始化功能的寄存器，注意第一个时钟上升沿到来之前（第零个周期）就已经将输出初始化
endmodule
