// Logisim project Logisim_fibonacci.circ as structural Verilog: 3 circuits, main circuit main
module main (
  input  [2:0] \input ,
  output [3:0] out_2
);

  wire clock_1_out, count_end;
  wire [3:0] calculate_out_3;

  count count (.\input (\input ), .in_2(clock_1_out), .\end (count_end));
  Clock clock_1 (.out(clock_1_out));
  calculate calculate (.\end (count_end), .CLK(clock_1_out), .out_3(calculate_out_3));
  Multiplexer #(.width(4)) multiplexer_1 (
    .in0(4'b0000), .in1(calculate_out_3), .out(out_2), .sel(count_end));  // open: en

  // Notes on the sheet:
  //   接收到end信号时输出
endmodule

module calculate (
  input  \end ,
  input  CLK,
  output [3:0] out_3
);

  wire counter_1_q, enable;
  wire [3:0] adder_1_out, multiplexer_1_out, prev;

  Counter #(.width(1), .max('h1), .ongoal("stay")) counter_1 (
    .Q(counter_1_q), .clk(CLK));  // open: load, D, count, carry, clr
  not not_1 (enable, \end );
  Multiplexer #(.width(4)) multiplexer_1 (
    .in0(4'b0001), .in1(out_3), .out(multiplexer_1_out), .sel(counter_1_q));  // open: en
  Register #(.width(4)) register_1 (.D(multiplexer_1_out), .en(enable), .Q(prev), .clk(CLK));  // open: clr
  // Probe on prev
  // Probe on out_3
  Adder #(.width(4)) adder_1 (.a(prev), .b(out_3), .out(adder_1_out));  // open: cin, cout
  Register #(.width(4)) register_2 (.D(adder_1_out), .en(enable), .Q(out_3), .clk(CLK));  // open: clr

  // Other names for the same wires on the sheet: now[3:0] = out_3

  // Notes on the sheet:
  //   第一个周期反向初始化，第二个周期颠倒回来，结果差一个周期
  //   初始化过程，在第一个时钟上升沿之前为0，为prev赋初始值，第一个时钟上升沿到达后，stay at overflow 恒为1，为prev赋值now
endmodule

module count (
  input  [2:0] \input ,
  input  in_2,
  output \end 
);

  wire [3:0] currentcount;
  wire [4:0] aim, bit_extender_2_out;

  assign aim = {{2{1'b0}}, \input };  // Bit_Extender bit_extender_1
  Counter #(.width(4), .max('h8), .ongoal("stay")) counter_1 (
    .Q(currentcount), .clk(in_2));  // open: load, D, count, carry, clr
  assign bit_extender_2_out = {{1{1'b0}}, currentcount};  // Bit_Extender bit_extender_2
  Comparator #(.width(5)) comparator_1 (.a(aim), .b(bit_extender_2_out), .lt(\end ));  // open: gt, eq

  // Other names for the same wires on the sheet: CLK = in_2

  // Notes on the sheet:
  //   达到最大时stay at overflow，从而使结果稳定输出
  //   extend到5位，确保有比0001大的count
endmodule
