// Logisim project Logisim_fibonacci2.circ as structural Verilog: 5 circuits, main circuit main
module main (
  input  [31:0] in_1,
  output [31:0] out
);

  wire clock_1_out, count_1_end;
  wire [31:0] A1, A2, A3, A4, multiply_1_a1_2, multiply_1_a2_2, multiply_1_a3_2, multiply_1_a4_2,
       \状态输出_1_output ;

  count count_1 (.\input (in_1), .CLK(clock_1_out), .\end (count_1_end));
  multiply multiply_1 (
    .A1(A1), .A2(A2), .A3(A3), .A4(A4), .A1_2(multiply_1_a1_2), .A2_2(multiply_1_a2_2),
    .A3_2(multiply_1_a3_2), .A4_2(multiply_1_a4_2));
  Clock clock_1 (.out(clock_1_out));
  register register (
    .in_1(multiply_1_a1_2), .in_2(multiply_1_a2_2), .in_3(multiply_1_a3_2), .in_4(multiply_1_a4_2),
    .\end (count_1_end), .in_6(clock_1_out), .A1(A1), .A2(A2), .A3(A3), .A4(A4));
  \状态输出  \u_状态输出_1  (.A1(A1), .A2(A2), .\input (in_1), .\output (\状态输出_1_output ));
  Multiplexer #(.width(32)) multiplexer_1 (
    .in0({32{1'b0}}), .in1(\状态输出_1_output ), .out(out), .sel(count_1_end));  // open: en

  // Other names for the same wires on the sheet: input[31:0] = in_1
endmodule

// mul
module multiply (
  input  [31:0] A1,
  input  [31:0] A2,
  input  [31:0] A3,
  input  [31:0] A4,
  output [31:0] A1_2,
  output [31:0] A2_2,
  output [31:0] A3_2,
  output [31:0] A4_2
);

  wire [31:0] B1, multiplier_1_out, multiplier_2_out, multiplier_3_out, multiplier_4_out, multiplier_5_out,
       multiplier_6_out, multiplier_7_out, multiplier_8_out;

  Multiplexer multiplexer_1 ();  // open: in0, in1, out, sel, en
  Multiplier #(.width(32)) multiplier_1 (.a(A1), .b(B1), .out(multiplier_1_out));  // open: cin, cout
  Multiplier #(.width(32)) multiplier_2 (.a(A2), .b(32'h1), .out(multiplier_2_out));  // open: cin, cout
  Multiplier #(.width(32)) multiplier_3 (.a(A1), .b(32'h1), .out(multiplier_3_out));  // open: cin, cout
  Multiplier #(.width(32)) multiplier_4 (.a(A2), .b({32{1'b0}}), .out(multiplier_4_out));  // open: cin, cout
  Multiplier #(.width(32)) multiplier_5 (.a(A3), .b(B1), .out(multiplier_5_out));  // open: cin, cout
  Multiplier #(.width(32)) multiplier_6 (.a(A4), .b(32'h1), .out(multiplier_6_out));  // open: cin, cout
  Multiplier #(.width(32)) multiplier_7 (.a(A3), .b(32'h1), .out(multiplier_7_out));  // open: cin, cout
  Multiplier #(.width(32)) multiplier_8 (.a(A4), .b({32{1'b0}}), .out(multiplier_8_out));  // open: cin, cout
  Adder #(.width(32)) adder_1 (.a(multiplier_1_out), .b(multiplier_2_out), .out(A1_2));  // open: cin, cout
  Adder #(.width(32)) adder_2 (.a(multiplier_3_out), .b(multiplier_4_out), .out(A2_2));  // open: cin, cout
  Adder #(.width(32)) adder_3 (.a(multiplier_5_out), .b(multiplier_6_out), .out(A3_2));  // open: cin, cout
  Adder #(.width(32)) adder_4 (.a(multiplier_7_out), .b(multiplier_8_out), .out(A4_2));  // open: cin, cout

  // Notes on the sheet:
  //   B1
  //   B2
  //   B3
  //   B4
endmodule

module register (
  input  [31:0] in_1,
  input  [31:0] in_2,
  input  [31:0] in_3,
  input  [31:0] in_4,
  input  \end ,
  input  in_6,
  output [31:0] A1,
  output [31:0] A2,
  output [31:0] A3,
  output [31:0] A4
);

  wire counter_1_q, counter_2_q, counter_3_q, counter_4_q, end_t;
  wire [31:0] multiplexer_1_out, multiplexer_2_out, multiplexer_3_out, multiplexer_4_out;

  not not_1 (end_t, \end );
  Counter #(.width(1), .max('h1), .ongoal("stay")) counter_1 (
    .Q(counter_1_q), .clk(in_6));  // open: load, D, count, carry, clr
  Counter #(.width(1), .max('h1), .ongoal("stay")) counter_2 (
    .Q(counter_2_q), .clk(in_6));  // open: load, D, count, carry, clr
  Counter #(.width(1), .max('h1), .ongoal("stay")) counter_3 (
    .Q(counter_3_q), .clk(in_6));  // open: load, D, count, carry, clr
  Counter #(.width(1), .max('h1), .ongoal("stay")) counter_4 (
    .Q(counter_4_q), .clk(in_6));  // open: load, D, count, carry, clr
  Multiplexer #(.width(32)) multiplexer_1 (
    .in0(32'h1), .in1(in_1), .out(multiplexer_1_out), .sel(counter_1_q));  // open: en
  Multiplexer #(.width(32)) multiplexer_2 (
    .in0(32'h1), .in1(in_2), .out(multiplexer_2_out), .sel(counter_2_q));  // open: en
  Multiplexer #(.width(32)) multiplexer_3 (
    .in0({32{1'b0}}), .in1(in_3), .out(multiplexer_3_out), .sel(counter_3_q));  // open: en
  Multiplexer #(.width(32)) multiplexer_4 (
    .in0(32'h1), .in1(in_4), .out(multiplexer_4_out), .sel(counter_4_q));  // open: en
  Register #(.width(32)) register_1 (.D(multiplexer_1_out), .en(end_t), .Q(A1), .clk(in_6));  // open: clr
  Register #(.width(32)) register_2 (.D(multiplexer_2_out), .en(end_t), .Q(A2), .clk(in_6));  // open: clr
  Register #(.width(32)) register_3 (.D(multiplexer_3_out), .en(end_t), .Q(A3), .clk(in_6));  // open: clr
  Register #(.width(32)) register_4 (.D(multiplexer_4_out), .en(end_t), .Q(A4), .clk(in_6));  // open: clr

  // Other names for the same wires on the sheet: CLK = in_6
endmodule

module count (
  input  [31:0] \input ,
  input  CLK,
  output \end 
);

  wire comparator_1_eq, comparator_1_lt;
  wire [31:0] adder_1_out, counter_1_q;

  Counter #(.width(32), .max('h40), .ongoal("stay")) counter_1 (
    .Q(counter_1_q), .clk(CLK));  // open: load, D, count, carry, clr
  Adder #(.width(32)) adder_1 (.a(counter_1_q), .b(32'h1), .out(adder_1_out));  // open: cin, cout
  Comparator #(.width(32), .mode("unsigned")) comparator_1 (
    .a(\input ), .b(adder_1_out), .eq(comparator_1_eq), .lt(comparator_1_lt));  // open: gt
  or or_1 (\end , comparator_1_eq, comparator_1_lt);
endmodule

module \状态输出  (
  input  [31:0] A1,
  input  [31:0] A2,
  input  [31:0] \input ,
  output [31:0] \output 
);

  wire comparator_1_eq;
  wire [31:0] adder_1_out;

  Adder #(.width(32)) adder_1 (.a(A1), .b(A2), .out(adder_1_out));  // open: cin, cout
  Comparator #(.width(32), .mode("unsigned")) comparator_1 (
    .a(\input ), .b(32'h1), .eq(comparator_1_eq));  // open: gt, lt
  Multiplexer #(.width(32)) multiplexer_1 (
    .in0(adder_1_out), .in1(32'h1), .out(\output ), .sel(comparator_1_eq));  // open: en
endmodule
