// Logisim project Logisim_fibonacci3.circ as structural Verilog: 10 circuits, main circuit main
module main (
  input  [31:0] \input ,
  output [31:0] out_2
);

  wire CLK, comparator_2_eq, counter_2_q, \end ;
  wire [31:0] A1, A2, A3, A4, A11, A22, A33, A44, B1, B2, B3, B4, counter_1_q, include_nextinput,
       multiplexer_1_out, multiplexer_3_out, nextinput, RE1, RE2, RE3, RE4, RE11, RE22, RE33, RE44,
       subtractor_1_out;

  // Probe on RE1
  // Probe on RE2
  Clock u_CLK (.out(CLK));
  \快速幂  \u_快速幂  (.A1(A11), .A2(A22), .A3(A33), .A4(A44), .A1_2(A1), .A2_2(A2), .A3_2(A3), .A4_2(A4));
  // Probe on subtractor_1_out
  Subtractor #(.width(32)) subtractor_1 (.a(\input ), .b(32'h1), .out(subtractor_1_out));  // open: bin, bout
  Counter #(.width(32), .max('h21), .ongoal("stay")) counter_1 (
    .Q(counter_1_q), .clk(CLK));  // open: load, D, count, carry, clr
  // Probe on RE11
  // Probe on RE3
  multiply multiply (
    .A1(RE1), .A2(RE2), .A3(RE3), .A4(RE4), .B1(B1), .B2(B2), .B3(B3), .B4(B4), .A1_2(RE11), .A2_2(RE22),
    .A3_2(RE33), .A4_2(RE44));
  Comparator #(.width(32), .mode("unsigned")) comparator_1 (.a(32'h20), .b(counter_1_q), .lt(\end ));  // open: gt, eq
  Multiplexer #(.width(32)) multiplexer_1 (
    .in0({32{1'b0}}), .in1(RE11), .out(multiplexer_1_out), .sel(\end ));  // open: en
  // Probe on RE4
  Multiplexer #(.width(32)) multiplexer_2 (
    .in0(multiplexer_1_out), .in1({32{1'b0}}), .out(out_2), .sel(comparator_2_eq));  // open: en
  Comparator #(.width(32)) comparator_2 (.a({32{1'b0}}), .b(\input ), .eq(comparator_2_eq));  // open: gt, lt
  register3 \u_寄存器  (
    .in_5(RE11), .in_6(RE22), .in_7(RE33), .in_8(RE44), .\end (\end ), .in_1(32'h1), .in_2({32{1'b0}}),
    .in_3({32{1'b0}}), .in_4(32'h1), .in_10(CLK), .A1(RE1), .A2(RE2), .A3(RE3), .A4(RE4));
  register3 \u_寄存器_2  (
    .in_5(A1), .in_6(A2), .in_7(A3), .in_8(A4), .\end (\end ), .in_1(32'h1), .in_2(32'h1), .in_3(32'h1),
    .in_4({32{1'b0}}), .in_10(CLK), .A1(A11), .A2(A22), .A3(A33), .A4(A44));
  Multiplexer #(.width(32)) multiplexer_3 (
    .in0(subtractor_1_out), .in1(nextinput), .out(multiplexer_3_out), .sel(counter_2_q));  // open: en
  Counter #(.width(1), .max('h1), .ongoal("stay")) counter_2 (
    .Q(counter_2_q), .clk(CLK));  // open: load, D, count, carry, clr
  // Probe on include_nextinput
  \include  \include  (
    .\input (multiplexer_3_out), .A1(A11), .A2(A22), .A3(A33), .A4(A44), .nextinput(include_nextinput),
    .out_7(B1), .out_8(B2), .out_9(B3), .out_10(B4));
  Register #(.width(32)) register_1 (.D(include_nextinput), .Q(nextinput), .clk(CLK));  // open: en, clr

  // Notes on the sheet:
  //   终止条件：向前移动32次
  //   判断input是否为零，为零则输出零
  //   输出re11
  //   注意周期的同步性，include是第一个周期就把input前移一位，寄存器也要在第一个周期就完成给A和RE赋初始值
  //   已有结果和快速幂结果相乘
  //   矩阵快速幂（2^n次幂）
  //   判断input在该位上是零还是一，从而判断A是单位阵还是此时的快速幂，并将input向前移动一位
endmodule

module \main1wrong_输入1时不能稳定输出  (
  input  [31:0] \input ,
  output [31:0] out_2
);

  wire CLK, comparator_1_eq, counter_1_q, \end ;
  wire [31:0] A1, A2, A3, A4, A11, A22, A33, A44, B1, B2, B3, B4, include_nextinput, judge,
       multiplexer_1_out, nextinput, RE1, RE2, RE3, RE4, RE11, RE22, RE33, RE44, subtractor_1_out;

  // Probe on RE1
  // Probe on RE2
  Clock u_CLK (.out(CLK));
  \快速幂  \u_快速幂  (.A1(A11), .A2(A22), .A3(A33), .A4(A44), .A1_2(A1), .A2_2(A2), .A3_2(A3), .A4_2(A4));
  // Probe on subtractor_1_out
  Subtractor #(.width(32)) subtractor_1 (.a(\input ), .b(32'h1), .out(subtractor_1_out));  // open: bin, bout
  // Probe on RE11
  // Probe on RE3
  multiply multiply (
    .A1(RE1), .A2(RE2), .A3(RE3), .A4(RE4), .B1(B1), .B2(B2), .B3(B3), .B4(B4), .A1_2(RE11), .A2_2(RE22),
    .A3_2(RE33), .A4_2(RE44));
  Multiplexer #(.width(32)) multiplexer_1 (
    .in0({32{1'b0}}), .in1(RE11), .out(multiplexer_1_out), .sel(\end ));  // open: en
  // Probe on RE4
  Multiplexer #(.width(32)) multiplexer_2 (
    .in0(multiplexer_1_out), .in1({32{1'b0}}), .out(out_2), .sel(comparator_1_eq));  // open: en
  Comparator #(.width(32)) comparator_1 (.a({32{1'b0}}), .b(\input ), .eq(comparator_1_eq));  // open: gt, lt
  register3 \u_寄存器  (
    .in_5(RE11), .in_6(RE22), .in_7(RE33), .in_8(RE44), .\end (\end ), .in_1(32'h1), .in_2({32{1'b0}}),
    .in_3({32{1'b0}}), .in_4(32'h1), .in_10(CLK), .A1(RE1), .A2(RE2), .A3(RE3), .A4(RE4));
  register3 \u_寄存器_2  (
    .in_5(A1), .in_6(A2), .in_7(A3), .in_8(A4), .\end (\end ), .in_1(32'h1), .in_2(32'h1), .in_3(32'h1),
    .in_4({32{1'b0}}), .in_10(CLK), .A1(A11), .A2(A22), .A3(A33), .A4(A44));
  Multiplexer #(.width(32)) multiplexer_3 (
    .in0(subtractor_1_out), .in1(nextinput), .out(judge), .sel(counter_1_q));  // open: en
  Counter #(.width(1), .max('h1), .ongoal("stay")) counter_1 (
    .Q(counter_1_q), .clk(CLK));  // open: load, D, count, carry, clr
  // Probe on include_nextinput
  \include  \include  (
    .\input (judge), .A1(A11), .A2(A22), .A3(A33), .A4(A44), .nextinput(include_nextinput), .out_7(B1),
    .out_8(B2), .out_9(B3), .out_10(B4));
  Comparator #(.width(32)) comparator_2 (.a(judge), .b({32{1'b0}}), .eq(\end ));  // open: gt, lt
  Register #(.width(32)) register_1 (.D(include_nextinput), .Q(nextinput), .clk(CLK));  // open: en, clr

  // Notes on the sheet:
  //   判断input是否为零，为零则输出零
  //   输出re11
  //   注意周期的同步性，include是第一个周期就把input前移一位，寄存器也要在第一个周期就完成给A和RE赋初始值
  //   已有结果和快速幂结果相乘
  //   矩阵快速幂（2^n次幂）
  //   判断input在该位上是零还是一，从而判断A是单位阵还是此时的快速幂，并将input向前移动一位
endmodule

module \include  (
  input  [31:0] \input ,
  input  [31:0] A1,
  input  [31:0] A2,
  input  [31:0] A3,
  input  [31:0] A4,
  output [31:0] nextinput,
  output [31:0] out_7,
  output [31:0] out_8,
  output [31:0] out_9,
  output [31:0] out_10
);

  Multiplexer #(.width(32)) multiplexer_1 (.in0(32'h1), .in1(A1), .out(out_7), .sel(\input [0]));  // open: en
  Multiplexer #(.width(32)) multiplexer_2 (.in0({32{1'b0}}), .in1(A2), .out(out_8), .sel(\input [0]));  // open: en
  Multiplexer #(.width(32)) multiplexer_3 (.in0({32{1'b0}}), .in1(A3), .out(out_9), .sel(\input [0]));  // open: en
  Multiplexer #(.width(32)) multiplexer_4 (.in0(32'h1), .in1(A4), .out(out_10), .sel(\input [0]));  // open: en

  assign nextinput = {1'b0, \input [31:1]};

  // Other names for the same wires on the sheet: includeornot = \input [0]

  // Notes on the sheet:
  //   对输入移位，每次判断最低位
endmodule

module \快速幂  (
  input  [31:0] A1,
  input  [31:0] A2,
  input  [31:0] A3,
  input  [31:0] A4,
  output [31:0] A1_2,
  output [31:0] A2_2,
  output [31:0] A3_2,
  output [31:0] A4_2
);

  wire [31:0] multiplier_1_out, multiplier_2_out, multiplier_3_out, multiplier_4_out, multiplier_5_out,
       multiplier_6_out, multiplier_7_out, multiplier_8_out;

  Multiplier #(.width(32)) multiplier_1 (.a(A1), .b(A1), .out(multiplier_1_out));  // open: cin, cout
  Multiplier #(.width(32)) multiplier_2 (.a(A2), .b(A3), .out(multiplier_2_out));  // open: cin, cout
  Multiplier #(.width(32)) multiplier_3 (.a(A1), .b(A2), .out(multiplier_3_out));  // open: cin, cout
  Multiplier #(.width(32)) multiplier_4 (.a(A2), .b(A4), .out(multiplier_4_out));  // open: cin, cout
  Multiplier #(.width(32)) multiplier_5 (.a(A3), .b(A1), .out(multiplier_5_out));  // open: cin, cout
  Multiplier #(.width(32)) multiplier_6 (.a(A4), .b(A2), .out(multiplier_6_out));  // open: cin, cout
  Multiplier #(.width(32)) multiplier_7 (.a(A3), .b(A2), .out(multiplier_7_out));  // open: cin, cout
  Multiplier #(.width(32)) multiplier_8 (.a(A4), .b(A4), .out(multiplier_8_out));  // open: cin, cout
  Adder #(.width(32)) adder_1 (.a(multiplier_1_out), .b(multiplier_2_out), .out(A1_2));  // open: cin, cout
  Adder #(.width(32)) adder_2 (.a(multiplier_3_out), .b(multiplier_4_out), .out(A2_2));  // open: cin, cout
  Adder #(.width(32)) adder_3 (.a(multiplier_5_out), .b(multiplier_6_out), .out(A3_2));  // open: cin, cout
  Adder #(.width(32)) adder_4 (.a(multiplier_7_out), .b(multiplier_8_out), .out(A4_2));  // open: cin, cout
endmodule

module register (
  input  [31:0] in_1,
  input  [31:0] in_2,
  input  [31:0] in_3,
  input  [31:0] in_4,
  input  [31:0] in_5,
  input  [31:0] in_6,
  input  [31:0] in_7,
  input  [31:0] in_8,
  input  \end ,
  input  in_10,
  output [31:0] A1,
  output [31:0] A2,
  output [31:0] A3,
  output [31:0] A4
);

  wire counter_1_q, counter_2_q, counter_3_q, counter_4_q, end_t;
  wire [31:0] multiplexer_1_out, multiplexer_2_out, multiplexer_3_out, multiplexer_4_out;

  not not_1 (end_t, \end );
  Counter #(.width(1), .max('h1), .ongoal("stay")) counter_1 (
    .Q(counter_1_q), .clk(in_10));  // open: load, D, count, carry, clr
  Counter #(.width(1), .max('h1), .ongoal("stay")) counter_2 (
    .Q(counter_2_q), .clk(in_10));  // open: load, D, count, carry, clr
  Counter #(.width(1), .max('h1), .ongoal("stay")) counter_3 (
    .Q(counter_3_q), .clk(in_10));  // open: load, D, count, carry, clr
  Counter #(.width(1), .max('h1), .ongoal("stay")) counter_4 (
    .Q(counter_4_q), .clk(in_10));  // open: load, D, count, carry, clr
  Multiplexer #(.width(32)) multiplexer_1 (
    .in0(in_1), .in1(in_5), .out(multiplexer_1_out), .sel(counter_1_q));  // open: en
  Multiplexer #(.width(32)) multiplexer_2 (
    .in0(in_2), .in1(in_6), .out(multiplexer_2_out), .sel(counter_2_q));  // open: en
  Multiplexer #(.width(32)) multiplexer_3 (
    .in0(in_3), .in1(in_7), .out(multiplexer_3_out), .sel(counter_3_q));  // open: en
  Multiplexer #(.width(32)) multiplexer_4 (
    .in0(in_4), .in1(in_8), .out(multiplexer_4_out), .sel(counter_4_q));  // open: en
  Register #(.width(32)) register_1 (.D(multiplexer_1_out), .en(end_t), .Q(A1), .clk(in_10));  // open: clr
  Register #(.width(32)) register_2 (.D(multiplexer_2_out), .en(end_t), .Q(A2), .clk(in_10));  // open: clr
  Register #(.width(32)) register_3 (.D(multiplexer_3_out), .en(end_t), .Q(A3), .clk(in_10));  // open: clr
  Register #(.width(32)) register_4 (.D(multiplexer_4_out), .en(end_t), .Q(A4), .clk(in_10));  // open: clr

  // Other names for the same wires on the sheet: CLK = in_10
endmodule

module multiply (
  input  [31:0] A1,
  input  [31:0] A2,
  input  [31:0] A3,
  input  [31:0] A4,
  input  [31:0] B1,
  input  [31:0] B2,
  input  [31:0] B3,
  input  [31:0] B4,
  output [31:0] A1_2,
  output [31:0] A2_2,
  output [31:0] A3_2,
  output [31:0] A4_2
);

  wire [31:0] multiplier_1_out, multiplier_2_out, multiplier_3_out, multiplier_4_out, multiplier_5_out,
       multiplier_6_out, multiplier_7_out, multiplier_8_out;

  Multiplier #(.width(32)) multiplier_1 (.a(A1), .b(B1), .out(multiplier_1_out));  // open: cin, cout
  Multiplier #(.width(32)) multiplier_2 (.a(A2), .b(B3), .out(multiplier_2_out));  // open: cin, cout
  Multiplier #(.width(32)) multiplier_3 (.a(A1), .b(B2), .out(multiplier_3_out));  // open: cin, cout
  Multiplier #(.width(32)) multiplier_4 (.a(A2), .b(B4), .out(multiplier_4_out));  // open: cin, cout
  Multiplier #(.width(32)) multiplier_5 (.a(A3), .b(B1), .out(multiplier_5_out));  // open: cin, cout
  Multiplier #(.width(32)) multiplier_6 (.a(A4), .b(B2), .out(multiplier_6_out));  // open: cin, cout
  Multiplier #(.width(32)) multiplier_7 (.a(A3), .b(B2), .out(multiplier_7_out));  // open: cin, cout
  Multiplier #(.width(32)) multiplier_8 (.a(A4), .b(B4), .out(multiplier_8_out));  // open: cin, cout
  Adder #(.width(32)) adder_1 (.a(multiplier_1_out), .b(multiplier_2_out), .out(A1_2));  // open: cin, cout
  Adder #(.width(32)) adder_2 (.a(multiplier_3_out), .b(multiplier_4_out), .out(A2_2));  // open: cin, cout
  Adder #(.width(32)) adder_3 (.a(multiplier_5_out), .b(multiplier_6_out), .out(A3_2));  // open: cin, cout
  Adder #(.width(32)) adder_4 (.a(multiplier_7_out), .b(multiplier_8_out), .out(A4_2));  // open: cin, cout
endmodule

module register1 (
  input  [31:0] in_1,
  input  [31:0] in_2,
  input  [31:0] in_3,
  input  [31:0] in_4,
  input  CLK,
  input  \end ,
  output [31:0] A1,
  output [31:0] A2,
  output [31:0] A3,
  output [31:0] A4
);

  wire not_1_out;

  not not_1 (not_1_out, \end );
  Register #(.width(32)) register_1 (.D(in_1), .en(not_1_out), .Q(A1), .clk(CLK));  // open: clr
  Register #(.width(32)) register_2 (.D(in_2), .en(not_1_out), .Q(A2), .clk(CLK));  // open: clr
  Register #(.width(32)) register_3 (.D(in_3), .en(not_1_out), .Q(A3), .clk(CLK));  // open: clr
  Register #(.width(32)) register_4 (.D(in_4), .en(not_1_out), .Q(A4), .clk(CLK));  // open: clr
endmodule

module \output  (
  input  [31:0] re1,
  input  [31:0] re2,
  input  [31:0] \input ,
  output [31:0] \output 
);

  wire comparator_1_eq;
  wire [31:0] adder_1_out;

  Adder #(.width(32)) adder_1 (.a(re1), .b(re2), .out(adder_1_out));  // open: cin, cout
  Comparator #(.width(32)) comparator_1 (.a(\input ), .b({32{1'b0}}), .eq(comparator_1_eq));  // open: gt, lt
  Multiplexer #(.width(32)) multiplexer_1 (
    .in0(adder_1_out), .in1({32{1'b0}}), .out(\output ), .sel(comparator_1_eq));  // open: en
endmodule

module register3 (
  input  [31:0] in_1,
  input  [31:0] in_2,
  input  [31:0] in_3,
  input  [31:0] in_4,
  input  [31:0] in_5,
  input  [31:0] in_6,
  input  [31:0] in_7,
  input  [31:0] in_8,
  input  \end ,
  input  in_10,
  output [31:0] A1,
  output [31:0] A2,
  output [31:0] A3,
  output [31:0] A4
);

  wire counter_1_q, counter_2_q, counter_3_q, counter_4_q, end_t;
  wire [31:0] register_1_q, register_2_q, register_3_q, register_4_q;

  not not_1 (end_t, \end );
  Counter #(.width(1), .max('h1), .ongoal("stay")) counter_1 (
    .Q(counter_1_q), .clk(in_10));  // open: load, D, count, carry, clr
  Register #(.width(32)) register_1 (.D(in_5), .en(end_t), .Q(register_1_q), .clk(in_10));  // open: clr
  Register #(.width(32)) register_2 (.D(in_6), .en(end_t), .Q(register_2_q), .clk(in_10));  // open: clr
  Counter #(.width(1), .max('h1), .ongoal("stay")) counter_2 (
    .Q(counter_2_q), .clk(in_10));  // open: load, D, count, carry, clr
  Register #(.width(32)) register_3 (.D(in_7), .en(end_t), .Q(register_3_q), .clk(in_10));  // open: clr
  Counter #(.width(1), .max('h1), .ongoal("stay")) counter_3 (
    .Q(counter_3_q), .clk(in_10));  // open: load, D, count, carry, clr
  Register #(.width(32)) register_4 (.D(in_8), .en(end_t), .Q(register_4_q), .clk(in_10));  // open: clr
  Counter #(.width(1), .max('h1), .ongoal("stay")) counter_4 (
    .Q(counter_4_q), .clk(in_10));  // open: load, D, count, carry, clr
  Multiplexer #(.width(32)) multiplexer_1 (.in0(in_1), .in1(register_1_q), .out(A1), .sel(counter_1_q));  // open: en
  Multiplexer #(.width(32)) multiplexer_2 (.in0(in_2), .in1(register_2_q), .out(A2), .sel(counter_2_q));  // open: en
  Multiplexer #(.width(32)) multiplexer_3 (.in0(in_3), .in1(register_3_q), .out(A3), .sel(counter_3_q));  // open: en
  Multiplexer #(.width(32)) multiplexer_4 (.in0(in_4), .in1(register_4_q), .out(A4), .sel(counter_4_q));  // open: en

  // Other names for the same wires on the sheet: CLK = in_10

  // Notes on the sheet:
  //   第一个周期开始之前就赋初始值，不经过寄存器
endmodule

module \判断方法  (
  input  [31:0] \input ,
  input  [31:0] input_2,
  output [31:0] nextinput
);

  wire [31:0] includeornot32, shifter_1_out;

  Shifter #(.width(32), .shift("rr")) shifter_1 (.in(input_2), .\dist (5'b00001), .out(shifter_1_out));
  assign includeornot32 = shifter_1_out & 32'h1;  // AND_Gate and_1, 32 bits wide

  assign nextinput = {1'b0, \input [31:1]};

  // Other names for the same wires on the sheet: includeornot = \input [0]

  // Notes on the sheet:
  //   用splitter分割输入，每次取出第零位，并将0接到最高位
  //   对输入移位，每次与常量（32位的1）AND，从而取出最高位（注意最终结果是32位的1或者0）
endmodule
