// Logisim project Logisim_mod5 another try.circ as structural Verilog: 4 circuits, main circuit mod5
module mod5 (
  input  In,
  output S0,
  output S1,
  output S2,
  output S3,
  output S4
);

  wire clock_1_out;
  wire [1:0] current, \状态转移_1_out_3 ;

  \状态转移  \u_状态转移_1  (.in_1(current), .In(In), .out_3(\状态转移_1_out_3 ));
  Register #(.width(2)) register_1 (.D(\状态转移_1_out_3 ), .Q(current), .clk(clock_1_out));  // open: en, clr
  Clock clock_1 (.out(clock_1_out));
  \状态传递  \u_状态传递_1  (.C1(current[0]), .C0(current[1]), .In(In), .S0(S0), .S1(S1), .S2(S2), .S3(S3), .S4(S4));
endmodule

module \状态转移  (
  input  [1:0] in_1,
  input  In,
  output [1:0] out_3
);

  wire and_1_out, and_2_out, and_3_out, and_4_out, and_5_out, and_6_out, not_1_out, not_2_out, not_3_out,
       not_4_out, not_5_out, not_6_out, not_7_out, not_8_out;

  not not_1 (not_1_out, in_1[0]);
  not not_2 (not_2_out, in_1[1]);
  not not_3 (not_3_out, in_1[0]);
  not not_4 (not_4_out, in_1[1]);
  not not_5 (not_5_out, in_1[0]);
  not not_6 (not_6_out, In);
  not not_7 (not_7_out, in_1[1]);
  not not_8 (not_8_out, In);
  and and_1 (and_1_out, not_1_out, in_1[1]);
  and and_2 (and_2_out, in_1[0], not_2_out);
  and and_3 (and_3_out, not_3_out, not_4_out, In);
  and and_4 (and_4_out, not_5_out, in_1[1], not_6_out);
  and and_5 (and_5_out, in_1[0], not_7_out, not_8_out);
  and and_6 (and_6_out, in_1[0], in_1[1], In);
  or or_1 (out_3[0], and_1_out, and_2_out);
  or or_2 (out_3[1], and_3_out, and_4_out, and_5_out, and_6_out);
endmodule

module \状态传递  (
  input  C1,
  input  C0,
  input  In,
  output S0,
  output S1,
  output S2,
  output S3,
  output S4
);

  wire and_1_out, and_2_out, and_3_out, and_4_out, and_5_out, and_6_out, and_7_out, and_8_out, not_1_out,
       not_2_out, not_3_out, not_4_out, not_5_out, not_6_out, not_7_out, not_8_out, not_9_out, not_10_out,
       not_11_out, not_12_out;

  not not_1 (not_1_out, C1);
  not not_2 (not_2_out, C0);
  not not_3 (not_3_out, In);
  not not_4 (not_4_out, In);
  not not_5 (not_5_out, C1);
  not not_6 (not_6_out, C0);
  not not_7 (not_7_out, C1);
  not not_8 (not_8_out, C0);
  not not_9 (not_9_out, C1);
  not not_10 (not_10_out, In);
  not not_11 (not_11_out, C0);
  not not_12 (not_12_out, In);
  and and_1 (and_1_out, not_1_out, not_2_out, not_3_out);
  and and_2 (and_2_out, C1, C0, not_4_out);
  and and_3 (and_3_out, not_5_out, not_6_out, In);
  and and_4 (and_4_out, C1, C0, In);
  and and_5 (and_5_out, not_7_out, C0, In);
  and and_6 (and_6_out, C1, not_8_out, In);
  and and_7 (and_7_out, not_9_out, C0, not_10_out);
  and and_8 (and_8_out, C1, not_11_out, not_12_out);
  or or_1 (S1, and_1_out, and_2_out);
  or or_2 (S2, and_3_out, and_4_out);
  or or_3 (S3, and_5_out, and_6_out);
  or or_4 (S4, and_7_out, and_8_out);

  assign S0 = 1'b0;
endmodule

module \测试电路  (
  output In,
  output out_2,
  output out_3,
  output out_4,
  output out_5,
  output out_6,
  output halt
);

  wire clock_1_out;
  wire [7:0] counter_1_q;

  Clock clock_1 (.out(clock_1_out));
  Counter #(.max('he), .ongoal("stay")) counter_1 (
    .Q(counter_1_q), .carry(halt), .clk(clock_1_out));  // open: load, D, count, clr
  RAM #(.dataWidth(1)) ram_1 (.addr(counter_1_q), .data(In));  // open: sel, clk, ld, clr
  mod5 mod5_1 (.In(In), .S0(out_2), .S1(out_3), .S2(out_4), .S3(out_5), .S4(out_6));
endmodule
