// Logisim project Logisim_swap.circ as structural Verilog: 1 circuit, main circuit main
module main (
  input  I1,
  input  I2,
  input  S,
  output O1,
  output O2
);

  Multiplexer multiplexer_1 (.in0(I1), .in1(I2), .out(O1), .sel(S));  // open: en
  Multiplexer multiplexer_2 (.in0(I2), .in1(I1), .out(O2), .sel(S));  // open: en
endmodule
