// Logisim project Logisim_swap1.circ as structural Verilog
module swap (
  input  I1,
  input  I2,
  input  S,
  output O1,
  output O2
);

  wire and_1_out, and_2_out, and_3_out, and_4_out, not_1_out;

  not not_1 (not_1_out, S);
  and and_1 (and_1_out, I1, not_1_out);
  and and_2 (and_2_out, not_1_out, I2);
  and and_3 (and_3_out, I2, S);
  and and_4 (and_4_out, I1, S);
  or or_1 (O1, and_1_out, and_3_out);
  or or_2 (O2, and_2_out, and_4_out);
endmodule
