// Logisim project learn20210908.circ as structural Verilog: 1 circuit, main circuit main
module main (
  input  in_1,
  input  in_2,
  input  in_3,
  input  in_4,
  input  in_5,
  input  in_6,
  input  in_7,
  input  in_8,
  input  in_9,
  input  in_10,
  input  in_11,
  input  in_12,
  output out_13,
  output out_14,
  output out_15,
  output out_16,
  output out_17,
  output out_18,
  output out_19,
  output out_20
);

  wire not_1_out, or_2_out, undriven;

  not not_1 (not_1_out, in_1);
  // Buffer buffer_1 is placed but not wired
  nor nor_1 (out_15, in_4, in_5, in_6);
  or or_1 (out_13, in_1, not_1_out);
  and and_1 (out_18, ~in_8, in_10);  // AND_Gate
  and and_2 (out_19, ~in_8, ~in_10, in_11);  // AND_Gate
  and and_3 (out_20, ~in_8, ~in_10, ~in_11, in_12);  // AND_Gate
  // NAND_Gate nand_1 is placed but not wired
  // XOR_Gate xor_1 is placed but not wired
  or or_2 (or_2_out, in_7, undriven, in_9);
  not not_2 (out_16, or_2_out);
  nor nor_2 (out_14, in_2, in_3);

  assign out_17 = in_8;

  // Notes on the sheet:
  //   优先级电路原理图
endmodule
