// Logisim project learn20210909.circ as structural Verilog: 3 circuits, main circuit main
module main (
  input  enable,
  input  in_2,
  input  in_3,
  input  \多路选择器 ,
  input  in_5,
  input  [7:0] in_6,
  input  in_7,
  input  [1:0] in_8,
  input  in_9,
  input  in_10,
  input  in_11,
  input  in_12,
  input  in_13,
  input  in_14,
  input  in_15,
  input  in_16,
  input  in_17,
  input  in_18,
  input  in_19,
  input  in_20,
  input  in_21,
  input  in_22,
  input  in_23,
  input  in_24,
  input  in_25,
  input  in_26,
  input  in_27,
  input  in_28,
  input  A,
  input  A_2,
  input  B,
  input  B_2,
  input  [2:0] in_33,
  input  [1:0] AB,
  input  C,
  input  [5:0] in_36,
  output out_37,
  output out_38,
  output \_4_1多路选择器 ,
  output out_40,
  output out_41,
  output out_42,
  output out_43,
  output Y,
  output out_45,
  output out_46,
  output out_47,
  output [2:0] out_48
);

  wire multiplexer_5_out, multiplexer_6_out, not_1_out, not_2_out, not_3_out, not_4_out;

  not not_1 (not_1_out, B);
  // Probe on in_33
  assign out_40 = in_9 ? in_13 : 1'bz;  // Controlled_Buffer controlled_buffer_1
  assign out_41 = in_17 ? ~in_18 : 1'bz;  // Controlled_Inverter controlled_inverter_1
  assign out_43 = not_2_out ? in_24 : 1'bz;  // Controlled_Buffer controlled_buffer_2
  not not_2 (not_2_out, in_26);
  assign out_43 = in_26 ? in_28 : 1'bz;  // Controlled_Buffer controlled_buffer_3
  Multiplexer multiplexer_1 (.in0(B), .in1(not_1_out), .out(Y), .sel(A));  // open: en
  Multiplexer #(.select(3)) multiplexer_2 (
    .in0(1'b1), .in1(1'b0), .in2(1'b0), .in3(1'b1), .in4(1'b1), .in5(1'b1), .in6(1'b0), .in7(1'b0),
    .out(out_47), .sel(in_33));  // open: en
  assign out_48 = ~(in_36[2:0] ^ in_36[5:3]);  // XNOR_Gate xnor_1, 3 bits wide
  not not_3 (not_3_out, C);
  not not_4 (not_4_out, 1'b1);
  Multiplexer multiplexer_3 (.in0(\多路选择器 ), .in1(in_5), .out(out_37), .sel(in_2), .en(enable));
  Multiplexer #(.select(2)) multiplexer_4 (
    .in0(in_10), .in1(in_11), .in2(in_14), .in3(in_15), .out(\_4_1多路选择器 ), .sel(in_8));  // open: en
  Multiplexer #(.enable("false")) multiplexer_5 (.in0(in_22), .in1(in_23), .out(multiplexer_5_out), .sel(in_21));
  Multiplexer #(.enable("false")) multiplexer_6 (.in0(in_25), .in1(in_27), .out(multiplexer_6_out), .sel(in_21));
  Multiplexer multiplexer_7 (.in0(not_4_out), .in1(B_2), .out(out_45), .sel(A_2));  // open: en
  Multiplexer #(.select(2)) multiplexer_8 (
    .in0(not_3_out), .in1(C), .in2(1'b1), .in3(1'b0), .out(out_46), .sel(AB));  // open: en
  Multiplexer #(.enable("false")) multiplexer_9 (
    .in0(multiplexer_5_out), .in1(multiplexer_6_out), .out(out_42), .sel(in_20));
  Pull_Resistor pull_resistor_1 (.node(in_12));
  Clock clock_1 (.out(in_16));
  _7_Segment_Display u_7_segment_display_1 (.g(in_19));  // open: f, a, b, e, d, c, dp

  assign in_7 = in_3;
  assign out_38 = in_3;

  // Notes on the sheet:
  //   A和B的异或
  //   2:1多路选择器
  //   三态缓冲器
  //   A与B
  //   4:1多路选择器
endmodule

module _2_1_mux (
  input  IN1,
  input  IN2,
  input  switch,
  output out_4
);

  wire and_1_out, and_2_out, not_1_out;

  not not_1 (not_1_out, switch);
  and and_1 (and_1_out, IN1, not_1_out);
  and and_2 (and_2_out, IN2, switch);
  or or_1 (out_4, and_1_out, and_2_out);
endmodule

module _4_1_mux (
  input  in_1,
  input  in_2,
  input  in_3,
  input  in_4,
  input  in_5,
  input  in_6,
  output out_7
);

  wire n2_1_mux_1_out_4, n2_1_mux_2_out_4;

  _2_1_mux u_2_1_mux_1 (.IN1(in_1), .IN2(in_2), .switch(in_6), .out_4(n2_1_mux_1_out_4));
  _2_1_mux u_2_1_mux_2 (.IN1(in_3), .IN2(in_4), .switch(in_6), .out_4(n2_1_mux_2_out_4));
  _2_1_mux u_2_1_mux_3 (.IN1(n2_1_mux_1_out_4), .IN2(n2_1_mux_2_out_4), .switch(in_5), .out_4(out_7));
endmodule
