// Logisim project learn20210910.circ as structural Verilog: 1 circuit, main circuit main
module main (
  input  [2:0] in_1,
  input  [2:0] in_2,
  input  [7:0] \从右向左排号_从零排位 ,
  input  [7:0] in_4,
  input  [1:0] in_5,
  input  in_6,
  input  [2:0] in_7,
  output [2:0] out_8,
  output [3:0] out_9,
  output [1:0] out_10,
  output [1:0] out_11,
  output [1:0] out_12,
  output out_13,
  output out_14,
  output out_15,
  output out_16,
  output out_17,
  output _00100000,
  output out_19,
  output out_20
);

  Multiplexer multiplexer_1 ();  // open: in0, in1, out, sel, en
  Demultiplexer #(.width(2)) demultiplexer_1 (.out0(out_11), .out1(out_12), .in(in_5), .sel(in_6));  // open: en
  Decoder #(.select(3)) decoder_1 (
    .out0(out_13), .out1(out_14), .out2(out_15), .out3(out_16), .out4(out_17), .out5(_00100000),
    .out6(out_19), .out7(out_20), .sel(in_7));  // open: en
  assign out_8 = in_1 & in_2;  // AND_Gate and_1, 3 bits wide
  // Probe on \从右向左排号_从零排位 [3:0]
  // Probe on \从右向左排号_从零排位 [7:4]
  and and_2 (out_10[0], in_4[0], in_4[0], in_4[2]);
  xnor xnor_1 (out_10[1], in_4[4], in_4[6]);
  assign out_9 = \从右向左排号_从零排位 [3:0] & \从右向左排号_从零排位 [7:4];  // AND_Gate and_3, 4 bits wide

  // Notes on the sheet:
  //   combine end
  //   读数往上看
  //   split end
  //   多路选择器，用于处理多个信号，选择其中一个作为输出
  //   多路分配器，与多路选择器功能恰好相反。能够根据需要传送到多个输出端的任何一个输出端
  //   位宽要匹配
  //   译码器：将二进制编码转化为独热码(只含有一个1其余都是0)，从下往上读
endmodule
