// Logisim project learn20210911.circ as structural Verilog: 7 circuits, main circuit main
module main (
  input  R,
  input  S,
  input  in_3,
  input  in_4,
  input  CLK,
  input  D,
  output Q,
  output nQ,
  output out_9,
  output out_10,
  output Q_2,
  output nQ_2
);

  wire and_1_out, and_2_out, and_3_out, and_4_out, not_1_out, not_2_out, not_3_out;

  not not_1 (not_1_out, in_3);
  not not_2 (not_2_out, in_4);
  not not_3 (not_3_out, D);
  nor nor_1 (Q, R, nQ);
  nor nor_2 (nQ, Q, S);
  and and_1 (and_1_out, not_1_out, out_10);
  and and_2 (and_2_out, out_9, not_2_out);
  and and_3 (and_3_out, CLK, not_3_out);
  and and_4 (and_4_out, D, CLK);
  not not_4 (out_9, and_1_out);
  not not_5 (out_10, and_2_out);
  nor nor_3 (Q_2, and_3_out, nQ_2);
  nor nor_4 (nQ_2, Q_2, and_4_out);

  // Notes on the sheet:
  //   R和S不能同时为零
  //   调成0时等于先前的值
  //   SR锁存器
  //   D锁存器:CLK为零时维持原状，为一时Q=D
  //   交叉耦合的或非门
  //   交叉耦合的或非门
endmodule

module full_adder (
  input  a,
  input  b,
  input  carry,
  output carry_2,
  output sum
);

  wire and_1_out, and_2_out, and_3_out, and_4_out, and_5_out, and_6_out, and_7_out, and_8_out, and_9_out,
       and_10_out, and_11_out, not_1_out, not_2_out, not_3_out, not_4_out, not_5_out, not_6_out, or_1_out,
       or_3_out, or_4_out;

  and and_1 (and_1_out, b, carry);
  and and_2 (and_2_out, a, carry);
  not not_1 (not_1_out, a);
  not not_2 (not_2_out, b);
  not not_3 (not_3_out, a);
  not not_4 (not_4_out, b);
  or or_1 (or_1_out, and_1_out, and_2_out);
  and and_3 (and_3_out, a, b);
  and and_4 (and_4_out, not_1_out, not_2_out);
  and and_5 (and_5_out, not_3_out, b);
  not not_5 (not_5_out, carry);
  and and_6 (and_6_out, a, not_4_out);
  not not_6 (not_6_out, carry);
  and and_7 (and_7_out, a, b);
  or or_2 (carry_2, or_1_out, and_3_out);
  and and_8 (and_8_out, and_4_out, carry);
  and and_9 (and_9_out, and_5_out, not_5_out);
  and and_10 (and_10_out, and_6_out, not_6_out);
  and and_11 (and_11_out, and_7_out, carry);
  or or_3 (or_3_out, and_8_out, and_9_out);
  or or_4 (or_4_out, and_10_out, and_11_out);
  or or_5 (sum, or_3_out, or_4_out);
endmodule

module fulladder (
  input  a,
  input  b,
  input  carry,
  output carry_2,
  output sum
);

  wire nand_1_out, nand_2_out, nand_3_out, nand_4_out, nand_5_out, nand_6_out, nand_7_out, nand_8_out,
       nand_9_out, nand_11_out, nand_12_out, nand_13_out, nand_14_out;

  nand nand_1 (nand_1_out, b, carry);
  nand nand_2 (nand_2_out, a, carry);
  nand nand_3 (nand_3_out, a, b);
  nand nand_4 (nand_4_out, a, a);
  nand nand_5 (nand_5_out, b, b);
  nand nand_6 (nand_6_out, a, a);
  nand nand_7 (nand_7_out, carry, carry);
  nand nand_8 (nand_8_out, b, b);
  nand nand_9 (nand_9_out, carry, carry);
  nand nand_10 (carry_2, nand_1_out, nand_2_out, nand_3_out);
  nand nand_11 (nand_11_out, nand_4_out, nand_5_out, carry);
  nand nand_12 (nand_12_out, nand_6_out, b, nand_7_out);
  nand nand_13 (nand_13_out, a, nand_8_out, nand_9_out);
  nand nand_14 (nand_14_out, a, b, carry);
  nand nand_15 (sum, nand_11_out, nand_12_out, nand_13_out, nand_14_out);
endmodule

module practice (
  input  [3:0] in_1,
  input  [3:0] in_2,
  input  Data,
  input  Enable,
  input  [1:0] in_5,
  input  Clear,
  input  [1:0] in_7,
  input  [3:0] in_8,
  input  in_9,
  input  in_10,
  input  in_11,
  output out_12,
  output Output,
  output [4:0] out_14,
  output out_15
);

  wire clock_1_out, Clock_3_out, register_1_q;

  Clock clock_1 (.out(clock_1_out));
  Clock clock_2 ();  // open: out
  Comparator #(.width(4)) comparator_1 (.a(in_1), .b(in_2), .eq(out_12));  // open: gt, lt
  Comparator #(.width(2)) comparator_2 (.a(in_5), .b(in_7));  // open: gt, eq, lt
  Register #(.width(1)) register_1 (.D(in_9), .Q(register_1_q), .clk(clock_1_out), .clr(in_10));  // open: en
  assign out_14 = {{1{1'b0}}, in_8};  // Bit_Extender bit_extender_1
  Register #(.width(1)) register_2 (.D(register_1_q), .Q(out_15), .clk(clock_1_out), .clr(in_11));  // open: en
  Clock Clock_3 (.out(Clock_3_out));
  Register #(.width(1)) register_3 (.D(Data), .en(Enable), .Q(Output), .clk(Clock_3_out), .clr(Clear));
  RAM #(.bus("separate")) ram_1 ();  // open: addr, din, data, str, sel, clk, ld, clr
  ROM rom_1 ();  // open: addr, data, sel

  // Notes on the sheet:
  //   时钟
  //   默认数字带有符号
  //   超过16将前面截断，空格或者换行分隔一组数据
  //   contents of rom_1 (hex, n*v repeats v):
  //   86*0 9
endmodule

module \SR锁存器  (
  input  R,
  input  S,
  output Q,
  output nQ
);

  nor nor_1 (Q, R, nQ);
  nor nor_2 (nQ, Q, S);

  // Notes on the sheet:
  //   R和S不能同时为零
  //   调成0时等于先前的值
  //   SR锁存器
  //   交叉耦合的或非门
endmodule

// 锁存器
module \D锁存器  (
  input  CLK,
  input  D,
  output Q,
  output nQ
);

  wire and_1_out, and_2_out, not_1_out;

  not not_1 (not_1_out, D);
  and and_1 (and_1_out, CLK, not_1_out);
  and and_2 (and_2_out, CLK, D);
  \SR锁存器  \SR锁存器  (.R(and_1_out), .S(and_2_out), .Q(Q), .nQ(nQ));
endmodule

module \D触发器  (
  input  CLK,
  input  D,
  output Q,
  output nQ
);

  wire not_1_out, \主锁存器_q ;

  not not_1 (not_1_out, CLK);
  \D锁存器  \u_主锁存器  (.D(D), .CLK(not_1_out), .Q(\主锁存器_q ));  // open: nQ
  \D锁存器  \u_从锁存器  (.D(\主锁存器_q ), .CLK(CLK), .Q(Q), .nQ(nQ));
endmodule
