// Logisim project learn20210912.circ as structural Verilog
module \SR锁存器  (
  input  R,
  input  S,
  output Q,
  output nQ
);

  nor nor_1 (Q, R, nQ);
  nor nor_2 (nQ, Q, S);
endmodule

module \D锁存器  (
  input  CLK,
  input  D,
  output Q,
  output nQ
);

  wire and_1_out, and_2_out, not_1_out;

  not not_1 (not_1_out, D);
  and and_1 (and_1_out, CLK, not_1_out);
  and and_2 (and_2_out, CLK, D);
  \SR锁存器  \sr锁存器_1  (.R(and_1_out), .S(and_2_out), .Q(Q), .nQ(nQ));
endmodule

module \D触发器  (
  input  CLK,
  input  D,
  output Q,
  output out_4
);

  wire \d锁存器_1_q , not_1_out;

  not not_1 (not_1_out, CLK);
  \D锁存器  \d锁存器_1  (.D(D), .CLK(not_1_out), .Q(\d锁存器_1_q ));  // open: nQ
  \D锁存器  \d锁存器_2  (.D(\d锁存器_1_q ), .CLK(CLK), .Q(Q), .nQ(out_4));
endmodule

module \带使能端的触发器  (
  input  CLK,
  input  Enable,
  input  D,
  output Q,
  output nQ
);

  wire multiplexer_1_out;

  Multiplexer multiplexer_1 (.in1(D), .out(multiplexer_1_out), .sel(Enable));  // open: in0, en
  \D触发器  \d触发器_1  (.D(multiplexer_1_out), .CLK(CLK), .Q(Q), .out_4(nQ));
endmodule

module \带复位功能的触发器  (
  input  CLK,
  input  D,
  input  nRESET,
  output Q,
  output nQ
);

  wire and_1_out;

  and and_1 (and_1_out, D, nRESET);
  \D触发器  \d触发器_1  (.D(and_1_out), .CLK(CLK), .Q(Q), .out_4(nQ));
endmodule

module \同步复位触发器  (
  input  CLK,
  input  D,
  input  reset,
  output Q
);

  wire multiplexer_1_out;

  Multiplexer multiplexer_1 (.in0(D), .in1(1'b0), .out(multiplexer_1_out), .sel(reset));  // open: en
  \D触发器  \d触发器_1  (.D(multiplexer_1_out), .CLK(CLK), .Q(Q));  // open: out_4
endmodule

module \同步置位触发器  (
  input  CLK,
  input  D,
  input  reset,
  output Q
);

  wire or_1_out;

  or or_1 (or_1_out, D, reset);
  \D触发器  \d触发器_1  (.D(or_1_out), .CLK(CLK), .Q(Q));  // open: out_4
endmodule

module \异步复位触发器  (
  input  D,
  input  reset,
  output out_3
);

  wire clock_1_out, \d触发器_1_q ;

  Clock clock_1 (.out(clock_1_out));
  \D触发器  \d触发器_1  (.D(D), .CLK(clock_1_out), .Q(\d触发器_1_q ));  // open: out_4
  and and_1 (out_3, \d触发器_1_q , ~reset);  // AND_Gate
endmodule

module \异步置位触发器  (
  input  in_1,
  input  reset,
  output out_3
);

  wire clock_1_out, \d触发器_1_q ;

  Clock clock_1 (.out(clock_1_out));
  \D触发器  \d触发器_1  (.D(in_1), .CLK(clock_1_out), .Q(\d触发器_1_q ));  // open: out_4
  or or_1 (out_3, \d触发器_1_q , reset);
endmodule

module \一个看似改进的D锁存器_异步电路  (
  input  in_1,
  input  in_2,
  output out_3
);

  wire and_1_out, and_2_out, CLK_out, not_1_out, register_1_q;

  Clock CLK (.out(CLK_out));
  not not_1 (not_1_out, CLK_out);
  and and_1 (and_1_out, in_1, CLK_out);
  and and_2 (and_2_out, not_1_out, register_1_q);
  Register #(.width(1)) register_1 (.D(out_3), .Q(register_1_q), .clk(CLK_out));  // open: en, clr
  or or_1 (out_3, and_1_out, and_2_out);

  // Other names for the same wires on the sheet: Data_to_Register = out_3
endmodule

module \两位的状态寄存器  (
  input  in_1,
  input  S11,
  input  S00,
  input  reset,
  output out_5,
  output out_6
);

  wire \d触发器_1_q , \d触发器_2_q , not_1_out;

  \D触发器  \d触发器_1  (.D(S11), .CLK(in_1), .Q(\d触发器_1_q ));  // open: out_4
  \D触发器  \d触发器_2  (.D(S00), .CLK(in_1), .Q(\d触发器_2_q ));  // open: out_4
  not not_1 (not_1_out, reset);
  and and_1 (out_5, \d触发器_1_q , not_1_out);
  and and_2 (out_6, \d触发器_2_q , not_1_out);
endmodule

module \三位的状态寄存器  (
  input  CLK,
  input  in_2,
  input  in_3,
  input  in_4,
  input  reset,
  output out_6,
  output out_7,
  output out_8
);

  wire \d触发器_1_q , \d触发器_2_q , \d触发器_3_q ;

  \D触发器  \d触发器_1  (.D(in_2), .CLK(CLK), .Q(\d触发器_1_q ));  // open: out_4
  \D触发器  \d触发器_2  (.D(in_3), .CLK(CLK), .Q(\d触发器_2_q ));  // open: out_4
  \D触发器  \d触发器_3  (.D(in_4), .CLK(CLK), .Q(\d触发器_3_q ));  // open: out_4
  and and_1 (out_6, \d触发器_1_q , ~reset);  // AND_Gate
  and and_2 (out_7, \d触发器_2_q , ~reset);  // AND_Gate
  or or_1 (out_8, \d触发器_3_q , reset);
endmodule

module \二进制输出表  (
  input  S1,
  input  S0,
  output La1,
  output La0,
  output Lb1,
  output Lb0
);

  wire not_1_out;

  not not_1 (not_1_out, S1);
  not not_2 (Lb1, S1);
  and and_1 (Lb0, S1, S0);
  and and_2 (La0, not_1_out, S0);

  assign La1 = S1;
endmodule

module \红绿灯路口  (
  input  Ta,
  input  Tb,
  input  reset,
  output Lb1,
  output Lb0,
  output La1,
  output La0
);

  wire and_1_out, and_2_out, clock_1_out, not_1_out, not_2_out, not_3_out, not_4_out, not_5_out, not_6_out,
       or_1_out, xor_1_out, \两位的状态寄存器_1_out_6 ;

  xor xor_1 (xor_1_out, \两位的状态寄存器_1_out_6 , Lb1);
  not not_1 (not_1_out, Lb1);
  not not_2 (not_2_out, \两位的状态寄存器_1_out_6 );
  not not_3 (not_3_out, Ta);
  not not_4 (not_4_out, \两位的状态寄存器_1_out_6 );
  not not_5 (not_5_out, Tb);
  and and_1 (and_1_out, not_1_out, not_2_out, not_3_out);
  and and_2 (and_2_out, Lb1, not_4_out, not_5_out);
  or or_1 (or_1_out, and_1_out, and_2_out);
  // Probe on xor_1_out
  // Probe on or_1_out
  Clock clock_1 (.out(clock_1_out));
  \两位的状态寄存器  \u_两位的状态寄存器_1  (
    .S11(xor_1_out), .S00(or_1_out), .in_1(clock_1_out), .reset(reset), .out_5(Lb1),
    .out_6(\两位的状态寄存器_1_out_6 ));
  not not_6 (not_6_out, Lb1);
  not not_7 (La1, Lb1);
  and and_3 (La0, Lb1, \两位的状态寄存器_1_out_6 );
  and and_4 (Lb0, not_6_out, \两位的状态寄存器_1_out_6 );

  // Notes on the sheet:
  //   这里必须有复位让系统步入第一个周期
endmodule

module \举重裁判RS锁存器  (
  output out_1
);

  wire or_1_out, \sr锁存器_1_q , \sr锁存器_2_q , \sr锁存器_3_q , \主裁判按键_out , \副裁判1按键_out , \副裁判2按键_out , \工作人员按键_out ;

  Button \u_主裁判按键  (.out(\主裁判按键_out ));
  \SR锁存器  \sr锁存器_1  (.R(\工作人员按键_out ), .S(\主裁判按键_out ), .Q(\sr锁存器_1_q ));  // open: nQ
  Button \u_副裁判1按键  (.out(\副裁判1按键_out ));
  and and_1 (out_1, \sr锁存器_1_q , or_1_out);
  \SR锁存器  \sr锁存器_2  (.R(\工作人员按键_out ), .S(\副裁判1按键_out ), .Q(\sr锁存器_2_q ));  // open: nQ
  Button \u_副裁判2按键  (.out(\副裁判2按键_out ));
  or or_1 (or_1_out, \sr锁存器_2_q , \sr锁存器_3_q );
  \SR锁存器  \sr锁存器_3  (.R(\工作人员按键_out ), .S(\副裁判2按键_out ), .Q(\sr锁存器_3_q ));  // open: nQ
  Button \u_工作人员按键  (.out(\工作人员按键_out ));
endmodule

module \举重裁判D触发器  (
  output out_1
);

  wire \d触发器_1_q , \d触发器_2_q , \d触发器_3_q , or_1_out, \主裁判_out , \副裁判1_out , \副裁判2_out ;

  Button \u_主裁判  (.out(\主裁判_out ));
  \D触发器  \d触发器_1  (.D(1'b1), .CLK(\主裁判_out ), .Q(\d触发器_1_q ));  // open: out_4
  and and_1 (out_1, \d触发器_1_q , or_1_out);
  Button \u_副裁判1  (.out(\副裁判1_out ));
  \D触发器  \d触发器_2  (.D(1'b1), .CLK(\副裁判1_out ), .Q(\d触发器_2_q ));  // open: out_4
  or or_1 (or_1_out, \d触发器_2_q , \d触发器_3_q );
  Button \u_副裁判2  (.out(\副裁判2_out ));
  \D触发器  \d触发器_3  (.D(1'b1), .CLK(\副裁判2_out ), .Q(\d触发器_3_q ));  // open: out_4
  Button \u_工作人员  ();  // open: out
endmodule

module \有限状态机的状态编码_二进制编码和独热编码  (
  input  reset,
  input  reset_2,
  output Output,
  output Output_2,
  output output_3
);

  wire and_2_out, CLK_out, clock_1_out, clock_2_out, not_1_out, not_2_out, not_3_out, not_4_out, or_1_out,
       S00, S1_q, S2_q, S11, S22;
  wire [0:0] register_1_q;
  wire [1:0] and_1_out;

  Clock CLK (.out(CLK_out));
  not not_1 (not_1_out, register_1_q[0]);
  not not_2 (not_2_out, and_1_out[0]);
  // Probe on and_1_out[0]
  and and_1 (and_1_out[1], not_1_out, not_2_out);
  // Probe on and_1_out[1]
  or or_1 (or_1_out, S11, and_2_out);
  and and_2 (and_2_out, S00, S22);
  \同步复位触发器  S1 (.D(output_3), .CLK(CLK_out), .reset(reset_2), .Q(S1_q));
  Register #(.width(2)) register_1 (
    .D(and_1_out), .Q({and_1_out[0], register_1_q[0]}), .clk(clock_1_out));  // open: en, clr
  Clock clock_1 (.out(clock_1_out));
  // Probe on or_1_out
  // Probe on S22
  // Probe on S00
  \同步复位触发器  S2 (.D(S1_q), .CLK(CLK_out), .reset(reset_2), .Q(S2_q));
  Clock clock_2 (.out(clock_2_out));
  \三位的状态寄存器  \u_三位的状态寄存器_1  (
    .in_2(or_1_out), .in_3(S22), .in_4(S00), .CLK(clock_2_out), .reset(reset), .out_6(S00), .out_7(S11),
    .out_8(S22));
  \同步置位触发器  S0 (.D(S2_q), .CLK(CLK_out), .reset(reset_2), .Q(output_3));
  not not_3 (not_3_out, register_1_q[0]);
  not not_4 (not_4_out, and_1_out[0]);
  and and_3 (Output, not_3_out, not_4_out);
  and and_4 (Output_2, ~S00, ~S11, S22);  // AND_Gate

  // Notes on the sheet:
  //   二进制编码
  //   独热编码
  //   这里用寄存器会直接初始化为零
  //   独热编码就是1的位置不断向后一位传递
endmodule

module \Moore型状态机和Mealy型状态机  (
  input  A,
  input  in_2,
  input  A_2,
  output Y,
  output Y_2
);

  wire and_1_out, clock_1_out, clock_2_out, \d触发器_1_q , not_1_out, not_2_out, S00;

  not not_1 (not_1_out, A_2);
  and and_1 (and_1_out, S00, A);
  not not_2 (not_2_out, A);
  Clock clock_1 (.out(clock_1_out));
  \D触发器  \d触发器_1  (.D(not_1_out), .CLK(clock_1_out), .Q(\d触发器_1_q ));  // open: out_4
  Clock clock_2 (.out(clock_2_out));
  // Probe on and_1_out
  // Probe on not_2_out
  // Probe on \d触发器_1_q 
  \两位的状态寄存器  \u_两位的状态寄存器_1  (
    .S11(and_1_out), .S00(not_2_out), .in_1(clock_2_out), .reset(in_2), .out_5(Y), .out_6(S00));
  and and_2 (Y_2, \d触发器_1_q , A_2);

  // Notes on the sheet:
  //   Moore
  //   Mealy
  //   mearly比moore快一个周期响应
endmodule

module temp (
  input  S,
  input  A,
  output SS
);

  not not_1 (SS, A);
endmodule
