// Logisim project learn20210913.circ as structural Verilog: 1 circuit, main circuit main
module main (
  input  in_1,
  input  in_2,
  input  in_3,
  input  [7:0] in_4,
  input  loaddata,
  input  [7:0] in_6,
  input  \为一时计数器递增_为零时计数器不变 ,
  input  in_8,
  input  reset,
  input  [3:0] in_10,
  input  [7:0] in_11,
  input  in_12,
  input  enable,
  input  in_14,
  output out_15,
  output out_16,
  output out_17,
  output out_18,
  output [7:0] out_19
);

  wire and_1_out, clock_1_out, clock_2_out, clock_3_out, clock_4_out, clock_5_out, clock_6_out, d_ff_1_qn,
       not_1_out, or_1_out, register_1_q;
  wire [3:0] adder_3_out, now, prev, register_3_q;
  wire [7:0] adder_1_out, counter_1_q, counter_2_q, ram_1_data, xnor_1_out;

  Counter counter_1 (.Q(counter_1_q), .clk(clock_4_out));  // open: load, D, count, carry, clr
  Adder adder_1 (.a(ram_1_data), .b(in_11), .out(adder_1_out));  // open: cin, cout
  not not_1 (not_1_out, in_3);
  Counter counter_2 (.Q(counter_2_q), .clk(clock_3_out));  // open: load, D, count, carry, clr
  and and_1 (and_1_out, in_3, not_1_out);
  Counter counter_3 (
    .load(loaddata), .D(in_6), .count(\为一时计数器递增_为零时计数器不变 ), .Q(out_19), .carry(in_8), .clk(clock_1_out),
    .clr(reset));
  Clock clock_1 (.out(clock_1_out));
  or or_1 (or_1_out, out_15, in_1);
  Register #(.width(1)) register_1 (.D(or_1_out), .Q(register_1_q), .clk(clock_2_out));  // open: en, clr
  Clock clock_2 (.out(clock_2_out));
  D_Flip_Flop d_ff_1 (.clk(and_1_out), .D(d_ff_1_qn), .Q(out_17), .Qn(d_ff_1_qn));  // open: preset, en, reset
  assign xnor_1_out = ~(counter_1_q ^ in_4);  // XNOR_Gate xnor_1, 8 bits wide
  // Probe on counter_1_q
  not not_2 (out_15, register_1_q);
  Clock clock_3 (.out(clock_3_out));
  Clock clock_4 (.out(clock_4_out));
  RAM #(.bus("separate")) ram_1 (
    .addr(counter_2_q), .din(adder_1_out), .data(ram_1_data), .clk(clock_3_out), .ld(in_12));  // open: str, sel, clr
  Clock clock_5 (.out(clock_5_out));
  RAM #(.bus("separate")) ram_2 (
    .addr(xnor_1_out), .din(counter_1_q), .clk(clock_4_out));  // open: data, str, sel, ld, clr
  D_Flip_Flop d_ff_2 (.clk(clock_5_out), .D(in_2), .Q(out_16));  // open: Qn, preset, en, reset
  \D触发器  \d触发器_1  (.D(in_2), .CLK(clock_5_out), .Q(out_18));  // open: out_4
  Clock clock_6 (.out(clock_6_out));
  Adder #(.width(4)) adder_2 (.a(prev), .b(now), .out(now));  // open: cin, cout
  Adder #(.width(4)) adder_3 (.a(in_10), .b(register_3_q), .out(adder_3_out));  // open: cin, cout
  Register #(.width(4)) register_2 (.D(now), .Q(prev), .clk(clock_6_out));  // open: en, clr
  Register #(.width(4)) register_3 (.D(adder_3_out), .en(enable), .Q(register_3_q), .clk(in_14));  // open: clr
endmodule
