// Logisim project learn20210914.circ as structural Verilog: 1 circuit, main circuit main
module main (
  input  [4:0] in_1,
  input  [2:0] \input ,
  output [3:0] out_3
);

  wire CLK, clock_2_out, \end ;
  wire [3:0] counter_1_q, now, ram_1_data;
  wire [4:0] bit_extender_2_out, count;

  Adder #(.width(4)) adder_1 (.a(out_3), .b(now), .out(now));  // open: cin, cout
  Clock clock_1 (.out(CLK));
  assign count = {{2{1'b0}}, \input };  // Bit_Extender bit_extender_1
  Counter #(.width(4), .max('hf)) counter_1 (.Q(counter_1_q), .clk(CLK));  // open: load, D, count, carry, clr
  Clock clock_2 (.out(clock_2_out));
  RAM #(.addrWidth(5), .dataWidth(4), .bus("separate")) ram_1 (
    .addr(in_1), .din(now), .data(ram_1_data), .clk(clock_2_out));  // open: str, sel, ld, clr
  assign bit_extender_2_out = {{1{1'b0}}, counter_1_q};  // Bit_Extender bit_extender_2
  Comparator #(.width(5)) comparator_1 (.a(bit_extender_2_out), .b(count), .eq(\end ));  // open: gt, lt
  Register #(.width(4)) register_1 (.D(ram_1_data), .Q(out_3), .clk(clock_2_out));  // open: en, clr
endmodule
