// Logisim project learn20210915.circ as structural Verilog: 6 circuits, main circuit main
module main (
  input  [31:0] in_1,
  input  [3:0] in_2,
  input  [2:0] \input ,
  output [31:0] out_4,
  output [3:0] out_5
);

  wire CLK, clock_1_out, clock_2_out, count1_end, counter_1_q, enable;
  wire [3:0] calculate_output, now, prev;

  Clock clock_1 (.out(clock_1_out));
  Multiplexer #(.width(32)) multiplexer_1 (.in0(32'h1), .in1(in_1), .out(out_4), .sel(counter_1_q));  // open: en
  Counter #(.width(1), .max('h1), .ongoal("stay")) counter_1 (
    .Q(counter_1_q), .clk(clock_1_out));  // open: load, D, count, carry, clr
  count1 count1 (.\input (\input ), .in_2(clock_2_out), .\end (count1_end));
  Clock clock_2 (.out(clock_2_out));
  Register_part #(.width(4)) register_1 (.D(now), .en(enable), .Q(prev), .clk(CLK));  // open: clr
  calculate calculate (.\end (count1_end), .init(in_2), .CLK(clock_2_out), .\output (calculate_output));
  Multiplexer #(.width(4)) multiplexer_2 (
    .in0(4'b0000), .in1(calculate_output), .out(out_5), .sel(count1_end));  // open: en
endmodule

module Register (
  input  [3:0] init,
  input  [3:0] Now,
  input  enable,
  output [3:0] out_4
);

  wire clock_1_out, counter_1_q;
  wire [3:0] register_1_q;

  Register_part #(.width(4)) register_1 (.D(Now), .en(enable), .Q(register_1_q), .clk(clock_1_out));  // open: clr
  Counter #(.width(1), .max('h1), .ongoal("stay")) counter_1 (
    .Q(counter_1_q), .clk(clock_1_out));  // open: load, D, count, carry, clr
  Clock clock_1 (.out(clock_1_out));
  Multiplexer #(.width(4)) multiplexer_1 (.in0(init), .in1(register_1_q), .out(out_4), .sel(counter_1_q));  // open: en

  // Notes on the sheet:
  //   这个寄存器在多路选择器前面，perfect regisistor中的寄存器放到了多路选择器后面，二者相差了一个周期
  //   带有初始化功能的寄存器，注意第一个时钟上升沿到来之前（第零个周期）就已经将输出初始化
endmodule

module pull_resistor (
  input  in_1,
  input  in_2,
  output out_3
);

  or or_1 (out_3, in_1, in_2);

  // Notes on the sheet:
  //   in_2: pull=down
  //   in_1: pull=down
endmodule

module practice (
  input  in_1,
  output out_2
);

  pull_resistor pull_resistor (.out_3(out_2));  // open: in_1, in_2
endmodule

module perfert_regisistor (
  input  [3:0] init,
  input  [3:0] \input ,
  input  enable,
  input  clear,
  output [3:0] out_5
);

  wire clock_1_out, counter_1_q;
  wire [3:0] multiplexer_1_out;

  Pull_Resistor #(.pull(1)) pull_resistor_1 (.node(enable));
  Counter #(.width(1), .max('h1), .ongoal("stay")) counter_1 (
    .Q(counter_1_q), .clk(clock_1_out), .clr(clear));  // open: load, D, count, carry
  Multiplexer #(.width(4)) multiplexer_1 (
    .in0(init), .in1(\input ), .out(multiplexer_1_out), .sel(counter_1_q));  // open: en
  Clock clock_1 (.out(clock_1_out));
  Register_part #(.width(4)) register_1 (.D(multiplexer_1_out), .en(enable), .Q(out_5), .clk(clock_1_out), .clr(clear));

  // Notes on the sheet:
  //   init: pull=down
  //   这个赋初始值经过了寄存器
endmodule

module calculate (
  input  [3:0] init,
  input  \end ,
  input  CLK,
  output [3:0] \output 
);

  wire enable;
  wire [3:0] adder_1_out, prev;

  not not_1 (enable, \end );
  Register_part #(.width(4)) register_1 (.D(\output ), .en(enable), .Q(prev), .clk(CLK));  // open: clr
  // Probe on prev
  Adder #(.width(4)) adder_1 (.a(prev), .b(\output ), .out(adder_1_out));  // open: cin, cout
  // Probe on \output 
  perfert_regisistor perfert_regisistor_1 (
    .\input (adder_1_out), .enable(enable), .init(init), .out_5(\output ));  // open: clear

  // Other names for the same wires on the sheet: now[3:0] = \output 
endmodule
