// Logisim project learn20210916.circ as structural Verilog: 1 circuit, main circuit main
module main (
  input  [31:0] in_1,
  input  [31:0] in_2,
  output [31:0] out_3,
  output [31:0] out_4
);

  wire [31:0] shifter_1_out;

  assign out_4 = in_2 & 32'h1;  // AND_Gate and_1, 32 bits wide
  Shifter #(.width(32), .shift("lr")) shifter_1 (.in(in_1), .\dist (5'b00001), .out(shifter_1_out));
  assign out_3 = 32'h1 & shifter_1_out;  // AND_Gate and_2, 32 bits wide
endmodule
