// Logisim project learn20210917.circ as structural Verilog
module add (
  input  a,
  input  b,
  input  carry1,
  output out,
  output carry2
);

  wire and_1_out, and_2_out, and_3_out, and_4_out, and_5_out, and_6_out, and_7_out, not_1_out, not_2_out,
       not_3_out, not_4_out, not_5_out, not_6_out;

  not not_1 (not_1_out, a);
  and and_1 (and_1_out, not_1_out, not_2_out, carry1);
  not not_2 (not_2_out, b);
  not not_3 (not_3_out, a);
  and and_2 (and_2_out, not_3_out, b, not_4_out);
  not not_4 (not_4_out, carry1);
  not not_5 (not_5_out, b);
  and and_3 (and_3_out, a, not_5_out, not_6_out);
  not not_6 (not_6_out, carry1);
  and and_4 (and_4_out, a, b, carry1);
  and and_5 (and_5_out, b, carry1);
  and and_6 (and_6_out, a, carry1);
  and and_7 (and_7_out, a, b);
  or or_1 (out, and_1_out, and_2_out, and_3_out, and_4_out);
  or or_2 (carry2, and_5_out, and_6_out, and_7_out);
endmodule
