// Logisim project learn20210918.circ as structural Verilog: 1 circuit, main circuit main
module main (
  input  in_1,
  input  in_2,
  input  in_3
);

  ExactlyOne xor_1 (.in0(in_1), .in2(in_2), .in4(in_3));  // open: out
endmodule
