// Logisim project learn20211005.circ as structural Verilog: 11 circuits, main circuit main
module main (
  input  in_1,
  input  in_2,
  output out_3
);

  D_Flip_Flop d_ff_1 (.clk(in_1), .D(in_2), .Q(out_3));  // open: Qn, preset, en, reset
endmodule

module \SR锁存器  (
  input  in_1,
  input  in_2,
  output out_3,
  output out_4
);

  nor nor_1 (out_3, out_4, in_1);
  nor nor_2 (out_4, out_3, in_2);
endmodule

module \D锁存器  (
  input  in_1,
  input  in_2,
  output out_3
);

  wire and_1_out, and_2_out, not_1_out;

  not not_1 (not_1_out, in_2);
  and and_1 (and_1_out, not_1_out, in_1);
  and and_2 (and_2_out, in_1, in_2);
  \SR锁存器  SR (.in_1(and_1_out), .in_2(and_2_out), .out_3(out_3));  // open: out_4
endmodule

module \D触发器  (
  input  in_1,
  input  in_2,
  output out_3
);

  wire D_out_3, not_1_out;

  not not_1 (not_1_out, in_1);
  \D锁存器  D (.in_2(in_2), .in_1(not_1_out), .out_3(D_out_3));
  \D锁存器  D_2 (.in_2(D_out_3), .in_1(in_1), .out_3(out_3));
endmodule

module \有限状态机mode1  (
  input  roadA,
  input  roadB,
  input  reset,
  output TA1,
  output TA2,
  output TB1,
  output TB2
);

  wire clk_out, register_1_q, register_2_q, S0, S1, \状态转移_s00 , \状态转移_s11 ;

  \状态转移  \u_状态转移  (.S1(S0), .S0(S1), .TA(roadA), .TB(roadB), .S00(\状态转移_s00 ), .S11(\状态转移_s11 ));
  Clock clk (.out(clk_out));
  Register #(.width(1)) register_1 (.D(\状态转移_s00 ), .Q(register_1_q), .clk(clk_out));  // open: en, clr
  Register #(.width(1)) register_2 (.D(\状态转移_s11 ), .Q(register_2_q), .clk(clk_out));  // open: en, clr
  Multiplexer multiplexer_1 (.in0(register_1_q), .in1(1'b0), .out(S0), .sel(reset));  // open: en
  Multiplexer multiplexer_2 (.in0(register_2_q), .in1(1'b0), .out(S1), .sel(reset));  // open: en
  \状态输出  \u_状态输出  (.S1(S0), .S0(S1), .LA0(TA1), .LA1(TA2), .LB0(TB1), .LB1(TB2));
endmodule

module \状态转移  (
  input  S1,
  input  S0,
  input  TA,
  input  TB,
  output S00,
  output S11
);

  wire and_1_out, and_2_out, and_3_out, and_4_out, not_1_out, not_2_out, not_3_out, not_4_out, not_5_out,
       not_6_out, not_7_out;

  not not_1 (not_1_out, S1);
  and and_1 (and_1_out, not_1_out, S0);
  and and_2 (and_2_out, S1, not_2_out);
  not not_2 (not_2_out, S0);
  not not_3 (not_3_out, S1);
  not not_4 (not_4_out, S0);
  and and_3 (and_3_out, not_3_out, not_4_out, not_5_out);
  not not_5 (not_5_out, TA);
  not not_6 (not_6_out, S0);
  and and_4 (and_4_out, S1, not_6_out, not_7_out);
  not not_7 (not_7_out, TB);
  or or_1 (S00, and_1_out, and_2_out);
  or or_2 (S11, and_3_out, and_4_out);
endmodule

module \状态输出  (
  input  S1,
  input  S0,
  output LA0,
  output LA1,
  output LB0,
  output LB1
);

  wire not_1_out, not_2_out, not_3_out, not_4_out;

  not not_1 (not_1_out, S1);
  not not_2 (not_2_out, S0);
  not not_3 (not_3_out, S1);
  not not_4 (not_4_out, S0);
  and and_1 (LB1, S1, S0);
  and and_2 (LA0, not_1_out, not_2_out);
  and and_3 (LA1, not_3_out, S0);
  and and_4 (LB0, S1, not_4_out);
endmodule

module \状态机的分解  (
  input  P,
  input  R,
  input  TA,
  input  TB,
  input  in_5,
  output LA1,
  output LA2,
  output LB1,
  output LB2
);

  wire clock_1_out, \模式状态机_out_5 ;

  \模式状态机  \u_模式状态机  (.P(P), .R(R), .CLK(clock_1_out), .RESET(in_5), .out_5(\模式状态机_out_5 ));
  Clock clock_1 (.out(clock_1_out));
  \灯状态机  \u_灯状态机  (
    .MODE(\模式状态机_out_5 ), .TA(TA), .TB(TB), .CLK(clock_1_out), .RESET(in_5), .out_6(LA1), .out_7(LA2),
    .out_8(LB1), .out_9(LB2));
endmodule

module \模式状态机  (
  input  P,
  input  R,
  input  CLK,
  input  RESET,
  output out_5
);

  wire and_1_out, not_1_out, or_1_out, register_1_q;

  not not_1 (not_1_out, R);
  and and_1 (and_1_out, not_1_out, out_5);
  or or_1 (or_1_out, and_1_out, P);
  Register #(.width(1)) register_1 (.D(or_1_out), .Q(register_1_q), .clk(CLK));  // open: en, clr
  Multiplexer multiplexer_1 (.in0(register_1_q), .in1(1'b0), .out(out_5), .sel(RESET));  // open: en

  // Other names for the same wires on the sheet: MODE = out_5
endmodule

module \灯状态机  (
  input  MODE,
  input  TA,
  input  TB,
  input  CLK,
  input  RESET,
  output out_6,
  output out_7,
  output out_8,
  output out_9
);

  wire register_1_q, register_2_q, S0, S1, \状态转移_s00 , \状态转移_s11 ;

  \灯状态机状态转移  \u_状态转移  (.S0(S0), .S1(S1), .M(MODE), .TA(TA), .TB(TB), .S00(\状态转移_s00 ), .S11(\状态转移_s11 ));
  Register #(.width(1)) register_1 (.D(\状态转移_s00 ), .Q(register_1_q), .clk(CLK));  // open: en, clr
  Register #(.width(1)) register_2 (.D(\状态转移_s11 ), .Q(register_2_q), .clk(CLK));  // open: en, clr
  Multiplexer multiplexer_1 (.in0(register_1_q), .in1(1'b0), .out(S0), .sel(RESET));  // open: en
  Multiplexer multiplexer_2 (.in0(register_2_q), .in1(1'b0), .out(S1), .sel(RESET));  // open: en
  \状态输出  \u_状态输出_1  (.S1(S0), .S0(S1), .LA0(out_6), .LA1(out_7), .LB0(out_8), .LB1(out_9));
endmodule

module \灯状态机状态转移  (
  input  S0,
  input  S1,
  input  M,
  input  TA,
  input  TB,
  output S00,
  output S11
);

  wire and_1_out, and_2_out, and_3_out, and_4_out, not_1_out, not_2_out, not_3_out, not_4_out, not_5_out,
       not_6_out, not_7_out, not_8_out;

  not not_1 (not_1_out, S0);
  not not_2 (not_2_out, S1);
  not not_3 (not_3_out, S0);
  not not_4 (not_4_out, S1);
  not not_5 (not_5_out, TA);
  not not_6 (not_6_out, S1);
  not not_7 (not_7_out, M);
  not not_8 (not_8_out, TB);
  and and_1 (and_1_out, not_1_out, S1);
  and and_2 (and_2_out, S0, not_2_out);
  and and_3 (and_3_out, not_3_out, not_4_out, not_5_out);
  and and_4 (and_4_out, S0, not_6_out, not_7_out, not_8_out);
  or or_1 (S00, and_1_out, and_2_out);
  or or_2 (S11, and_3_out, and_4_out);
endmodule
