// Logisim project learn20211010.circ as structural Verilog: 1 circuit, main circuit main
module main (
  input  reset,
  input  in_2,
  input  in_3,
  input  in_4,
  input  in_5,
  input  in_6,
  input  in_7,
  input  in_8,
  input  in_9,
  input  in_10,
  input  in_11,
  input  in_12,
  input  in_13,
  input  in_14,
  input  in_15,
  input  in_16,
  input  [7:0] in_17,
  input  [7:0] in_18,
  input  in_19,
  input  in_20,
  input  in_21,
  input  [7:0] in_22,
  input  [7:0] in_23,
  input  in_24,
  input  in_25,
  input  [7:0] in_26,
  input  [7:0] in_27,
  input  in_28,
  output [2:0] out_29,
  output out_30,
  output out_31,
  output out_32,
  output [7:0] out_33,
  output [7:0] out_34
);

  wire clk_out;
  wire [2:0] adder_1_out, multiplexer_1_out;

  Multiplexer #(.width(3)) multiplexer_1 (
    .in0(adder_1_out), .in1(3'b000), .out(multiplexer_1_out), .sel(reset));  // open: en
  Multiplexer multiplexer_2 (.in0(in_7), .in1(in_9), .out(out_31), .sel(in_13), .en(in_14));
  RAM #(.bus("separate")) ram_1 (
    .addr(in_17), .din(in_18), .data(out_33), .str(in_19), .clk(in_21), .ld(in_20));  // open: sel, clr
  RAM ram_2 (.addr(in_23), .data(in_22), .clk(in_25), .ld(in_24));  // open: sel, clr
  RAM #(.bus("asynch")) ram_3 (.addr(in_26), .data(in_27), .ld(in_28));  // open: sel, clr
  Register #(.width(3)) register_1 (.D(multiplexer_1_out), .Q(out_29), .clk(clk_out));  // open: en, clr
  Clock clk (.out(clk_out));
  Adder #(.width(3)) adder_1 (.a(3'b001), .b(out_29), .out(adder_1_out));  // open: cin, cout
  Register #(.width(1), .trigger("high")) register_2 (.D(in_11), .clk(in_16));  // open: en, Q, clr
  ExactlyOne xor_1 (.out(out_32), .in0(in_8), .in1(in_10), .in2(in_12), .in3(in_15));
  ExactlyOne xor_2 (.out(out_30), .in0(in_2), .in1(in_3), .in3(in_4), .in4(in_5));

  // Notes on the sheet:
  //   in_6: pull=up
endmodule
