// Logisim project learn20211012.circ as structural Verilog: 1 circuit, main circuit main
module main (
  input  [4:0] in_1,
  input  [7:0] in_2,
  input  in_3,
  input  in_4,
  input  [4:0] in_5,
  input  in_6,
  input  [7:0] in_7,
  input  value_shift_to_the_first_edge,
  input  in_9,
  input  in_10,
  input  [7:0] in_11,
  input  in_12,
  input  [7:0] in_13,
  input  [7:0] in_14,
  input  [7:0] in_15,
  input  in_16,
  input  [7:0] in_17,
  input  \写使能 ,
  input  [7:0] in_19,
  input  [7:0] in_20,
  input  in_21,
  input  [3:0] in_22,
  input  [6:0] in_23,
  output out_24,
  output out_25,
  output out_26,
  output out_27,
  output out_28,
  output out_29,
  output [2:0] out_30,
  output [7:0] out_31,
  output [7:0] out_32,
  output [3:0] out_33,
  output [7:0] out_34,
  output [7:0] out_35
);

  wire clock_1_out, clock_2_out, clock_3_out, not_1_out;

  Controlled_Buffer controlled_buffer_1 ();  // open: in, out, en
  assign out_29 = in_10 ? ~in_9 : 1'bz;  // Controlled_Inverter controlled_inverter_1
  BitAdder bitadder_1 ();  // open: in0, out
  Transistor transistor_1 ();  // open: in, out, gate
  xor odd_parity_1 (out_24, in_1[0], in_1[1], in_1[2], in_1[3], in_1[4]);
  // Buffer buffer_1 is placed but not wired
  xnor even_parity_1 (out_27, in_5[0], in_5[1], in_5[2], in_5[3], in_5[4]);
  Priority_Encoder priority_encoder_1 (
    .in0(in_11[0]), .in1(in_11[1]), .in2(in_11[2]), .in3(in_11[3]), .in4(in_11[4]), .in5(in_11[5]),
    .in6(in_11[6]), .in7(in_11[7]), .out(out_30), .en_in(in_12));  // open: gs, en_out
  Divider divider_1 (.a(in_13), .b(in_14), .out(out_31), .rem(out_32));  // open: upper
  BitAdder bitadder_2 (.in0(in_15), .out(out_33));
  Joystick joystick_1 ();  // open: x, y
  Hex_Digit_Display hex_digit_display_1 (.value(in_22));  // open: dp
  BitSelector bitselector_1 (.in(in_2), .out(out_25));  // open: sel
  Decoder decoder_1 ();  // open: out0, out1, sel, en
  Shift_Register shift_register_1 (
    .in(value_shift_to_the_first_edge), .clk(clock_1_out), .out(out_28), .load(in_6), .d0(in_7[7]),
    .d1(in_7[6]), .d2(in_7[5]), .d3(in_7[4]), .d4(in_7[3]), .d5(in_7[2]), .d6(in_7[1]), .d7(in_7[0]));  // open: shift, clr, q0, q1, q2, q3, q4, q5, q6, q7
  Clock clock_1 (.out(clock_1_out));
  RAM #(.bus("separate")) ram_1 (.addr(in_19));  // open: din, data, str, sel, clk, ld, clr
  LED led_1 (.in(in_21));
  assign out_35 = \写使能  ? in_17 : 8'bz;  // Controlled_Buffer controlled_buffer_2
  not not_1 (not_1_out, \写使能 );
  DotMatrix dotmatrix_1 (.col0(in_23));  // open: col1, col2, col3, col4
  assign out_26 = in_4 ? in_3 : 1'bz;  // Controlled_Buffer controlled_buffer_3
  Bit_Extender bit_extender_1 ();  // open: in, out
  Negator negator_1 ();  // open: in, out
  Shift_Register shift_register_2 ();  // open: shift, in, clk, out, load, clr, d0, q0, d1, q1, d2, q2, d3, q3, d4, q4, d5, q5, d6, q6, d7, q7
  Clock clock_2 (.out(clock_2_out));
  Clock clock_3 (.out(clock_3_out));
  _7_Segment_Display u_7_segment_display_1 ();  // open: g, f, a, b, e, d, c, dp
  Counter counter_1 ();  // open: load, D, count, Q, carry, clk, clr
  Random random_1 (.clk(clock_2_out), .out(out_34));  // open: next, clr
  RAM ram_2 (.addr(in_20), .data(out_35), .clk(clock_3_out), .ld(not_1_out));  // open: sel, clr
endmodule
