// Logisim project learn20211015.circ as structural Verilog: 1 circuit, main circuit main
module main (
  input  in_1,
  output out_2
);

  wire clock_1_out;

  Clock clock_1 (.out(clock_1_out));
  Register #(.width(1)) register_1 (.D(in_1), .Q(out_2), .clk(clock_1_out), .clr(out_2));  // open: en
endmodule
