// Logisim project learn20211020.circ as structural Verilog: 4 circuits, main circuit main
module main (
  input  [1:0] in_1,
  input  [7:0] in_2,
  input  reset,
  input  in_4,
  input  [3:0] in_5,
  input  in_6,
  input  [3:0] in_7,
  input  in_8,
  input  [7:0] in_9,
  input  [15:0] in_10,
  input  [3:0] in_11,
  output out_12,
  output out_13,
  output [7:0] out_14,
  output out_15,
  output [3:0] out_16,
  output out_17,
  output out_18,
  output [3:0] out_19,
  output [15:0] out_20
);

  wire clock_1_out, sign;
  wire [7:0] multiplexer_1_out;
  wire [14:0] demultiplexer_1_out1;
  wire [15:0] demultiplexer_1_out0;

  Decoder #(.select(2), .tristate("true")) decoder_1 (
    .out1(out_12), .out3(out_13), .sel(in_1));  // open: out0, out2, en
  Adder adder_1 ();  // open: a, b, out, cin, cout
  Demultiplexer #(.width(16)) demultiplexer_1 (
    .out0(demultiplexer_1_out0), .out1({sign, demultiplexer_1_out1}), .in(in_10), .sel(in_11[0]));  // open: en
  Adder #(.width(4)) adder_2 (.a(in_5), .b(in_7), .out(out_16), .cin(in_4), .cout(out_17));
  Multiplexer #(.width(8)) multiplexer_1 (
    .in0(in_2), .in1({8{1'b0}}), .out(multiplexer_1_out), .sel(reset));  // open: en
  Register register_1 ();  // open: D, en, Q, clk, clr
  Register register_2 (.D(multiplexer_1_out), .Q(out_14), .clk(clock_1_out));  // open: en, clr
  Clock clock_1 (.out(clock_1_out));
  assign out_20 = {{2{sign}}, demultiplexer_1_out1[14:1]} | demultiplexer_1_out0;  // OR_Gate or_1, 16 bits wide
  nor nor_1 (out_15, out_18, in_6);
  nor nor_2 (out_18, out_15, in_8);
endmodule

module SR (
  input  in_1,
  input  in_2,
  output out_3,
  output out_4
);

  nor nor_1 (out_3, out_4, in_1);
  nor nor_2 (out_4, out_3, in_2);
endmodule

module \D锁存器  (
  input  in_1,
  input  in_2,
  output out_3,
  output out_4
);

  wire and_1_out, and_2_out, not_1_out;

  not not_1 (not_1_out, in_2);
  and and_1 (and_1_out, in_1, not_1_out);
  and and_2 (and_2_out, in_1, in_2);
  SR sr_1 (.in_1(and_1_out), .in_2(and_2_out), .out_3(out_3), .out_4(out_4));
endmodule

module \D触发器  (
  input  in_1,
  input  in_2,
  input  in_3,
  input  in_4,
  output out_5,
  output out_6
);

  wire \d锁存器_1_out_3 , not_1_out;

  \D锁存器  \d锁存器_1  (.in_2(in_2), .in_1(not_1_out), .out_3(\d锁存器_1_out_3 ));  // open: out_4
  not not_1 (not_1_out, in_1);
  D_Flip_Flop d_ff_1 (.clk(in_3), .D(in_4), .Q(out_6));  // open: Qn, preset, en, reset
  \D锁存器  \d锁存器_2  (.in_2(\d锁存器_1_out_3 ), .in_1(in_1), .out_3(out_5));  // open: out_4
endmodule
