// Logisim project my first logisim 20210907.circ as structural Verilog: 1 circuit, main circuit main
module main (
  input  x,
  input  y,
  input  in_3,
  input  in_4,
  output out_5,
  output out_6
);

  wire and_1_out, and_2_out, not_1_out, not_2_out, not_3_out, not_4_out, or_1_out, or_2_out;

  not not_1 (not_1_out, in_3);
  not not_2 (not_2_out, in_4);
  not not_3 (not_3_out, x);
  not not_4 (not_4_out, y);
  or or_1 (or_1_out, not_1_out, in_4);
  or or_2 (or_2_out, in_3, not_2_out);
  and and_1 (and_1_out, not_3_out, y);
  and and_2 (and_2_out, x, not_4_out);
  or or_3 (out_5, and_1_out, and_2_out);
  and and_3 (out_6, or_1_out, or_2_out);
endmodule
